// Logisim project Design A CPU vnf sectie 3 hfst 20.circ as structural Verilog: 45 circuits, main circuit main
// e
module main (
);
endmodule

module ML___Active_Low_S_R_Latch (
  input  s,
  input  r,
  output q,
  output nq
);

  nand nand_1 (q, s, nq);
  nand nand_2 (nq, q, r);

  // Notes on the sheet:
  //   Active Low S R Latch
endmodule

module ML___Active_High_with_Enable (
  input  s,
  input  e,
  input  r,
  output q,
  output nq
);

  wire nand_1_out, nand_2_out;

  nand nand_1 (nand_1_out, s, e);
  nand nand_2 (nand_2_out, e, r);
  nand nand_3 (q, nand_1_out, nq);
  nand nand_4 (nq, q, nand_2_out);

  // Notes on the sheet:
  //   Active High with Enable
endmodule

module ML___CPU_MEM_1 (
  input  i,
  input  s,
  output o
);

  wire nand_1_out, nand_2_out, nand_4_out;

  nand nand_1 (nand_1_out, i, s);
  nand nand_2 (nand_2_out, nand_1_out, s);
  nand nand_3 (o, nand_1_out, nand_4_out);
  nand nand_4 (nand_4_out, o, nand_2_out);

  // Notes on the sheet:
  //   s: pull=down
  //   o: pull=down
  //   i: pull=down
  //   1 bit memory cell
endmodule

module ML___ENABLER_VARIANT_1 (
  input  [7:0] i,
  input  e,
  output [7:0] o
);

  and and_1 (o[0], i[0], e);
  and and_2 (o[1], i[1], e);
  and and_3 (o[2], i[2], e);
  and and_4 (o[3], i[3], e);
  and and_5 (o[4], i[4], e);
  and and_6 (o[5], i[5], e);
  and and_7 (o[6], i[6], e);
  and and_8 (o[7], i[7], e);

  // Notes on the sheet:
  //   ML 6-10-25: Enabler zonder controller Buffer: vaker al toegepast. Later pakt hij er een (bij de ALU) met control buffer. Die heb ik ook en is ML_ENABLER Variant 2
endmodule

module ML___ENABLER_VARIANT_2 (
  input  [7:0] i,
  input  e,
  output [7:0] o
);

  wire and_1_out, and_2_out, and_3_out, and_4_out, and_5_out, and_6_out, and_7_out, and_8_out;

  and and_1 (and_1_out, i[0], e);
  and and_2 (and_2_out, i[1], e);
  and and_3 (and_3_out, i[2], e);
  and and_4 (and_4_out, i[3], e);
  and and_5 (and_5_out, i[4], e);
  and and_6 (and_6_out, i[5], e);
  and and_7 (and_7_out, i[6], e);
  and and_8 (and_8_out, i[7], e);
  assign o[0] = e ? and_1_out : 1'bz;  // Controlled_Buffer controlled_buffer_1
  assign o[1] = e ? and_2_out : 1'bz;  // Controlled_Buffer controlled_buffer_2
  assign o[2] = e ? and_3_out : 1'bz;  // Controlled_Buffer controlled_buffer_3
  assign o[3] = e ? and_4_out : 1'bz;  // Controlled_Buffer controlled_buffer_4
  assign o[4] = e ? and_5_out : 1'bz;  // Controlled_Buffer controlled_buffer_5
  assign o[5] = e ? and_6_out : 1'bz;  // Controlled_Buffer controlled_buffer_6
  assign o[6] = e ? and_7_out : 1'bz;  // Controlled_Buffer controlled_buffer_7
  assign o[7] = e ? and_8_out : 1'bz;  // Controlled_Buffer controlled_buffer_8

  // Notes on the sheet:
  //   ML - Enabler Variant 2 met Controll Buffer
endmodule

module ML___2_4_DECODER_4_outputs_west (
  input  A,
  input  B,
  output out_3,
  output out_4,
  output out_5,
  output out_6
);

  wire not_1_out, not_2_out;

  not not_1 (not_1_out, A);
  not not_2 (not_2_out, B);
  and _00 (out_3, not_1_out, not_2_out);
  and _01 (out_4, A, not_2_out);
  and _10 (out_5, B, not_1_out);
  and _11 (out_6, A, B);

  // Notes on the sheet:
  //   nB
  //   nA
  //   15-10-25: Aangepast door lijntjes te wijzigen zoals ook in de cursus maar volgens mij klopt het daar niet
endmodule

module ML___2_4_DECODER_4_outputs_east (
  input  A,
  input  B,
  output out_3,
  output out_4,
  output out_5,
  output out_6
);

  wire not_1_out, not_2_out;

  not not_1 (not_1_out, A);
  not not_2 (not_2_out, B);
  and _00 (out_3, not_1_out, not_2_out);
  and _01 (out_4, A, not_2_out);
  and _10 (out_5, B, not_1_out);
  and _11 (out_6, B, A);

  // Notes on the sheet:
  //   A: pull=down
  //   B: pull=down
  //   18-11-25: weer verandert
  //   nA
  //   nB
  //   15-10-25: Aangepast door lijntjes te wijzigen zoals ook in de cursus maar volgens mij klopt het daar niet
endmodule

module ML___3_8_DECODER_1_output_east (
  input  C__Msb,
  input  B,
  input  A__Lsb,
  output [7:0] out_4
);

  wire not_1_out, not_2_out, not_3_out;

  not not_1 (not_1_out, C__Msb);
  not not_2 (not_2_out, B);
  not not_3 (not_3_out, A__Lsb);
  and _0__000 (out_4[0], not_1_out, not_2_out, not_3_out);
  and _1__001 (out_4[1], not_1_out, not_2_out, A__Lsb);
  and _2__010 (out_4[2], not_1_out, B, not_3_out);
  and _3__011 (out_4[3], not_1_out, B, A__Lsb);
  and _4__100 (out_4[4], C__Msb, not_2_out, not_3_out);
  and _5__101 (out_4[5], C__Msb, not_2_out, A__Lsb);
  and _6__110 (out_4[6], C__Msb, B, not_3_out);
  and _7__111 (out_4[7], C__Msb, B, A__Lsb);

  // Notes on the sheet:
  //   nB
  //   nA
  //   nC
  //   3*8 Decoder door ML 18-9-2025
endmodule

module ML___3_8_DECODER_8_outputs_east (
  input  C__Msb,
  input  B,
  input  A__Lsb,
  output out_4,
  output out_5,
  output out_6,
  output out_7,
  output out_8,
  output out_9,
  output out_10,
  output out_11
);

  wire not_1_out, not_2_out, not_3_out;

  not not_1 (not_1_out, C__Msb);
  not not_2 (not_2_out, B);
  not not_3 (not_3_out, A__Lsb);
  and _0__000 (out_4, not_1_out, not_2_out, not_3_out);
  and _1__001 (out_5, not_1_out, not_2_out, A__Lsb);
  and _2__010 (out_6, not_1_out, B, not_3_out);
  and _3__011 (out_7, not_1_out, B, A__Lsb);
  and _4__100 (out_8, C__Msb, not_2_out, not_3_out);
  and _5__101 (out_9, C__Msb, not_2_out, A__Lsb);
  and _6__110 (out_10, C__Msb, B, not_3_out);
  and _7__111 (out_11, C__Msb, B, A__Lsb);

  // Notes on the sheet:
  //   B: pull=down
  //   C__Msb: pull=down
  //   A__Lsb: pull=down
  //   nB
  //   nA
  //   nC
  //   3*8 Decoder door ML 15-10-2025 8 outputs east
endmodule

module ML___4_16_DECODER_16_outputs_west (
  input  [3:0] in_1,
  output [3:0] out_2,
  output _0000,
  output _0001,
  output _0010,
  output _0011,
  output _0100,
  output _0101,
  output _0110,
  output _0111,
  output _1000,
  output _1001,
  output _1010,
  output _1011,
  output _1100,
  output _1101,
  output _1110,
  output _1111
);

  not not_1 (out_2[0], in_1[0]);
  not not_2 (out_2[1], in_1[1]);
  not not_3 (out_2[2], in_1[2]);
  not not_4 (out_2[3], in_1[3]);
  and _0__0000 (_0000, out_2[0], out_2[1], out_2[2], out_2[3]);
  and _1__0001 (_0001, in_1[0], out_2[1], out_2[2], out_2[3]);
  and _2__0010 (_0010, out_2[0], in_1[1], out_2[2], out_2[3]);
  and _3__0011 (_0011, in_1[0], in_1[1], out_2[2], out_2[3]);
  and _4__0100 (_0100, out_2[0], out_2[1], in_1[2], out_2[3]);
  and _5__0101 (_0101, in_1[0], out_2[1], in_1[2], out_2[3]);
  and _6__0110 (_0110, out_2[0], in_1[1], in_1[2], out_2[3]);
  and _7__0111 (_0111, in_1[0], in_1[1], in_1[2], out_2[3]);
  and _8__1000 (_1000, out_2[0], out_2[1], out_2[2], in_1[3]);
  and _9__1001 (_1001, in_1[0], out_2[1], out_2[2], in_1[3]);
  and _10__1010 (_1010, out_2[0], in_1[1], out_2[2], in_1[3]);
  and _11__1011 (_1011, in_1[0], in_1[1], out_2[2], in_1[3]);
  and _12__1100 (_1100, out_2[0], out_2[1], in_1[2], in_1[3]);
  and _13__1101 (_1101, in_1[0], out_2[1], in_1[2], in_1[3]);
  and _14__1110 (_1110, out_2[0], in_1[1], in_1[2], in_1[3]);
  and _15__1111 (_1111, in_1[0], in_1[1], in_1[2], in_1[3]);

  // Notes on the sheet:
  //   in_1: pull=down
  //   4*16 Decoder
  //   23-9-2025: Door ML
endmodule

module ML___Memory_8 (
  input  [7:0] i,
  input  s,
  output [7:0] o
);

  ML___CPU_MEM_1 ml_cpu_mem_1_1 (.i(i[0]), .s(s), .o(o[0]));
  ML___CPU_MEM_1 ml_cpu_mem_1_2 (.i(i[1]), .s(s), .o(o[1]));
  ML___CPU_MEM_1 ml_cpu_mem_1_3 (.i(i[2]), .s(s), .o(o[2]));
  ML___CPU_MEM_1 ml_cpu_mem_1_4 (.i(i[3]), .s(s), .o(o[3]));
  ML___CPU_MEM_1 ml_cpu_mem_1_5 (.i(i[4]), .s(s), .o(o[4]));
  ML___CPU_MEM_1 ml_cpu_mem_1_6 (.i(i[5]), .s(s), .o(o[5]));
  ML___CPU_MEM_1 ml_cpu_mem_1_7 (.i(i[6]), .s(s), .o(o[6]));
  ML___CPU_MEM_1 ml_cpu_mem_1_8 (.i(i[7]), .s(s), .o(o[7]));

  // Notes on the sheet:
  //   i: pull=down
  //   s: pull=down
  //   o: pull=down
endmodule

module ML___Register_8 (
  input  [7:0] i,
  input  S,
  input  e,
  output [7:0] out_4,
  output [7:0] o
);

  wire [7:0] ml_enabler_variant_2_1_o;

  ML___Memory_8 ml_memory_8_1 (.i(i), .o(out_4), .s(S));
  ML___ENABLER_VARIANT_2 ml_enabler_variant_2_1 (.i(out_4), .o(ml_enabler_variant_2_1_o), .e(e));
  assign o = e ? ml_enabler_variant_2_1_o : 8'bz;  // Controlled_Buffer controlled_buffer_1

  // Notes on the sheet:
  //   out_4: pull=down
  //   i: pull=down
  //   o: pull=down
  //   Dit is een register: 8 Bit Memory + Enabler
  //   18-11-25: Niet meer ingebruik? Zie CPU_DESIGN_BONUS
  //   REG
  //   ML 25-9-25: Control Buffer toegevoegd
  //   8-10: Control buffer kan zomaar oorzaak van alle errors zijn geweest
  //   ML 25-9-25: De derde tussenliggende output pin (REG) er later bij gezet c.f. sectie 1 les 11
endmodule

module ML___Register (
  input  [7:0] \input ,
  input  s,
  input  e,
  output [7:0] out_4,
  output [7:0] \output 
);

  ML___Register_8 ml_register_8_1 (.i(\input ), .o(\output ), .S(s), .e(e), .out_4(out_4));

  // Notes on the sheet:
  //   output: pull=down
  //   e: pull=down
  //   input: pull=down
  //   out_4: pull=down
  //   s: pull=down
  //   Is bijna hetzelfde weer als accumulator
  //   Ik geloof dat hier alle bits gewoon de getallen voorstellen. De eerste mogelijk negatief.
  //   7-10-25: Register is hier het register dat in de CPU komt (4 stuks + 1 IAR). Dit is gelijk aan de Register_8. REG_BYTE is weer wat anders
endmodule

module ML___REG_BYTE (
  input  [7:0] \input ,
  input  reset,
  input  h,
  input  v,
  input  s,
  input  e,
  output [7:0] op,
  output [7:0] \output 
);

  wire and_1_out, and_2_out, and_3_out, or_1_out;
  wire [7:0] ml_register_8_1_o;

  and and_1 (and_1_out, h, v);
  and and_2 (and_2_out, and_1_out, s);
  and and_3 (and_3_out, and_1_out, e);
  or or_1 (or_1_out, reset, and_2_out);
  assign \output  = and_3_out ? ml_register_8_1_o : 8'bz;  // Controlled_Buffer controlled_buffer_1
  ML___Register_8 ml_register_8_1 (.i(\input ), .o(ml_register_8_1_o), .S(or_1_out), .e(and_3_out), .out_4(op));

  // Notes on the sheet:
  //   output: pull=down
  //   h: pull=down
  //   e: pull=down
  //   s: pull=down
  //   reset: pull=down
  //   input: pull=down
  //   op: pull=down
  //   v: pull=down
endmodule

module VB_automatisch_circuit_bouwen (
  input  a,
  input  b,
  input  c,
  output o1,
  output o2,
  output o3,
  output o4,
  output o5,
  output o6,
  output o7,
  output o8
);

  wire not_1_out, not_2_out, not_3_out, not_4_out, not_5_out, not_6_out, not_7_out, not_8_out, not_9_out,
       not_10_out, not_11_out, not_12_out;

  and and_1 (o1, a, b, c);
  and and_2 (o2, a, b, not_1_out);
  not not_1 (not_1_out, c);
  and and_3 (o3, a, not_2_out, c);
  not not_2 (not_2_out, b);
  not not_3 (not_3_out, b);
  and and_4 (o4, a, not_3_out, not_4_out);
  not not_4 (not_4_out, c);
  not not_5 (not_5_out, a);
  and and_5 (o5, not_5_out, b, c);
  not not_6 (not_6_out, a);
  and and_6 (o6, not_6_out, b, not_7_out);
  not not_7 (not_7_out, c);
  not not_8 (not_8_out, a);
  not not_9 (not_9_out, b);
  and and_7 (o7, not_8_out, not_9_out, c);
  not not_10 (not_10_out, a);
  not not_11 (not_11_out, b);
  and and_8 (o8, not_10_out, not_11_out, not_12_out);
  not not_12 (not_12_out, c);

  // Notes on the sheet:
  //   23-9-25: Sectie 1 les 9: voorbeeld van automatisch circuit bouwen
endmodule

module ML___Control_Buffer (
  input  in_1,
  input  in_2,
  input  in_3,
  input  in_4,
  input  in_5,
  input  in_6,
  input  in_7,
  input  in_8,
  input  in_9,
  input  in_10,
  input  in_11,
  input  in_12,
  input  in_13,
  input  in_14,
  input  in_15,
  input  in_16
);

  wire and_1_out, and_2_out, and_3_out, and_4_out, and_5_out, and_6_out, and_7_out, and_9_out, and_10_out,
       and_11_out, and_12_out, controlled_buffer_1_out, or_1_out, or_2_out, RESET_2_out, RESET_3_out,
       RESET_4_out, RESET_5_out, RESET_6_out, RESET_out;

  and and_1 (and_1_out, in_5, in_6);
  and and_2 (and_2_out, in_7, in_8);
  and and_3 (and_3_out, in_9, in_10);
  and and_4 (and_4_out, in_11, in_12);
  and and_5 (and_5_out, in_1, in_2);
  assign controlled_buffer_1_out = RESET_6_out ? and_5_out : 1'bz;  // Controlled_Buffer controlled_buffer_1
  assign controlled_buffer_1_out = RESET_out ? and_6_out : 1'bz;  // Controlled_Buffer controlled_buffer_2
  and and_6 (and_6_out, in_3, in_4);
  Button RESET (.out(RESET_out));
  and and_7 (and_7_out, and_1_out, RESET_3_out);
  and and_8 (and_7_out, and_2_out, RESET_2_out);
  Button RESET_2 (.out(RESET_2_out));
  Button RESET_3 (.out(RESET_3_out));
  Button RESET_4 (.out(RESET_4_out));
  Button RESET_5 (.out(RESET_5_out));
  and and_9 (and_9_out, in_13, in_14);
  and and_10 (and_10_out, in_15, in_16);
  Button RESET_6 (.out(RESET_6_out));
  and and_11 (and_11_out, and_3_out, RESET_5_out);
  or or_1 (or_1_out, and_11_out, and_12_out);
  and and_12 (and_12_out, and_4_out, RESET_4_out);
  or or_2 (or_2_out, and_9_out, and_10_out);

  // Notes on the sheet:
  //   INPUT A
  //   INPUT B
  //   INPUT A
  //   INPUT B
  //   INPUT A
  //   INPUT B
  //   INPUT A
  //   INPUT B
  //   BUS
  //   BUS
  //   BUS
  //   Control Buffer
  //   En dit ook
  //   ML 23-9-25: Waarom niet met and switches. Werkt niet blijkbaar
  //   Dit werkt wel geloof ik
  //   Combinatorisch gezien werkt het, alleen je moet in praktijk rekening houden met elektrisciteit.
endmodule

module ML___RAM_V4__kanweg (
  input  [7:0] address,
  input  sa,
  input  reset,
  input  s,
  input  e,
  input  [7:0] \input ,
  output [7:0] \output ,
  output [7:0] _15,
  output [7:0] _14,
  output [7:0] _13,
  output [7:0] _12,
  output [7:0] _11,
  output [7:0] _10,
  output [7:0] _9,
  output [7:0] _8,
  output [7:0] _7,
  output [7:0] _6,
  output [7:0] _5,
  output [7:0] _4,
  output [7:0] _3,
  output [7:0] _2,
  output [7:0] _1,
  output [7:0] _0,
  output [7:0] _31,
  output [7:0] _30,
  output [7:0] _29,
  output [7:0] _28,
  output [7:0] _27,
  output [7:0] _26,
  output [7:0] _25,
  output [7:0] _24,
  output [7:0] _23,
  output [7:0] _22,
  output [7:0] _21,
  output [7:0] _20,
  output [7:0] _19,
  output [7:0] _18,
  output [7:0] _17,
  output [7:0] _16,
  output [7:0] _47,
  output [7:0] _46,
  output [7:0] _45,
  output [7:0] _44,
  output [7:0] _43,
  output [7:0] _42,
  output [7:0] _41,
  output [7:0] _40,
  output [7:0] _39,
  output [7:0] _38,
  output [7:0] _37,
  output [7:0] _36,
  output [7:0] _35,
  output [7:0] _34,
  output [7:0] _33,
  output [7:0] _32,
  output [7:0] _63,
  output [7:0] _62,
  output [7:0] _61,
  output [7:0] _60,
  output [7:0] _59,
  output [7:0] _58,
  output [7:0] _57,
  output [7:0] _56,
  output [7:0] _55,
  output [7:0] _54,
  output [7:0] _53,
  output [7:0] _52,
  output [7:0] _51,
  output [7:0] _50,
  output [7:0] _49,
  output [7:0] _48
);

  wire ml_4_16_decoder_16_outputs_west_1__0000, ml_4_16_decoder_16_outputs_west_1__0001,
       ml_4_16_decoder_16_outputs_west_1__0010, ml_4_16_decoder_16_outputs_west_1__0011,
       ml_4_16_decoder_16_outputs_west_2__0000, ml_4_16_decoder_16_outputs_west_2__0001,
       ml_4_16_decoder_16_outputs_west_2__0010, ml_4_16_decoder_16_outputs_west_2__0011,
       ml_4_16_decoder_16_outputs_west_2__0100, ml_4_16_decoder_16_outputs_west_2__0101,
       ml_4_16_decoder_16_outputs_west_2__0110, ml_4_16_decoder_16_outputs_west_2__0111,
       ml_4_16_decoder_16_outputs_west_2__1000, ml_4_16_decoder_16_outputs_west_2__1001,
       ml_4_16_decoder_16_outputs_west_2__1010, ml_4_16_decoder_16_outputs_west_2__1011,
       ml_4_16_decoder_16_outputs_west_2__1100, ml_4_16_decoder_16_outputs_west_2__1101,
       ml_4_16_decoder_16_outputs_west_2__1110, ml_4_16_decoder_16_outputs_west_2__1111;
  wire [7:0] ml_memory_8_1_p3, ml_reg_byte_1_output;

  // ML___Memory_8 ml_memory_8_1: pin names not known; wires that end beside it: address, sa, ml_memory_8_1_p3
  assign \output  = e ? ml_reg_byte_1_output : 8'bz;  // Controlled_Buffer controlled_buffer_1
  ML___4_16_DECODER_16_outputs_west ml_4_16_decoder_16_outputs_west_1 (
    .in_1(ml_memory_8_1_p3[7:4]), ._0000(ml_4_16_decoder_16_outputs_west_1__0000),
    ._0001(ml_4_16_decoder_16_outputs_west_1__0001), ._0010(ml_4_16_decoder_16_outputs_west_1__0010),
    ._0011(ml_4_16_decoder_16_outputs_west_1__0011));  // open: out_2, _0100, _0101, _0110, _0111, _1000, _1001, _1010, _1011, _1100, _1101, _1110, _1111
  ML___REG_BYTE ml_reg_byte_1 (
    .op(_15), .\output (ml_reg_byte_1_output), .\input (\input ),
    .h(ml_4_16_decoder_16_outputs_west_1__0000), .v(ml_4_16_decoder_16_outputs_west_2__1111), .s(s), .e(e),
    .reset(reset));
  ML___REG_BYTE ml_reg_byte_2 (
    .op(_31), .\output (ml_reg_byte_1_output), .\input (\input ),
    .h(ml_4_16_decoder_16_outputs_west_1__0001), .v(ml_4_16_decoder_16_outputs_west_2__1111), .s(s), .e(e),
    .reset(reset));
  ML___REG_BYTE ml_reg_byte_3 (
    .op(_47), .\output (ml_reg_byte_1_output), .\input (\input ),
    .h(ml_4_16_decoder_16_outputs_west_1__0010), .v(ml_4_16_decoder_16_outputs_west_2__1111), .s(s), .e(e),
    .reset(reset));
  ML___REG_BYTE ml_reg_byte_4 (
    .op(_63), .\output (ml_reg_byte_1_output), .\input (\input ),
    .h(ml_4_16_decoder_16_outputs_west_1__0011), .v(ml_4_16_decoder_16_outputs_west_2__1111), .s(s), .e(e),
    .reset(reset));
  ML___REG_BYTE ml_reg_byte_5 (
    .op(_14), .\output (ml_reg_byte_1_output), .\input (\input ),
    .h(ml_4_16_decoder_16_outputs_west_1__0000), .v(ml_4_16_decoder_16_outputs_west_2__1110), .s(s), .e(e),
    .reset(reset));
  ML___REG_BYTE ml_reg_byte_6 (
    .op(_30), .\output (ml_reg_byte_1_output), .\input (\input ),
    .h(ml_4_16_decoder_16_outputs_west_1__0001), .v(ml_4_16_decoder_16_outputs_west_2__1110), .s(s), .e(e),
    .reset(reset));
  ML___REG_BYTE ml_reg_byte_7 (
    .op(_46), .\output (ml_reg_byte_1_output), .\input (\input ),
    .h(ml_4_16_decoder_16_outputs_west_1__0010), .v(ml_4_16_decoder_16_outputs_west_2__1110), .s(s), .e(e),
    .reset(reset));
  ML___REG_BYTE ml_reg_byte_8 (
    .op(_62), .\output (ml_reg_byte_1_output), .\input (\input ),
    .h(ml_4_16_decoder_16_outputs_west_1__0011), .v(ml_4_16_decoder_16_outputs_west_2__1110), .s(s), .e(e),
    .reset(reset));
  ML___REG_BYTE ml_reg_byte_9 (
    .op(_13), .\output (ml_reg_byte_1_output), .\input (\input ),
    .h(ml_4_16_decoder_16_outputs_west_1__0000), .v(ml_4_16_decoder_16_outputs_west_2__1101), .s(s), .e(e),
    .reset(reset));
  ML___REG_BYTE ml_reg_byte_10 (
    .op(_29), .\output (ml_reg_byte_1_output), .\input (\input ),
    .h(ml_4_16_decoder_16_outputs_west_1__0001), .v(ml_4_16_decoder_16_outputs_west_2__1101), .s(s), .e(e),
    .reset(reset));
  ML___REG_BYTE ml_reg_byte_11 (
    .op(_45), .\output (ml_reg_byte_1_output), .\input (\input ),
    .h(ml_4_16_decoder_16_outputs_west_1__0010), .v(ml_4_16_decoder_16_outputs_west_2__1101), .s(s), .e(e),
    .reset(reset));
  ML___REG_BYTE ml_reg_byte_12 (
    .op(_61), .\output (ml_reg_byte_1_output), .\input (\input ),
    .h(ml_4_16_decoder_16_outputs_west_1__0011), .v(ml_4_16_decoder_16_outputs_west_2__1101), .s(s), .e(e),
    .reset(reset));
  ML___REG_BYTE ml_reg_byte_13 (
    .op(_12), .\output (ml_reg_byte_1_output), .\input (\input ),
    .h(ml_4_16_decoder_16_outputs_west_1__0000), .v(ml_4_16_decoder_16_outputs_west_2__1100), .s(s), .e(e),
    .reset(reset));
  ML___REG_BYTE ml_reg_byte_14 (
    .op(_28), .\output (ml_reg_byte_1_output), .\input (\input ),
    .h(ml_4_16_decoder_16_outputs_west_1__0001), .v(ml_4_16_decoder_16_outputs_west_2__1100), .s(s), .e(e),
    .reset(reset));
  ML___REG_BYTE ml_reg_byte_15 (
    .op(_44), .\output (ml_reg_byte_1_output), .\input (\input ),
    .h(ml_4_16_decoder_16_outputs_west_1__0010), .v(ml_4_16_decoder_16_outputs_west_2__1100), .s(s), .e(e),
    .reset(reset));
  ML___REG_BYTE ml_reg_byte_16 (
    .op(_60), .\output (ml_reg_byte_1_output), .\input (\input ),
    .h(ml_4_16_decoder_16_outputs_west_1__0011), .v(ml_4_16_decoder_16_outputs_west_2__1100), .s(s), .e(e),
    .reset(reset));
  ML___REG_BYTE ml_reg_byte_17 (
    .op(_11), .\output (ml_reg_byte_1_output), .\input (\input ),
    .h(ml_4_16_decoder_16_outputs_west_1__0000), .v(ml_4_16_decoder_16_outputs_west_2__1011), .s(s), .e(e),
    .reset(reset));
  ML___REG_BYTE ml_reg_byte_18 (
    .op(_27), .\output (ml_reg_byte_1_output), .\input (\input ),
    .h(ml_4_16_decoder_16_outputs_west_1__0001), .v(ml_4_16_decoder_16_outputs_west_2__1011), .s(s), .e(e),
    .reset(reset));
  ML___REG_BYTE ml_reg_byte_19 (
    .op(_43), .\output (ml_reg_byte_1_output), .\input (\input ),
    .h(ml_4_16_decoder_16_outputs_west_1__0010), .v(ml_4_16_decoder_16_outputs_west_2__1011), .s(s), .e(e),
    .reset(reset));
  ML___REG_BYTE ml_reg_byte_20 (
    .op(_59), .\output (ml_reg_byte_1_output), .\input (\input ),
    .h(ml_4_16_decoder_16_outputs_west_1__0011), .v(ml_4_16_decoder_16_outputs_west_2__1011), .s(s), .e(e),
    .reset(reset));
  ML___REG_BYTE ml_reg_byte_21 (
    .op(_10), .\output (ml_reg_byte_1_output), .\input (\input ),
    .h(ml_4_16_decoder_16_outputs_west_1__0000), .v(ml_4_16_decoder_16_outputs_west_2__1010), .s(s), .e(e),
    .reset(reset));
  ML___REG_BYTE ml_reg_byte_22 (
    .op(_26), .\output (ml_reg_byte_1_output), .\input (\input ),
    .h(ml_4_16_decoder_16_outputs_west_1__0001), .v(ml_4_16_decoder_16_outputs_west_2__1010), .s(s), .e(e),
    .reset(reset));
  ML___REG_BYTE ml_reg_byte_23 (
    .op(_42), .\output (ml_reg_byte_1_output), .\input (\input ),
    .h(ml_4_16_decoder_16_outputs_west_1__0010), .v(ml_4_16_decoder_16_outputs_west_2__1010), .s(s), .e(e),
    .reset(reset));
  ML___REG_BYTE ml_reg_byte_24 (
    .op(_58), .\output (ml_reg_byte_1_output), .\input (\input ),
    .h(ml_4_16_decoder_16_outputs_west_1__0011), .v(ml_4_16_decoder_16_outputs_west_2__1010), .s(s), .e(e),
    .reset(reset));
  ML___REG_BYTE ml_reg_byte_25 (
    .op(_9), .\output (ml_reg_byte_1_output), .\input (\input ), .h(ml_4_16_decoder_16_outputs_west_1__0000),
    .v(ml_4_16_decoder_16_outputs_west_2__1001), .s(s), .e(e), .reset(reset));
  ML___REG_BYTE ml_reg_byte_26 (
    .op(_25), .\output (ml_reg_byte_1_output), .\input (\input ),
    .h(ml_4_16_decoder_16_outputs_west_1__0001), .v(ml_4_16_decoder_16_outputs_west_2__1001), .s(s), .e(e),
    .reset(reset));
  ML___REG_BYTE ml_reg_byte_27 (
    .op(_41), .\output (ml_reg_byte_1_output), .\input (\input ),
    .h(ml_4_16_decoder_16_outputs_west_1__0010), .v(ml_4_16_decoder_16_outputs_west_2__1001), .s(s), .e(e),
    .reset(reset));
  ML___REG_BYTE ml_reg_byte_28 (
    .op(_57), .\output (ml_reg_byte_1_output), .\input (\input ),
    .h(ml_4_16_decoder_16_outputs_west_1__0011), .v(ml_4_16_decoder_16_outputs_west_2__1001), .s(s), .e(e),
    .reset(reset));
  ML___REG_BYTE ml_reg_byte_29 (
    .op(_8), .\output (ml_reg_byte_1_output), .\input (\input ), .h(ml_4_16_decoder_16_outputs_west_1__0000),
    .v(ml_4_16_decoder_16_outputs_west_2__1000), .s(s), .e(e), .reset(reset));
  ML___REG_BYTE ml_reg_byte_30 (
    .op(_24), .\output (ml_reg_byte_1_output), .\input (\input ),
    .h(ml_4_16_decoder_16_outputs_west_1__0001), .v(ml_4_16_decoder_16_outputs_west_2__1000), .s(s), .e(e),
    .reset(reset));
  ML___REG_BYTE ml_reg_byte_31 (
    .op(_40), .\output (ml_reg_byte_1_output), .\input (\input ),
    .h(ml_4_16_decoder_16_outputs_west_1__0010), .v(ml_4_16_decoder_16_outputs_west_2__1000), .s(s), .e(e),
    .reset(reset));
  ML___REG_BYTE ml_reg_byte_32 (
    .op(_56), .\output (ml_reg_byte_1_output), .\input (\input ),
    .h(ml_4_16_decoder_16_outputs_west_1__0011), .v(ml_4_16_decoder_16_outputs_west_2__1000), .s(s), .e(e),
    .reset(reset));
  ML___4_16_DECODER_16_outputs_west ml_4_16_decoder_16_outputs_west_2 (
    .in_1(ml_memory_8_1_p3[3:0]), ._0000(ml_4_16_decoder_16_outputs_west_2__0000),
    ._0001(ml_4_16_decoder_16_outputs_west_2__0001), ._0010(ml_4_16_decoder_16_outputs_west_2__0010),
    ._0011(ml_4_16_decoder_16_outputs_west_2__0011), ._0100(ml_4_16_decoder_16_outputs_west_2__0100),
    ._0101(ml_4_16_decoder_16_outputs_west_2__0101), ._0110(ml_4_16_decoder_16_outputs_west_2__0110),
    ._0111(ml_4_16_decoder_16_outputs_west_2__0111), ._1000(ml_4_16_decoder_16_outputs_west_2__1000),
    ._1001(ml_4_16_decoder_16_outputs_west_2__1001), ._1010(ml_4_16_decoder_16_outputs_west_2__1010),
    ._1011(ml_4_16_decoder_16_outputs_west_2__1011), ._1100(ml_4_16_decoder_16_outputs_west_2__1100),
    ._1101(ml_4_16_decoder_16_outputs_west_2__1101), ._1110(ml_4_16_decoder_16_outputs_west_2__1110),
    ._1111(ml_4_16_decoder_16_outputs_west_2__1111));  // open: out_2
  ML___REG_BYTE ml_reg_byte_33 (
    .op(_7), .\output (ml_reg_byte_1_output), .\input (\input ), .h(ml_4_16_decoder_16_outputs_west_1__0000),
    .v(ml_4_16_decoder_16_outputs_west_2__0111), .s(s), .e(e), .reset(reset));
  ML___REG_BYTE ml_reg_byte_34 (
    .op(_23), .\output (ml_reg_byte_1_output), .\input (\input ),
    .h(ml_4_16_decoder_16_outputs_west_1__0001), .v(ml_4_16_decoder_16_outputs_west_2__0111), .s(s), .e(e),
    .reset(reset));
  ML___REG_BYTE ml_reg_byte_35 (
    .op(_39), .\output (ml_reg_byte_1_output), .\input (\input ),
    .h(ml_4_16_decoder_16_outputs_west_1__0010), .v(ml_4_16_decoder_16_outputs_west_2__0111), .s(s), .e(e),
    .reset(reset));
  ML___REG_BYTE ml_reg_byte_36 (
    .op(_55), .\output (ml_reg_byte_1_output), .\input (\input ),
    .h(ml_4_16_decoder_16_outputs_west_1__0011), .v(ml_4_16_decoder_16_outputs_west_2__0111), .s(s), .e(e),
    .reset(reset));
  ML___REG_BYTE ml_reg_byte_37 (
    .op(_6), .\output (ml_reg_byte_1_output), .\input (\input ), .h(ml_4_16_decoder_16_outputs_west_1__0000),
    .v(ml_4_16_decoder_16_outputs_west_2__0110), .s(s), .e(e), .reset(reset));
  ML___REG_BYTE ml_reg_byte_38 (
    .op(_22), .\output (ml_reg_byte_1_output), .\input (\input ),
    .h(ml_4_16_decoder_16_outputs_west_1__0001), .v(ml_4_16_decoder_16_outputs_west_2__0110), .s(s), .e(e),
    .reset(reset));
  ML___REG_BYTE ml_reg_byte_39 (
    .op(_38), .\output (ml_reg_byte_1_output), .\input (\input ),
    .h(ml_4_16_decoder_16_outputs_west_1__0010), .v(ml_4_16_decoder_16_outputs_west_2__0110), .s(s), .e(e),
    .reset(reset));
  ML___REG_BYTE ml_reg_byte_40 (
    .op(_54), .\output (ml_reg_byte_1_output), .\input (\input ),
    .h(ml_4_16_decoder_16_outputs_west_1__0011), .v(ml_4_16_decoder_16_outputs_west_2__0110), .s(s), .e(e),
    .reset(reset));
  ML___REG_BYTE ml_reg_byte_41 (
    .op(_5), .\output (ml_reg_byte_1_output), .\input (\input ), .h(ml_4_16_decoder_16_outputs_west_1__0000),
    .v(ml_4_16_decoder_16_outputs_west_2__0101), .s(s), .e(e), .reset(reset));
  ML___REG_BYTE ml_reg_byte_42 (
    .op(_21), .\output (ml_reg_byte_1_output), .\input (\input ),
    .h(ml_4_16_decoder_16_outputs_west_1__0001), .v(ml_4_16_decoder_16_outputs_west_2__0101), .s(s), .e(e),
    .reset(reset));
  ML___REG_BYTE ml_reg_byte_43 (
    .op(_37), .\output (ml_reg_byte_1_output), .\input (\input ),
    .h(ml_4_16_decoder_16_outputs_west_1__0010), .v(ml_4_16_decoder_16_outputs_west_2__0101), .s(s), .e(e),
    .reset(reset));
  ML___REG_BYTE ml_reg_byte_44 (
    .op(_53), .\output (ml_reg_byte_1_output), .\input (\input ),
    .h(ml_4_16_decoder_16_outputs_west_1__0011), .v(ml_4_16_decoder_16_outputs_west_2__0101), .s(s), .e(e),
    .reset(reset));
  ML___REG_BYTE ml_reg_byte_45 (
    .op(_4), .\output (ml_reg_byte_1_output), .\input (\input ), .h(ml_4_16_decoder_16_outputs_west_1__0000),
    .v(ml_4_16_decoder_16_outputs_west_2__0100), .s(s), .e(e), .reset(reset));
  ML___REG_BYTE ml_reg_byte_46 (
    .op(_20), .\output (ml_reg_byte_1_output), .\input (\input ),
    .h(ml_4_16_decoder_16_outputs_west_1__0001), .v(ml_4_16_decoder_16_outputs_west_2__0100), .s(s), .e(e),
    .reset(reset));
  ML___REG_BYTE ml_reg_byte_47 (
    .op(_36), .\output (ml_reg_byte_1_output), .\input (\input ),
    .h(ml_4_16_decoder_16_outputs_west_1__0010), .v(ml_4_16_decoder_16_outputs_west_2__0100), .s(s), .e(e),
    .reset(reset));
  ML___REG_BYTE ml_reg_byte_48 (
    .op(_52), .\output (ml_reg_byte_1_output), .\input (\input ),
    .h(ml_4_16_decoder_16_outputs_west_1__0011), .v(ml_4_16_decoder_16_outputs_west_2__0100), .s(s), .e(e),
    .reset(reset));
  ML___REG_BYTE ml_reg_byte_49 (
    .op(_3), .\output (ml_reg_byte_1_output), .\input (\input ), .h(ml_4_16_decoder_16_outputs_west_1__0000),
    .v(ml_4_16_decoder_16_outputs_west_2__0011), .s(s), .e(e), .reset(reset));
  ML___REG_BYTE ml_reg_byte_50 (
    .op(_19), .\output (ml_reg_byte_1_output), .\input (\input ),
    .h(ml_4_16_decoder_16_outputs_west_1__0001), .v(ml_4_16_decoder_16_outputs_west_2__0011), .s(s), .e(e),
    .reset(reset));
  ML___REG_BYTE ml_reg_byte_51 (
    .op(_35), .\output (ml_reg_byte_1_output), .\input (\input ),
    .h(ml_4_16_decoder_16_outputs_west_1__0010), .v(ml_4_16_decoder_16_outputs_west_2__0011), .s(s), .e(e),
    .reset(reset));
  ML___REG_BYTE ml_reg_byte_52 (
    .op(_51), .\output (ml_reg_byte_1_output), .\input (\input ),
    .h(ml_4_16_decoder_16_outputs_west_1__0011), .v(ml_4_16_decoder_16_outputs_west_2__0011), .s(s), .e(e),
    .reset(reset));
  ML___REG_BYTE ml_reg_byte_53 (
    .op(_2), .\output (ml_reg_byte_1_output), .\input (\input ), .h(ml_4_16_decoder_16_outputs_west_1__0000),
    .v(ml_4_16_decoder_16_outputs_west_2__0010), .s(s), .e(e), .reset(reset));
  ML___REG_BYTE ml_reg_byte_54 (
    .op(_18), .\output (ml_reg_byte_1_output), .\input (\input ),
    .h(ml_4_16_decoder_16_outputs_west_1__0001), .v(ml_4_16_decoder_16_outputs_west_2__0010), .s(s), .e(e),
    .reset(reset));
  ML___REG_BYTE ml_reg_byte_55 (
    .op(_34), .\output (ml_reg_byte_1_output), .\input (\input ),
    .h(ml_4_16_decoder_16_outputs_west_1__0010), .v(ml_4_16_decoder_16_outputs_west_2__0010), .s(s), .e(e),
    .reset(reset));
  ML___REG_BYTE ml_reg_byte_56 (
    .op(_50), .\output (ml_reg_byte_1_output), .\input (\input ),
    .h(ml_4_16_decoder_16_outputs_west_1__0011), .v(ml_4_16_decoder_16_outputs_west_2__0010), .s(s), .e(e),
    .reset(reset));
  ML___REG_BYTE ml_reg_byte_57 (
    .op(_1), .\output (ml_reg_byte_1_output), .\input (\input ), .h(ml_4_16_decoder_16_outputs_west_1__0000),
    .v(ml_4_16_decoder_16_outputs_west_2__0001), .s(s), .e(e), .reset(reset));
  ML___REG_BYTE ml_reg_byte_58 (
    .op(_17), .\output (ml_reg_byte_1_output), .\input (\input ),
    .h(ml_4_16_decoder_16_outputs_west_1__0001), .v(ml_4_16_decoder_16_outputs_west_2__0001), .s(s), .e(e),
    .reset(reset));
  ML___REG_BYTE ml_reg_byte_59 (
    .op(_33), .\output (ml_reg_byte_1_output), .\input (\input ),
    .h(ml_4_16_decoder_16_outputs_west_1__0010), .v(ml_4_16_decoder_16_outputs_west_2__0001), .s(s), .e(e),
    .reset(reset));
  ML___REG_BYTE ml_reg_byte_60 (
    .op(_49), .\output (ml_reg_byte_1_output), .\input (\input ),
    .h(ml_4_16_decoder_16_outputs_west_1__0011), .v(ml_4_16_decoder_16_outputs_west_2__0001), .s(s), .e(e),
    .reset(reset));
  ML___REG_BYTE ml_reg_byte_61 (
    .op(_0), .\output (ml_reg_byte_1_output), .\input (\input ), .h(ml_4_16_decoder_16_outputs_west_1__0000),
    .v(ml_4_16_decoder_16_outputs_west_2__0000), .s(s), .e(e), .reset(reset));
  ML___REG_BYTE ml_reg_byte_62 (
    .op(_16), .\output (ml_reg_byte_1_output), .\input (\input ),
    .h(ml_4_16_decoder_16_outputs_west_1__0001), .v(ml_4_16_decoder_16_outputs_west_2__0000), .s(s), .e(e),
    .reset(reset));
  ML___REG_BYTE ml_reg_byte_63 (
    .op(_32), .\output (ml_reg_byte_1_output), .\input (\input ),
    .h(ml_4_16_decoder_16_outputs_west_1__0010), .v(ml_4_16_decoder_16_outputs_west_2__0000), .s(s), .e(e),
    .reset(reset));
  ML___REG_BYTE ml_reg_byte_64 (
    .op(_48), .\output (ml_reg_byte_1_output), .\input (\input ),
    .h(ml_4_16_decoder_16_outputs_west_1__0011), .v(ml_4_16_decoder_16_outputs_west_2__0000), .s(s), .e(e),
    .reset(reset));

  // Notes on the sheet:
  //   ML - RAM 1 oktober 2025
  //   2-10-25: 64 Byte RAm zou moeten werken
endmodule

module ML___Adder (
  input  a,
  input  b,
  input  carry_in,
  output sum,
  output carry_out
);

  wire and_1_out, and_2_out, xor_1_out;

  xor xor_1 (xor_1_out, a, b);
  and and_1 (and_1_out, carry_in, xor_1_out);
  and and_2 (and_2_out, a, b);
  xor xor_2 (sum, xor_1_out, carry_in);
  or or_1 (carry_out, and_1_out, and_2_out);

  // Notes on the sheet:
  //   ML 2-10-25: Full Adder
endmodule

module ML___Adder_8 (
  input  [7:0] in_1,
  input  Carry_In,
  input  [7:0] in_3,
  output Carry_Out,
  output [7:0] out_5
);

  wire ml_adder_2_carry_out, ml_adder_3_carry_out, ml_adder_4_carry_out, ml_adder_5_carry_out,
       ml_adder_6_carry_out, ml_adder_7_carry_out, ml_adder_8_carry_out;

  ML___Adder ml_adder_1 (
    .a(in_1[7]), .b(in_3[7]), .carry_in(ml_adder_2_carry_out), .sum(out_5[7]), .carry_out(Carry_Out));
  ML___Adder ml_adder_2 (
    .a(in_1[6]), .b(in_3[6]), .carry_in(ml_adder_3_carry_out), .sum(out_5[6]),
    .carry_out(ml_adder_2_carry_out));
  ML___Adder ml_adder_3 (
    .a(in_1[5]), .b(in_3[5]), .carry_in(ml_adder_4_carry_out), .sum(out_5[5]),
    .carry_out(ml_adder_3_carry_out));
  ML___Adder ml_adder_4 (
    .a(in_1[4]), .b(in_3[4]), .carry_in(ml_adder_5_carry_out), .sum(out_5[4]),
    .carry_out(ml_adder_4_carry_out));
  ML___Adder ml_adder_5 (
    .a(in_1[3]), .b(in_3[3]), .carry_in(ml_adder_6_carry_out), .sum(out_5[3]),
    .carry_out(ml_adder_5_carry_out));
  ML___Adder ml_adder_6 (
    .a(in_1[2]), .b(in_3[2]), .carry_in(ml_adder_7_carry_out), .sum(out_5[2]),
    .carry_out(ml_adder_6_carry_out));
  ML___Adder ml_adder_7 (
    .a(in_1[1]), .b(in_3[1]), .carry_in(ml_adder_8_carry_out), .sum(out_5[1]),
    .carry_out(ml_adder_7_carry_out));
  ML___Adder ml_adder_8 (
    .a(in_1[0]), .b(in_3[0]), .carry_in(Carry_In), .sum(out_5[0]), .carry_out(ml_adder_8_carry_out));

  // Notes on the sheet:
  //   Let op bits omgedraaid in splitter
  //   ML 3-10-2025: CPU - ADDER
  //   Most Significant Bit
  //   Least Significant Bit
endmodule
module ML___RAM_V7_256_byte (
  input  [7:0] address,
  input  sa,
  input  reset,
  input  s,
  input  e,
  input  [7:0] \input ,
  output [7:0] \output ,
  output [7:0] _15,
  output [7:0] _14,
  output [7:0] _13,
  output [7:0] _12,
  output [7:0] _11,
  output [7:0] _10,
  output [7:0] _9,
  output [7:0] _8,
  output [7:0] _7,
  output [7:0] _6,
  output [7:0] _5,
  output [7:0] _4,
  output [7:0] _3,
  output [7:0] _2,
  output [7:0] _1,
  output [7:0] _0,
  output [7:0] _31,
  output [7:0] _30,
  output [7:0] _29,
  output [7:0] _28,
  output [7:0] _27,
  output [7:0] _26,
  output [7:0] _25,
  output [7:0] _24,
  output [7:0] _23,
  output [7:0] _22,
  output [7:0] _21,
  output [7:0] _20,
  output [7:0] _19,
  output [7:0] _18,
  output [7:0] _17,
  output [7:0] _16,
  output [7:0] _47,
  output [7:0] _46,
  output [7:0] _45,
  output [7:0] _44,
  output [7:0] _43,
  output [7:0] _42,
  output [7:0] _41,
  output [7:0] _40,
  output [7:0] _39,
  output [7:0] _38,
  output [7:0] _37,
  output [7:0] _36,
  output [7:0] _35,
  output [7:0] _34,
  output [7:0] _33,
  output [7:0] _32,
  output [7:0] _63,
  output [7:0] _62,
  output [7:0] _61,
  output [7:0] _60,
  output [7:0] _59,
  output [7:0] _58,
  output [7:0] _57,
  output [7:0] _56,
  output [7:0] _55,
  output [7:0] _54,
  output [7:0] _53,
  output [7:0] _52,
  output [7:0] _51,
  output [7:0] _50,
  output [7:0] _49,
  output [7:0] _48,
  output [7:0] _79,
  output [7:0] _78,
  output [7:0] _77,
  output [7:0] _76,
  output [7:0] _75,
  output [7:0] _74,
  output [7:0] _73,
  output [7:0] _72,
  output [7:0] _71,
  output [7:0] _70,
  output [7:0] _69,
  output [7:0] _68,
  output [7:0] _67,
  output [7:0] _66,
  output [7:0] _65,
  output [7:0] _64,
  output [7:0] _95,
  output [7:0] _94,
  output [7:0] _93,
  output [7:0] _92,
  output [7:0] _91,
  output [7:0] _90,
  output [7:0] _89,
  output [7:0] _88,
  output [7:0] _87,
  output [7:0] _86,
  output [7:0] _85,
  output [7:0] _84,
  output [7:0] _83,
  output [7:0] _82,
  output [7:0] _81,
  output [7:0] _80,
  output [7:0] _111,
  output [7:0] _110,
  output [7:0] _109,
  output [7:0] _108,
  output [7:0] _107,
  output [7:0] _106,
  output [7:0] _105,
  output [7:0] _104,
  output [7:0] _103,
  output [7:0] _102,
  output [7:0] _101,
  output [7:0] _100,
  output [7:0] _99,
  output [7:0] _98,
  output [7:0] _97,
  output [7:0] _96,
  output [7:0] _127,
  output [7:0] _126,
  output [7:0] _125,
  output [7:0] _124,
  output [7:0] _123,
  output [7:0] _122,
  output [7:0] _121,
  output [7:0] _120,
  output [7:0] _119,
  output [7:0] _118,
  output [7:0] _117,
  output [7:0] _116,
  output [7:0] _115,
  output [7:0] _114,
  output [7:0] _113,
  output [7:0] _112,
  output [7:0] _143,
  output [7:0] _142,
  output [7:0] _141,
  output [7:0] _140,
  output [7:0] _139,
  output [7:0] _138,
  output [7:0] _137,
  output [7:0] _136,
  output [7:0] _135,
  output [7:0] _134,
  output [7:0] _133,
  output [7:0] _132,
  output [7:0] _131,
  output [7:0] _130,
  output [7:0] _129,
  output [7:0] _128,
  output [7:0] _159,
  output [7:0] _158,
  output [7:0] _157,
  output [7:0] _156,
  output [7:0] _155,
  output [7:0] _154,
  output [7:0] _153,
  output [7:0] _152,
  output [7:0] _151,
  output [7:0] _150,
  output [7:0] _149,
  output [7:0] _148,
  output [7:0] _147,
  output [7:0] _18_2,
  output [7:0] _145,
  output [7:0] _144,
  output [7:0] _175,
  output [7:0] _174,
  output [7:0] _173,
  output [7:0] _172,
  output [7:0] _171,
  output [7:0] _170,
  output [7:0] _169,
  output [7:0] _168,
  output [7:0] _167,
  output [7:0] _166,
  output [7:0] _165,
  output [7:0] _164,
  output [7:0] _163,
  output [7:0] _162,
  output [7:0] _161,
  output [7:0] _160,
  output [7:0] _191,
  output [7:0] _190,
  output [7:0] _189,
  output [7:0] _188,
  output [7:0] _187,
  output [7:0] _186,
  output [7:0] _185,
  output [7:0] _184,
  output [7:0] _183,
  output [7:0] _182,
  output [7:0] _181,
  output [7:0] _180,
  output [7:0] _179,
  output [7:0] _178,
  output [7:0] _177,
  output [7:0] _176,
  output [7:0] _207,
  output [7:0] _206,
  output [7:0] _205,
  output [7:0] _204,
  output [7:0] _203,
  output [7:0] _202,
  output [7:0] _201,
  output [7:0] _72_2,
  output [7:0] _199,
  output [7:0] _198,
  output [7:0] _197,
  output [7:0] _196,
  output [7:0] _195,
  output [7:0] _194,
  output [7:0] _193,
  output [7:0] _192,
  output [7:0] _223,
  output [7:0] _222,
  output [7:0] _221,
  output [7:0] _220,
  output [7:0] _219,
  output [7:0] _218,
  output [7:0] _217,
  output [7:0] _216,
  output [7:0] _215,
  output [7:0] _214,
  output [7:0] _213,
  output [7:0] _212,
  output [7:0] _211,
  output [7:0] _210,
  output [7:0] _209,
  output [7:0] _208,
  output [7:0] _239,
  output [7:0] _238,
  output [7:0] _237,
  output [7:0] _236,
  output [7:0] _235,
  output [7:0] _234,
  output [7:0] _233,
  output [7:0] _232,
  output [7:0] _231,
  output [7:0] _230,
  output [7:0] _229,
  output [7:0] _228,
  output [7:0] _227,
  output [7:0] _226,
  output [7:0] _225,
  output [7:0] _224,
  output [7:0] _255,
  output [7:0] _254,
  output [7:0] _253,
  output [7:0] _252,
  output [7:0] _251,
  output [7:0] _250,
  output [7:0] _249,
  output [7:0] _248,
  output [7:0] _247,
  output [7:0] _246,
  output [7:0] _245,
  output [7:0] _244,
  output [7:0] _243,
  output [7:0] _242,
  output [7:0] _241,
  output [7:0] _240
);

  wire ml_4_16_decoder_16_outputs_west_1__0000, ml_4_16_decoder_16_outputs_west_1__0001,
       ml_4_16_decoder_16_outputs_west_1__0010, ml_4_16_decoder_16_outputs_west_1__0011,
       ml_4_16_decoder_16_outputs_west_1__0100, ml_4_16_decoder_16_outputs_west_1__0101,
       ml_4_16_decoder_16_outputs_west_1__0110, ml_4_16_decoder_16_outputs_west_1__0111,
       ml_4_16_decoder_16_outputs_west_1__1000, ml_4_16_decoder_16_outputs_west_1__1001,
       ml_4_16_decoder_16_outputs_west_1__1010, ml_4_16_decoder_16_outputs_west_1__1011,
       ml_4_16_decoder_16_outputs_west_1__1100, ml_4_16_decoder_16_outputs_west_1__1101,
       ml_4_16_decoder_16_outputs_west_1__1110, ml_4_16_decoder_16_outputs_west_1__1111,
       ml_4_16_decoder_16_outputs_west_2__0000, ml_4_16_decoder_16_outputs_west_2__0001,
       ml_4_16_decoder_16_outputs_west_2__0010, ml_4_16_decoder_16_outputs_west_2__0011,
       ml_4_16_decoder_16_outputs_west_2__0100, ml_4_16_decoder_16_outputs_west_2__0101,
       ml_4_16_decoder_16_outputs_west_2__0110, ml_4_16_decoder_16_outputs_west_2__0111,
       ml_4_16_decoder_16_outputs_west_2__1000, ml_4_16_decoder_16_outputs_west_2__1001,
       ml_4_16_decoder_16_outputs_west_2__1010, ml_4_16_decoder_16_outputs_west_2__1011,
       ml_4_16_decoder_16_outputs_west_2__1100, ml_4_16_decoder_16_outputs_west_2__1101,
       ml_4_16_decoder_16_outputs_west_2__1110, ml_4_16_decoder_16_outputs_west_2__1111;
  wire [7:0] ml_reg_byte_1_output, ml_register_8_1_o;

  ML___Register_8 ml_register_8_1 (.i(address), .o(ml_register_8_1_o), .S(sa), .e(sa));  // open: out_4
  assign \output  = e ? ml_reg_byte_1_output : 8'bz;  // Controlled_Buffer controlled_buffer_1
  ML___4_16_DECODER_16_outputs_west ml_4_16_decoder_16_outputs_west_1 (
    .in_1(ml_register_8_1_o[7:4]), ._0000(ml_4_16_decoder_16_outputs_west_1__0000),
    ._0001(ml_4_16_decoder_16_outputs_west_1__0001), ._0010(ml_4_16_decoder_16_outputs_west_1__0010),
    ._0011(ml_4_16_decoder_16_outputs_west_1__0011), ._0100(ml_4_16_decoder_16_outputs_west_1__0100),
    ._0101(ml_4_16_decoder_16_outputs_west_1__0101), ._0110(ml_4_16_decoder_16_outputs_west_1__0110),
    ._0111(ml_4_16_decoder_16_outputs_west_1__0111), ._1000(ml_4_16_decoder_16_outputs_west_1__1000),
    ._1001(ml_4_16_decoder_16_outputs_west_1__1001), ._1010(ml_4_16_decoder_16_outputs_west_1__1010),
    ._1011(ml_4_16_decoder_16_outputs_west_1__1011), ._1100(ml_4_16_decoder_16_outputs_west_1__1100),
    ._1101(ml_4_16_decoder_16_outputs_west_1__1101), ._1110(ml_4_16_decoder_16_outputs_west_1__1110),
    ._1111(ml_4_16_decoder_16_outputs_west_1__1111));  // open: out_2
  ML___REG_BYTE ml_reg_byte_1 (
    .op(_15), .\output (ml_reg_byte_1_output), .\input (\input ),
    .h(ml_4_16_decoder_16_outputs_west_1__0000), .v(ml_4_16_decoder_16_outputs_west_2__1111), .s(s), .e(e),
    .reset(reset));
  ML___REG_BYTE ml_reg_byte_2 (
    .op(_31), .\output (ml_reg_byte_1_output), .\input (\input ),
    .h(ml_4_16_decoder_16_outputs_west_1__0001), .v(ml_4_16_decoder_16_outputs_west_2__1111), .s(s), .e(e),
    .reset(reset));
  ML___REG_BYTE ml_reg_byte_3 (
    .op(_47), .\output (ml_reg_byte_1_output), .\input (\input ),
    .h(ml_4_16_decoder_16_outputs_west_1__0010), .v(ml_4_16_decoder_16_outputs_west_2__1111), .s(s), .e(e),
    .reset(reset));
  ML___REG_BYTE ml_reg_byte_4 (
    .op(_63), .\output (ml_reg_byte_1_output), .\input (\input ),
    .h(ml_4_16_decoder_16_outputs_west_1__0011), .v(ml_4_16_decoder_16_outputs_west_2__1111), .s(s), .e(e),
    .reset(reset));
  ML___REG_BYTE ml_reg_byte_5 (
    .op(_79), .\output (ml_reg_byte_1_output), .\input (\input ),
    .h(ml_4_16_decoder_16_outputs_west_1__0100), .v(ml_4_16_decoder_16_outputs_west_2__1111), .s(s), .e(e),
    .reset(reset));
  ML___REG_BYTE ml_reg_byte_6 (
    .op(_95), .\output (ml_reg_byte_1_output), .\input (\input ),
    .h(ml_4_16_decoder_16_outputs_west_1__0101), .v(ml_4_16_decoder_16_outputs_west_2__1111), .s(s), .e(e),
    .reset(reset));
  ML___REG_BYTE ml_reg_byte_7 (
    .op(_111), .\output (ml_reg_byte_1_output), .\input (\input ),
    .h(ml_4_16_decoder_16_outputs_west_1__0110), .v(ml_4_16_decoder_16_outputs_west_2__1111), .s(s), .e(e),
    .reset(reset));
  ML___REG_BYTE ml_reg_byte_8 (
    .op(_127), .\output (ml_reg_byte_1_output), .\input (\input ),
    .h(ml_4_16_decoder_16_outputs_west_1__0111), .v(ml_4_16_decoder_16_outputs_west_2__1111), .s(s), .e(e),
    .reset(reset));
  ML___REG_BYTE ml_reg_byte_9 (
    .op(_143), .\output (ml_reg_byte_1_output), .\input (\input ),
    .h(ml_4_16_decoder_16_outputs_west_1__1000), .v(ml_4_16_decoder_16_outputs_west_2__1111), .s(s), .e(e),
    .reset(reset));
  ML___REG_BYTE ml_reg_byte_10 (
    .op(_159), .\output (ml_reg_byte_1_output), .\input (\input ),
    .h(ml_4_16_decoder_16_outputs_west_1__1001), .v(ml_4_16_decoder_16_outputs_west_2__1111), .s(s), .e(e),
    .reset(reset));
  ML___REG_BYTE ml_reg_byte_11 (
    .op(_175), .\output (ml_reg_byte_1_output), .\input (\input ),
    .h(ml_4_16_decoder_16_outputs_west_1__1010), .v(ml_4_16_decoder_16_outputs_west_2__1111), .s(s), .e(e),
    .reset(reset));
  ML___REG_BYTE ml_reg_byte_12 (
    .op(_191), .\output (ml_reg_byte_1_output), .\input (\input ),
    .h(ml_4_16_decoder_16_outputs_west_1__1011), .v(ml_4_16_decoder_16_outputs_west_2__1111), .s(s), .e(e),
    .reset(reset));
  ML___REG_BYTE ml_reg_byte_13 (
    .op(_207), .\output (ml_reg_byte_1_output), .\input (\input ),
    .h(ml_4_16_decoder_16_outputs_west_1__1100), .v(ml_4_16_decoder_16_outputs_west_2__1111), .s(s), .e(e),
    .reset(reset));
  ML___REG_BYTE ml_reg_byte_14 (
    .op(_223), .\output (ml_reg_byte_1_output), .\input (\input ),
    .h(ml_4_16_decoder_16_outputs_west_1__1101), .v(ml_4_16_decoder_16_outputs_west_2__1111), .s(s), .e(e),
    .reset(reset));
  ML___REG_BYTE ml_reg_byte_15 (
    .op(_239), .\output (ml_reg_byte_1_output), .\input (\input ),
    .h(ml_4_16_decoder_16_outputs_west_1__1110), .v(ml_4_16_decoder_16_outputs_west_2__1111), .s(s), .e(e),
    .reset(reset));
  ML___REG_BYTE ml_reg_byte_16 (
    .op(_255), .\output (ml_reg_byte_1_output), .\input (\input ),
    .h(ml_4_16_decoder_16_outputs_west_1__1111), .v(ml_4_16_decoder_16_outputs_west_2__1111), .s(s), .e(e),
    .reset(reset));
  ML___REG_BYTE ml_reg_byte_17 (
    .op(_14), .\output (ml_reg_byte_1_output), .\input (\input ),
    .h(ml_4_16_decoder_16_outputs_west_1__0000), .v(ml_4_16_decoder_16_outputs_west_2__1110), .s(s), .e(e),
    .reset(reset));
  ML___REG_BYTE ml_reg_byte_18 (
    .op(_30), .\output (ml_reg_byte_1_output), .\input (\input ),
    .h(ml_4_16_decoder_16_outputs_west_1__0001), .v(ml_4_16_decoder_16_outputs_west_2__1110), .s(s), .e(e),
    .reset(reset));
  ML___REG_BYTE ml_reg_byte_19 (
    .op(_46), .\output (ml_reg_byte_1_output), .\input (\input ),
    .h(ml_4_16_decoder_16_outputs_west_1__0010), .v(ml_4_16_decoder_16_outputs_west_2__1110), .s(s), .e(e),
    .reset(reset));
  ML___REG_BYTE ml_reg_byte_20 (
    .op(_62), .\output (ml_reg_byte_1_output), .\input (\input ),
    .h(ml_4_16_decoder_16_outputs_west_1__0011), .v(ml_4_16_decoder_16_outputs_west_2__1110), .s(s), .e(e),
    .reset(reset));
  ML___REG_BYTE ml_reg_byte_21 (
    .op(_78), .\output (ml_reg_byte_1_output), .\input (\input ),
    .h(ml_4_16_decoder_16_outputs_west_1__0100), .v(ml_4_16_decoder_16_outputs_west_2__1110), .s(s), .e(e),
    .reset(reset));
  ML___REG_BYTE ml_reg_byte_22 (
    .op(_94), .\output (ml_reg_byte_1_output), .\input (\input ),
    .h(ml_4_16_decoder_16_outputs_west_1__0101), .v(ml_4_16_decoder_16_outputs_west_2__1110), .s(s), .e(e),
    .reset(reset));
  ML___REG_BYTE ml_reg_byte_23 (
    .op(_110), .\output (ml_reg_byte_1_output), .\input (\input ),
    .h(ml_4_16_decoder_16_outputs_west_1__0110), .v(ml_4_16_decoder_16_outputs_west_2__1110), .s(s), .e(e),
    .reset(reset));
  ML___REG_BYTE ml_reg_byte_24 (
    .op(_126), .\output (ml_reg_byte_1_output), .\input (\input ),
    .h(ml_4_16_decoder_16_outputs_west_1__0111), .v(ml_4_16_decoder_16_outputs_west_2__1110), .s(s), .e(e),
    .reset(reset));
  ML___REG_BYTE ml_reg_byte_25 (
    .op(_142), .\output (ml_reg_byte_1_output), .\input (\input ),
    .h(ml_4_16_decoder_16_outputs_west_1__1000), .v(ml_4_16_decoder_16_outputs_west_2__1110), .s(s), .e(e),
    .reset(reset));
  ML___REG_BYTE ml_reg_byte_26 (
    .op(_158), .\output (ml_reg_byte_1_output), .\input (\input ),
    .h(ml_4_16_decoder_16_outputs_west_1__1001), .v(ml_4_16_decoder_16_outputs_west_2__1110), .s(s), .e(e),
    .reset(reset));
  ML___REG_BYTE ml_reg_byte_27 (
    .op(_174), .\output (ml_reg_byte_1_output), .\input (\input ),
    .h(ml_4_16_decoder_16_outputs_west_1__1010), .v(ml_4_16_decoder_16_outputs_west_2__1110), .s(s), .e(e),
    .reset(reset));
  ML___REG_BYTE ml_reg_byte_28 (
    .op(_190), .\output (ml_reg_byte_1_output), .\input (\input ),
    .h(ml_4_16_decoder_16_outputs_west_1__1011), .v(ml_4_16_decoder_16_outputs_west_2__1110), .s(s), .e(e),
    .reset(reset));
  ML___REG_BYTE ml_reg_byte_29 (
    .op(_206), .\output (ml_reg_byte_1_output), .\input (\input ),
    .h(ml_4_16_decoder_16_outputs_west_1__1100), .v(ml_4_16_decoder_16_outputs_west_2__1110), .s(s), .e(e),
    .reset(reset));
  ML___REG_BYTE ml_reg_byte_30 (
    .op(_222), .\output (ml_reg_byte_1_output), .\input (\input ),
    .h(ml_4_16_decoder_16_outputs_west_1__1101), .v(ml_4_16_decoder_16_outputs_west_2__1110), .s(s), .e(e),
    .reset(reset));
  ML___REG_BYTE ml_reg_byte_31 (
    .op(_238), .\output (ml_reg_byte_1_output), .\input (\input ),
    .h(ml_4_16_decoder_16_outputs_west_1__1110), .v(ml_4_16_decoder_16_outputs_west_2__1110), .s(s), .e(e),
    .reset(reset));
  ML___REG_BYTE ml_reg_byte_32 (
    .op(_254), .\output (ml_reg_byte_1_output), .\input (\input ),
    .h(ml_4_16_decoder_16_outputs_west_1__1111), .v(ml_4_16_decoder_16_outputs_west_2__1110), .s(s), .e(e),
    .reset(reset));
  ML___REG_BYTE ml_reg_byte_33 (
    .op(_13), .\output (ml_reg_byte_1_output), .\input (\input ),
    .h(ml_4_16_decoder_16_outputs_west_1__0000), .v(ml_4_16_decoder_16_outputs_west_2__1101), .s(s), .e(e),
    .reset(reset));
  ML___REG_BYTE ml_reg_byte_34 (
    .op(_29), .\output (ml_reg_byte_1_output), .\input (\input ),
    .h(ml_4_16_decoder_16_outputs_west_1__0001), .v(ml_4_16_decoder_16_outputs_west_2__1101), .s(s), .e(e),
    .reset(reset));
  ML___REG_BYTE ml_reg_byte_35 (
    .op(_45), .\output (ml_reg_byte_1_output), .\input (\input ),
    .h(ml_4_16_decoder_16_outputs_west_1__0010), .v(ml_4_16_decoder_16_outputs_west_2__1101), .s(s), .e(e),
    .reset(reset));
  ML___REG_BYTE ml_reg_byte_36 (
    .op(_61), .\output (ml_reg_byte_1_output), .\input (\input ),
    .h(ml_4_16_decoder_16_outputs_west_1__0011), .v(ml_4_16_decoder_16_outputs_west_2__1101), .s(s), .e(e),
    .reset(reset));
  ML___REG_BYTE ml_reg_byte_37 (
    .op(_77), .\output (ml_reg_byte_1_output), .\input (\input ),
    .h(ml_4_16_decoder_16_outputs_west_1__0100), .v(ml_4_16_decoder_16_outputs_west_2__1101), .s(s), .e(e),
    .reset(reset));
  ML___REG_BYTE ml_reg_byte_38 (
    .op(_93), .\output (ml_reg_byte_1_output), .\input (\input ),
    .h(ml_4_16_decoder_16_outputs_west_1__0101), .v(ml_4_16_decoder_16_outputs_west_2__1101), .s(s), .e(e),
    .reset(reset));
  ML___REG_BYTE ml_reg_byte_39 (
    .op(_109), .\output (ml_reg_byte_1_output), .\input (\input ),
    .h(ml_4_16_decoder_16_outputs_west_1__0110), .v(ml_4_16_decoder_16_outputs_west_2__1101), .s(s), .e(e),
    .reset(reset));
  ML___REG_BYTE ml_reg_byte_40 (
    .op(_125), .\output (ml_reg_byte_1_output), .\input (\input ),
    .h(ml_4_16_decoder_16_outputs_west_1__0111), .v(ml_4_16_decoder_16_outputs_west_2__1101), .s(s), .e(e),
    .reset(reset));
  ML___REG_BYTE ml_reg_byte_41 (
    .op(_141), .\output (ml_reg_byte_1_output), .\input (\input ),
    .h(ml_4_16_decoder_16_outputs_west_1__1000), .v(ml_4_16_decoder_16_outputs_west_2__1101), .s(s), .e(e),
    .reset(reset));
  ML___REG_BYTE ml_reg_byte_42 (
    .op(_157), .\output (ml_reg_byte_1_output), .\input (\input ),
    .h(ml_4_16_decoder_16_outputs_west_1__1001), .v(ml_4_16_decoder_16_outputs_west_2__1101), .s(s), .e(e),
    .reset(reset));
  ML___REG_BYTE ml_reg_byte_43 (
    .op(_173), .\output (ml_reg_byte_1_output), .\input (\input ),
    .h(ml_4_16_decoder_16_outputs_west_1__1010), .v(ml_4_16_decoder_16_outputs_west_2__1101), .s(s), .e(e),
    .reset(reset));
  ML___REG_BYTE ml_reg_byte_44 (
    .op(_189), .\output (ml_reg_byte_1_output), .\input (\input ),
    .h(ml_4_16_decoder_16_outputs_west_1__1011), .v(ml_4_16_decoder_16_outputs_west_2__1101), .s(s), .e(e),
    .reset(reset));
  ML___REG_BYTE ml_reg_byte_45 (
    .op(_205), .\output (ml_reg_byte_1_output), .\input (\input ),
    .h(ml_4_16_decoder_16_outputs_west_1__1100), .v(ml_4_16_decoder_16_outputs_west_2__1101), .s(s), .e(e),
    .reset(reset));
  ML___REG_BYTE ml_reg_byte_46 (
    .op(_221), .\output (ml_reg_byte_1_output), .\input (\input ),
    .h(ml_4_16_decoder_16_outputs_west_1__1101), .v(ml_4_16_decoder_16_outputs_west_2__1101), .s(s), .e(e),
    .reset(reset));
  ML___REG_BYTE ml_reg_byte_47 (
    .op(_237), .\output (ml_reg_byte_1_output), .\input (\input ),
    .h(ml_4_16_decoder_16_outputs_west_1__1110), .v(ml_4_16_decoder_16_outputs_west_2__1101), .s(s), .e(e),
    .reset(reset));
  ML___REG_BYTE ml_reg_byte_48 (
    .op(_253), .\output (ml_reg_byte_1_output), .\input (\input ),
    .h(ml_4_16_decoder_16_outputs_west_1__1111), .v(ml_4_16_decoder_16_outputs_west_2__1101), .s(s), .e(e),
    .reset(reset));
  ML___REG_BYTE ml_reg_byte_49 (
    .op(_12), .\output (ml_reg_byte_1_output), .\input (\input ),
    .h(ml_4_16_decoder_16_outputs_west_1__0000), .v(ml_4_16_decoder_16_outputs_west_2__1100), .s(s), .e(e),
    .reset(reset));
  ML___REG_BYTE ml_reg_byte_50 (
    .op(_28), .\output (ml_reg_byte_1_output), .\input (\input ),
    .h(ml_4_16_decoder_16_outputs_west_1__0001), .v(ml_4_16_decoder_16_outputs_west_2__1100), .s(s), .e(e),
    .reset(reset));
  ML___REG_BYTE ml_reg_byte_51 (
    .op(_44), .\output (ml_reg_byte_1_output), .\input (\input ),
    .h(ml_4_16_decoder_16_outputs_west_1__0010), .v(ml_4_16_decoder_16_outputs_west_2__1100), .s(s), .e(e),
    .reset(reset));
  ML___REG_BYTE ml_reg_byte_52 (
    .op(_60), .\output (ml_reg_byte_1_output), .\input (\input ),
    .h(ml_4_16_decoder_16_outputs_west_1__0011), .v(ml_4_16_decoder_16_outputs_west_2__1100), .s(s), .e(e),
    .reset(reset));
  ML___REG_BYTE ml_reg_byte_53 (
    .op(_76), .\output (ml_reg_byte_1_output), .\input (\input ),
    .h(ml_4_16_decoder_16_outputs_west_1__0100), .v(ml_4_16_decoder_16_outputs_west_2__1100), .s(s), .e(e),
    .reset(reset));
  ML___REG_BYTE ml_reg_byte_54 (
    .op(_92), .\output (ml_reg_byte_1_output), .\input (\input ),
    .h(ml_4_16_decoder_16_outputs_west_1__0101), .v(ml_4_16_decoder_16_outputs_west_2__1100), .s(s), .e(e),
    .reset(reset));
  ML___REG_BYTE ml_reg_byte_55 (
    .op(_108), .\output (ml_reg_byte_1_output), .\input (\input ),
    .h(ml_4_16_decoder_16_outputs_west_1__0110), .v(ml_4_16_decoder_16_outputs_west_2__1100), .s(s), .e(e),
    .reset(reset));
  ML___REG_BYTE ml_reg_byte_56 (
    .op(_124), .\output (ml_reg_byte_1_output), .\input (\input ),
    .h(ml_4_16_decoder_16_outputs_west_1__0111), .v(ml_4_16_decoder_16_outputs_west_2__1100), .s(s), .e(e),
    .reset(reset));
  ML___REG_BYTE ml_reg_byte_57 (
    .op(_140), .\output (ml_reg_byte_1_output), .\input (\input ),
    .h(ml_4_16_decoder_16_outputs_west_1__1000), .v(ml_4_16_decoder_16_outputs_west_2__1100), .s(s), .e(e),
    .reset(reset));
  ML___REG_BYTE ml_reg_byte_58 (
    .op(_156), .\output (ml_reg_byte_1_output), .\input (\input ),
    .h(ml_4_16_decoder_16_outputs_west_1__1001), .v(ml_4_16_decoder_16_outputs_west_2__1100), .s(s), .e(e),
    .reset(reset));
  ML___REG_BYTE ml_reg_byte_59 (
    .op(_172), .\output (ml_reg_byte_1_output), .\input (\input ),
    .h(ml_4_16_decoder_16_outputs_west_1__1010), .v(ml_4_16_decoder_16_outputs_west_2__1100), .s(s), .e(e),
    .reset(reset));
  ML___REG_BYTE ml_reg_byte_60 (
    .op(_188), .\output (ml_reg_byte_1_output), .\input (\input ),
    .h(ml_4_16_decoder_16_outputs_west_1__1011), .v(ml_4_16_decoder_16_outputs_west_2__1100), .s(s), .e(e),
    .reset(reset));
  ML___REG_BYTE ml_reg_byte_61 (
    .op(_204), .\output (ml_reg_byte_1_output), .\input (\input ),
    .h(ml_4_16_decoder_16_outputs_west_1__1100), .v(ml_4_16_decoder_16_outputs_west_2__1100), .s(s), .e(e),
    .reset(reset));
  ML___REG_BYTE ml_reg_byte_62 (
    .op(_220), .\output (ml_reg_byte_1_output), .\input (\input ),
    .h(ml_4_16_decoder_16_outputs_west_1__1101), .v(ml_4_16_decoder_16_outputs_west_2__1100), .s(s), .e(e),
    .reset(reset));
  ML___REG_BYTE ml_reg_byte_63 (
    .op(_236), .\output (ml_reg_byte_1_output), .\input (\input ),
    .h(ml_4_16_decoder_16_outputs_west_1__1110), .v(ml_4_16_decoder_16_outputs_west_2__1100), .s(s), .e(e),
    .reset(reset));
  ML___REG_BYTE ml_reg_byte_64 (
    .op(_252), .\output (ml_reg_byte_1_output), .\input (\input ),
    .h(ml_4_16_decoder_16_outputs_west_1__1111), .v(ml_4_16_decoder_16_outputs_west_2__1100), .s(s), .e(e),
    .reset(reset));
  ML___REG_BYTE ml_reg_byte_65 (
    .op(_11), .\output (ml_reg_byte_1_output), .\input (\input ),
    .h(ml_4_16_decoder_16_outputs_west_1__0000), .v(ml_4_16_decoder_16_outputs_west_2__1011), .s(s), .e(e),
    .reset(reset));
  ML___REG_BYTE ml_reg_byte_66 (
    .op(_27), .\output (ml_reg_byte_1_output), .\input (\input ),
    .h(ml_4_16_decoder_16_outputs_west_1__0001), .v(ml_4_16_decoder_16_outputs_west_2__1011), .s(s), .e(e),
    .reset(reset));
  ML___REG_BYTE ml_reg_byte_67 (
    .op(_43), .\output (ml_reg_byte_1_output), .\input (\input ),
    .h(ml_4_16_decoder_16_outputs_west_1__0010), .v(ml_4_16_decoder_16_outputs_west_2__1011), .s(s), .e(e),
    .reset(reset));
  ML___REG_BYTE ml_reg_byte_68 (
    .op(_59), .\output (ml_reg_byte_1_output), .\input (\input ),
    .h(ml_4_16_decoder_16_outputs_west_1__0011), .v(ml_4_16_decoder_16_outputs_west_2__1011), .s(s), .e(e),
    .reset(reset));
  ML___REG_BYTE ml_reg_byte_69 (
    .op(_75), .\output (ml_reg_byte_1_output), .\input (\input ),
    .h(ml_4_16_decoder_16_outputs_west_1__0100), .v(ml_4_16_decoder_16_outputs_west_2__1011), .s(s), .e(e),
    .reset(reset));
  ML___REG_BYTE ml_reg_byte_70 (
    .op(_91), .\output (ml_reg_byte_1_output), .\input (\input ),
    .h(ml_4_16_decoder_16_outputs_west_1__0101), .v(ml_4_16_decoder_16_outputs_west_2__1011), .s(s), .e(e),
    .reset(reset));
  ML___REG_BYTE ml_reg_byte_71 (
    .op(_107), .\output (ml_reg_byte_1_output), .\input (\input ),
    .h(ml_4_16_decoder_16_outputs_west_1__0110), .v(ml_4_16_decoder_16_outputs_west_2__1011), .s(s), .e(e),
    .reset(reset));
  ML___REG_BYTE ml_reg_byte_72 (
    .op(_123), .\output (ml_reg_byte_1_output), .\input (\input ),
    .h(ml_4_16_decoder_16_outputs_west_1__0111), .v(ml_4_16_decoder_16_outputs_west_2__1011), .s(s), .e(e),
    .reset(reset));
  ML___REG_BYTE ml_reg_byte_73 (
    .op(_139), .\output (ml_reg_byte_1_output), .\input (\input ),
    .h(ml_4_16_decoder_16_outputs_west_1__1000), .v(ml_4_16_decoder_16_outputs_west_2__1011), .s(s), .e(e),
    .reset(reset));
  ML___REG_BYTE ml_reg_byte_74 (
    .op(_155), .\output (ml_reg_byte_1_output), .\input (\input ),
    .h(ml_4_16_decoder_16_outputs_west_1__1001), .v(ml_4_16_decoder_16_outputs_west_2__1011), .s(s), .e(e),
    .reset(reset));
  ML___REG_BYTE ml_reg_byte_75 (
    .op(_171), .\output (ml_reg_byte_1_output), .\input (\input ),
    .h(ml_4_16_decoder_16_outputs_west_1__1010), .v(ml_4_16_decoder_16_outputs_west_2__1011), .s(s), .e(e),
    .reset(reset));
  ML___REG_BYTE ml_reg_byte_76 (
    .op(_187), .\output (ml_reg_byte_1_output), .\input (\input ),
    .h(ml_4_16_decoder_16_outputs_west_1__1011), .v(ml_4_16_decoder_16_outputs_west_2__1011), .s(s), .e(e),
    .reset(reset));
  ML___REG_BYTE ml_reg_byte_77 (
    .op(_203), .\output (ml_reg_byte_1_output), .\input (\input ),
    .h(ml_4_16_decoder_16_outputs_west_1__1100), .v(ml_4_16_decoder_16_outputs_west_2__1011), .s(s), .e(e),
    .reset(reset));
  ML___REG_BYTE ml_reg_byte_78 (
    .op(_219), .\output (ml_reg_byte_1_output), .\input (\input ),
    .h(ml_4_16_decoder_16_outputs_west_1__1101), .v(ml_4_16_decoder_16_outputs_west_2__1011), .s(s), .e(e),
    .reset(reset));
  ML___REG_BYTE ml_reg_byte_79 (
    .op(_235), .\output (ml_reg_byte_1_output), .\input (\input ),
    .h(ml_4_16_decoder_16_outputs_west_1__1110), .v(ml_4_16_decoder_16_outputs_west_2__1011), .s(s), .e(e),
    .reset(reset));
  ML___REG_BYTE ml_reg_byte_80 (
    .op(_251), .\output (ml_reg_byte_1_output), .\input (\input ),
    .h(ml_4_16_decoder_16_outputs_west_1__1111), .v(ml_4_16_decoder_16_outputs_west_2__1011), .s(s), .e(e),
    .reset(reset));
  ML___REG_BYTE ml_reg_byte_81 (
    .op(_10), .\output (ml_reg_byte_1_output), .\input (\input ),
    .h(ml_4_16_decoder_16_outputs_west_1__0000), .v(ml_4_16_decoder_16_outputs_west_2__1010), .s(s), .e(e),
    .reset(reset));
  ML___REG_BYTE ml_reg_byte_82 (
    .op(_26), .\output (ml_reg_byte_1_output), .\input (\input ),
    .h(ml_4_16_decoder_16_outputs_west_1__0001), .v(ml_4_16_decoder_16_outputs_west_2__1010), .s(s), .e(e),
    .reset(reset));
  ML___REG_BYTE ml_reg_byte_83 (
    .op(_42), .\output (ml_reg_byte_1_output), .\input (\input ),
    .h(ml_4_16_decoder_16_outputs_west_1__0010), .v(ml_4_16_decoder_16_outputs_west_2__1010), .s(s), .e(e),
    .reset(reset));
  ML___REG_BYTE ml_reg_byte_84 (
    .op(_58), .\output (ml_reg_byte_1_output), .\input (\input ),
    .h(ml_4_16_decoder_16_outputs_west_1__0011), .v(ml_4_16_decoder_16_outputs_west_2__1010), .s(s), .e(e),
    .reset(reset));
  ML___REG_BYTE ml_reg_byte_85 (
    .op(_74), .\output (ml_reg_byte_1_output), .\input (\input ),
    .h(ml_4_16_decoder_16_outputs_west_1__0100), .v(ml_4_16_decoder_16_outputs_west_2__1010), .s(s), .e(e),
    .reset(reset));
  ML___REG_BYTE ml_reg_byte_86 (
    .op(_90), .\output (ml_reg_byte_1_output), .\input (\input ),
    .h(ml_4_16_decoder_16_outputs_west_1__0101), .v(ml_4_16_decoder_16_outputs_west_2__1010), .s(s), .e(e),
    .reset(reset));
  ML___REG_BYTE ml_reg_byte_87 (
    .op(_106), .\output (ml_reg_byte_1_output), .\input (\input ),
    .h(ml_4_16_decoder_16_outputs_west_1__0110), .v(ml_4_16_decoder_16_outputs_west_2__1010), .s(s), .e(e),
    .reset(reset));
  ML___REG_BYTE ml_reg_byte_88 (
    .op(_122), .\output (ml_reg_byte_1_output), .\input (\input ),
    .h(ml_4_16_decoder_16_outputs_west_1__0111), .v(ml_4_16_decoder_16_outputs_west_2__1010), .s(s), .e(e),
    .reset(reset));
  ML___REG_BYTE ml_reg_byte_89 (
    .op(_138), .\output (ml_reg_byte_1_output), .\input (\input ),
    .h(ml_4_16_decoder_16_outputs_west_1__1000), .v(ml_4_16_decoder_16_outputs_west_2__1010), .s(s), .e(e),
    .reset(reset));
  ML___REG_BYTE ml_reg_byte_90 (
    .op(_154), .\output (ml_reg_byte_1_output), .\input (\input ),
    .h(ml_4_16_decoder_16_outputs_west_1__1001), .v(ml_4_16_decoder_16_outputs_west_2__1010), .s(s), .e(e),
    .reset(reset));
  ML___REG_BYTE ml_reg_byte_91 (
    .op(_170), .\output (ml_reg_byte_1_output), .\input (\input ),
    .h(ml_4_16_decoder_16_outputs_west_1__1010), .v(ml_4_16_decoder_16_outputs_west_2__1010), .s(s), .e(e),
    .reset(reset));
  ML___REG_BYTE ml_reg_byte_92 (
    .op(_186), .\output (ml_reg_byte_1_output), .\input (\input ),
    .h(ml_4_16_decoder_16_outputs_west_1__1011), .v(ml_4_16_decoder_16_outputs_west_2__1010), .s(s), .e(e),
    .reset(reset));
  ML___REG_BYTE ml_reg_byte_93 (
    .op(_202), .\output (ml_reg_byte_1_output), .\input (\input ),
    .h(ml_4_16_decoder_16_outputs_west_1__1100), .v(ml_4_16_decoder_16_outputs_west_2__1010), .s(s), .e(e),
    .reset(reset));
  ML___REG_BYTE ml_reg_byte_94 (
    .op(_218), .\output (ml_reg_byte_1_output), .\input (\input ),
    .h(ml_4_16_decoder_16_outputs_west_1__1101), .v(ml_4_16_decoder_16_outputs_west_2__1010), .s(s), .e(e),
    .reset(reset));
  ML___REG_BYTE ml_reg_byte_95 (
    .op(_234), .\output (ml_reg_byte_1_output), .\input (\input ),
    .h(ml_4_16_decoder_16_outputs_west_1__1110), .v(ml_4_16_decoder_16_outputs_west_2__1010), .s(s), .e(e),
    .reset(reset));
  ML___REG_BYTE ml_reg_byte_96 (
    .op(_250), .\output (ml_reg_byte_1_output), .\input (\input ),
    .h(ml_4_16_decoder_16_outputs_west_1__1111), .v(ml_4_16_decoder_16_outputs_west_2__1010), .s(s), .e(e),
    .reset(reset));
  ML___REG_BYTE ml_reg_byte_97 (
    .op(_9), .\output (ml_reg_byte_1_output), .\input (\input ), .h(ml_4_16_decoder_16_outputs_west_1__0000),
    .v(ml_4_16_decoder_16_outputs_west_2__1001), .s(s), .e(e), .reset(reset));
  ML___REG_BYTE ml_reg_byte_98 (
    .op(_25), .\output (ml_reg_byte_1_output), .\input (\input ),
    .h(ml_4_16_decoder_16_outputs_west_1__0001), .v(ml_4_16_decoder_16_outputs_west_2__1001), .s(s), .e(e),
    .reset(reset));
  ML___REG_BYTE ml_reg_byte_99 (
    .op(_41), .\output (ml_reg_byte_1_output), .\input (\input ),
    .h(ml_4_16_decoder_16_outputs_west_1__0010), .v(ml_4_16_decoder_16_outputs_west_2__1001), .s(s), .e(e),
    .reset(reset));
  ML___REG_BYTE ml_reg_byte_100 (
    .op(_57), .\output (ml_reg_byte_1_output), .\input (\input ),
    .h(ml_4_16_decoder_16_outputs_west_1__0011), .v(ml_4_16_decoder_16_outputs_west_2__1001), .s(s), .e(e),
    .reset(reset));
  ML___REG_BYTE ml_reg_byte_101 (
    .op(_73), .\output (ml_reg_byte_1_output), .\input (\input ),
    .h(ml_4_16_decoder_16_outputs_west_1__0100), .v(ml_4_16_decoder_16_outputs_west_2__1001), .s(s), .e(e),
    .reset(reset));
  ML___REG_BYTE ml_reg_byte_102 (
    .op(_89), .\output (ml_reg_byte_1_output), .\input (\input ),
    .h(ml_4_16_decoder_16_outputs_west_1__0101), .v(ml_4_16_decoder_16_outputs_west_2__1001), .s(s), .e(e),
    .reset(reset));
  ML___REG_BYTE ml_reg_byte_103 (
    .op(_105), .\output (ml_reg_byte_1_output), .\input (\input ),
    .h(ml_4_16_decoder_16_outputs_west_1__0110), .v(ml_4_16_decoder_16_outputs_west_2__1001), .s(s), .e(e),
    .reset(reset));
  ML___REG_BYTE ml_reg_byte_104 (
    .op(_121), .\output (ml_reg_byte_1_output), .\input (\input ),
    .h(ml_4_16_decoder_16_outputs_west_1__0111), .v(ml_4_16_decoder_16_outputs_west_2__1001), .s(s), .e(e),
    .reset(reset));
  ML___REG_BYTE ml_reg_byte_105 (
    .op(_137), .\output (ml_reg_byte_1_output), .\input (\input ),
    .h(ml_4_16_decoder_16_outputs_west_1__1000), .v(ml_4_16_decoder_16_outputs_west_2__1001), .s(s), .e(e),
    .reset(reset));
  ML___REG_BYTE ml_reg_byte_106 (
    .op(_153), .\output (ml_reg_byte_1_output), .\input (\input ),
    .h(ml_4_16_decoder_16_outputs_west_1__1001), .v(ml_4_16_decoder_16_outputs_west_2__1001), .s(s), .e(e),
    .reset(reset));
  ML___REG_BYTE ml_reg_byte_107 (
    .op(_169), .\output (ml_reg_byte_1_output), .\input (\input ),
    .h(ml_4_16_decoder_16_outputs_west_1__1010), .v(ml_4_16_decoder_16_outputs_west_2__1001), .s(s), .e(e),
    .reset(reset));
  ML___REG_BYTE ml_reg_byte_108 (
    .op(_185), .\output (ml_reg_byte_1_output), .\input (\input ),
    .h(ml_4_16_decoder_16_outputs_west_1__1011), .v(ml_4_16_decoder_16_outputs_west_2__1001), .s(s), .e(e),
    .reset(reset));
  ML___REG_BYTE ml_reg_byte_109 (
    .op(_201), .\output (ml_reg_byte_1_output), .\input (\input ),
    .h(ml_4_16_decoder_16_outputs_west_1__1100), .v(ml_4_16_decoder_16_outputs_west_2__1001), .s(s), .e(e),
    .reset(reset));
  ML___REG_BYTE ml_reg_byte_110 (
    .op(_217), .\output (ml_reg_byte_1_output), .\input (\input ),
    .h(ml_4_16_decoder_16_outputs_west_1__1101), .v(ml_4_16_decoder_16_outputs_west_2__1001), .s(s), .e(e),
    .reset(reset));
  ML___REG_BYTE ml_reg_byte_111 (
    .op(_233), .\output (ml_reg_byte_1_output), .\input (\input ),
    .h(ml_4_16_decoder_16_outputs_west_1__1110), .v(ml_4_16_decoder_16_outputs_west_2__1001), .s(s), .e(e),
    .reset(reset));
  ML___REG_BYTE ml_reg_byte_112 (
    .op(_249), .\output (ml_reg_byte_1_output), .\input (\input ),
    .h(ml_4_16_decoder_16_outputs_west_1__1111), .v(ml_4_16_decoder_16_outputs_west_2__1001), .s(s), .e(e),
    .reset(reset));
  ML___REG_BYTE ml_reg_byte_113 (
    .op(_8), .\output (ml_reg_byte_1_output), .\input (\input ), .h(ml_4_16_decoder_16_outputs_west_1__0000),
    .v(ml_4_16_decoder_16_outputs_west_2__1000), .s(s), .e(e), .reset(reset));
  ML___REG_BYTE ml_reg_byte_114 (
    .op(_24), .\output (ml_reg_byte_1_output), .\input (\input ),
    .h(ml_4_16_decoder_16_outputs_west_1__0001), .v(ml_4_16_decoder_16_outputs_west_2__1000), .s(s), .e(e),
    .reset(reset));
  ML___REG_BYTE ml_reg_byte_115 (
    .op(_40), .\output (ml_reg_byte_1_output), .\input (\input ),
    .h(ml_4_16_decoder_16_outputs_west_1__0010), .v(ml_4_16_decoder_16_outputs_west_2__1000), .s(s), .e(e),
    .reset(reset));
  ML___REG_BYTE ml_reg_byte_116 (
    .op(_56), .\output (ml_reg_byte_1_output), .\input (\input ),
    .h(ml_4_16_decoder_16_outputs_west_1__0011), .v(ml_4_16_decoder_16_outputs_west_2__1000), .s(s), .e(e),
    .reset(reset));
  ML___REG_BYTE ml_reg_byte_117 (
    .op(_72), .\output (ml_reg_byte_1_output), .\input (\input ),
    .h(ml_4_16_decoder_16_outputs_west_1__0100), .v(ml_4_16_decoder_16_outputs_west_2__1000), .s(s), .e(e),
    .reset(reset));
  ML___REG_BYTE ml_reg_byte_118 (
    .op(_88), .\output (ml_reg_byte_1_output), .\input (\input ),
    .h(ml_4_16_decoder_16_outputs_west_1__0101), .v(ml_4_16_decoder_16_outputs_west_2__1000), .s(s), .e(e),
    .reset(reset));
  ML___REG_BYTE ml_reg_byte_119 (
    .op(_104), .\output (ml_reg_byte_1_output), .\input (\input ),
    .h(ml_4_16_decoder_16_outputs_west_1__0110), .v(ml_4_16_decoder_16_outputs_west_2__1000), .s(s), .e(e),
    .reset(reset));
  ML___REG_BYTE ml_reg_byte_120 (
    .op(_120), .\output (ml_reg_byte_1_output), .\input (\input ),
    .h(ml_4_16_decoder_16_outputs_west_1__0111), .v(ml_4_16_decoder_16_outputs_west_2__1000), .s(s), .e(e),
    .reset(reset));
  ML___REG_BYTE ml_reg_byte_121 (
    .op(_136), .\output (ml_reg_byte_1_output), .\input (\input ),
    .h(ml_4_16_decoder_16_outputs_west_1__1000), .v(ml_4_16_decoder_16_outputs_west_2__1000), .s(s), .e(e),
    .reset(reset));
  ML___REG_BYTE ml_reg_byte_122 (
    .op(_152), .\output (ml_reg_byte_1_output), .\input (\input ),
    .h(ml_4_16_decoder_16_outputs_west_1__1001), .v(ml_4_16_decoder_16_outputs_west_2__1000), .s(s), .e(e),
    .reset(reset));
  ML___REG_BYTE ml_reg_byte_123 (
    .op(_168), .\output (ml_reg_byte_1_output), .\input (\input ),
    .h(ml_4_16_decoder_16_outputs_west_1__1010), .v(ml_4_16_decoder_16_outputs_west_2__1000), .s(s), .e(e),
    .reset(reset));
  ML___REG_BYTE ml_reg_byte_124 (
    .op(_184), .\output (ml_reg_byte_1_output), .\input (\input ),
    .h(ml_4_16_decoder_16_outputs_west_1__1011), .v(ml_4_16_decoder_16_outputs_west_2__1000), .s(s), .e(e),
    .reset(reset));
  ML___REG_BYTE ml_reg_byte_125 (
    .op(_72_2), .\output (ml_reg_byte_1_output), .\input (\input ),
    .h(ml_4_16_decoder_16_outputs_west_1__1100), .v(ml_4_16_decoder_16_outputs_west_2__1000), .s(s), .e(e),
    .reset(reset));
  ML___REG_BYTE ml_reg_byte_126 (
    .op(_216), .\output (ml_reg_byte_1_output), .\input (\input ),
    .h(ml_4_16_decoder_16_outputs_west_1__1101), .v(ml_4_16_decoder_16_outputs_west_2__1000), .s(s), .e(e),
    .reset(reset));
  ML___REG_BYTE ml_reg_byte_127 (
    .op(_232), .\output (ml_reg_byte_1_output), .\input (\input ),
    .h(ml_4_16_decoder_16_outputs_west_1__1110), .v(ml_4_16_decoder_16_outputs_west_2__1000), .s(s), .e(e),
    .reset(reset));
  ML___REG_BYTE ml_reg_byte_128 (
    .op(_248), .\output (ml_reg_byte_1_output), .\input (\input ),
    .h(ml_4_16_decoder_16_outputs_west_1__1111), .v(ml_4_16_decoder_16_outputs_west_2__1000), .s(s), .e(e),
    .reset(reset));
  ML___4_16_DECODER_16_outputs_west ml_4_16_decoder_16_outputs_west_2 (
    .in_1(ml_register_8_1_o[3:0]), ._0000(ml_4_16_decoder_16_outputs_west_2__0000),
    ._0001(ml_4_16_decoder_16_outputs_west_2__0001), ._0010(ml_4_16_decoder_16_outputs_west_2__0010),
    ._0011(ml_4_16_decoder_16_outputs_west_2__0011), ._0100(ml_4_16_decoder_16_outputs_west_2__0100),
    ._0101(ml_4_16_decoder_16_outputs_west_2__0101), ._0110(ml_4_16_decoder_16_outputs_west_2__0110),
    ._0111(ml_4_16_decoder_16_outputs_west_2__0111), ._1000(ml_4_16_decoder_16_outputs_west_2__1000),
    ._1001(ml_4_16_decoder_16_outputs_west_2__1001), ._1010(ml_4_16_decoder_16_outputs_west_2__1010),
    ._1011(ml_4_16_decoder_16_outputs_west_2__1011), ._1100(ml_4_16_decoder_16_outputs_west_2__1100),
    ._1101(ml_4_16_decoder_16_outputs_west_2__1101), ._1110(ml_4_16_decoder_16_outputs_west_2__1110),
    ._1111(ml_4_16_decoder_16_outputs_west_2__1111));  // open: out_2
  ML___REG_BYTE ml_reg_byte_129 (
    .op(_7), .\output (ml_reg_byte_1_output), .\input (\input ), .h(ml_4_16_decoder_16_outputs_west_1__0000),
    .v(ml_4_16_decoder_16_outputs_west_2__0111), .s(s), .e(e), .reset(reset));
  ML___REG_BYTE ml_reg_byte_130 (
    .op(_23), .\output (ml_reg_byte_1_output), .\input (\input ),
    .h(ml_4_16_decoder_16_outputs_west_1__0001), .v(ml_4_16_decoder_16_outputs_west_2__0111), .s(s), .e(e),
    .reset(reset));
  ML___REG_BYTE ml_reg_byte_131 (
    .op(_39), .\output (ml_reg_byte_1_output), .\input (\input ),
    .h(ml_4_16_decoder_16_outputs_west_1__0010), .v(ml_4_16_decoder_16_outputs_west_2__0111), .s(s), .e(e),
    .reset(reset));
  ML___REG_BYTE ml_reg_byte_132 (
    .op(_55), .\output (ml_reg_byte_1_output), .\input (\input ),
    .h(ml_4_16_decoder_16_outputs_west_1__0011), .v(ml_4_16_decoder_16_outputs_west_2__0111), .s(s), .e(e),
    .reset(reset));
  ML___REG_BYTE ml_reg_byte_133 (
    .op(_71), .\output (ml_reg_byte_1_output), .\input (\input ),
    .h(ml_4_16_decoder_16_outputs_west_1__0100), .v(ml_4_16_decoder_16_outputs_west_2__0111), .s(s), .e(e),
    .reset(reset));
  ML___REG_BYTE ml_reg_byte_134 (
    .op(_87), .\output (ml_reg_byte_1_output), .\input (\input ),
    .h(ml_4_16_decoder_16_outputs_west_1__0101), .v(ml_4_16_decoder_16_outputs_west_2__0111), .s(s), .e(e),
    .reset(reset));
  ML___REG_BYTE ml_reg_byte_135 (
    .op(_103), .\output (ml_reg_byte_1_output), .\input (\input ),
    .h(ml_4_16_decoder_16_outputs_west_1__0110), .v(ml_4_16_decoder_16_outputs_west_2__0111), .s(s), .e(e),
    .reset(reset));
  ML___REG_BYTE ml_reg_byte_136 (
    .op(_119), .\output (ml_reg_byte_1_output), .\input (\input ),
    .h(ml_4_16_decoder_16_outputs_west_1__0111), .v(ml_4_16_decoder_16_outputs_west_2__0111), .s(s), .e(e),
    .reset(reset));
  ML___REG_BYTE ml_reg_byte_137 (
    .op(_135), .\output (ml_reg_byte_1_output), .\input (\input ),
    .h(ml_4_16_decoder_16_outputs_west_1__1000), .v(ml_4_16_decoder_16_outputs_west_2__0111), .s(s), .e(e),
    .reset(reset));
  ML___REG_BYTE ml_reg_byte_138 (
    .op(_151), .\output (ml_reg_byte_1_output), .\input (\input ),
    .h(ml_4_16_decoder_16_outputs_west_1__1001), .v(ml_4_16_decoder_16_outputs_west_2__0111), .s(s), .e(e),
    .reset(reset));
  ML___REG_BYTE ml_reg_byte_139 (
    .op(_167), .\output (ml_reg_byte_1_output), .\input (\input ),
    .h(ml_4_16_decoder_16_outputs_west_1__1010), .v(ml_4_16_decoder_16_outputs_west_2__0111), .s(s), .e(e),
    .reset(reset));
  ML___REG_BYTE ml_reg_byte_140 (
    .op(_183), .\output (ml_reg_byte_1_output), .\input (\input ),
    .h(ml_4_16_decoder_16_outputs_west_1__1011), .v(ml_4_16_decoder_16_outputs_west_2__0111), .s(s), .e(e),
    .reset(reset));
  ML___REG_BYTE ml_reg_byte_141 (
    .op(_199), .\output (ml_reg_byte_1_output), .\input (\input ),
    .h(ml_4_16_decoder_16_outputs_west_1__1100), .v(ml_4_16_decoder_16_outputs_west_2__0111), .s(s), .e(e),
    .reset(reset));
  ML___REG_BYTE ml_reg_byte_142 (
    .op(_215), .\output (ml_reg_byte_1_output), .\input (\input ),
    .h(ml_4_16_decoder_16_outputs_west_1__1101), .v(ml_4_16_decoder_16_outputs_west_2__0111), .s(s), .e(e),
    .reset(reset));
  ML___REG_BYTE ml_reg_byte_143 (
    .op(_231), .\output (ml_reg_byte_1_output), .\input (\input ),
    .h(ml_4_16_decoder_16_outputs_west_1__1110), .v(ml_4_16_decoder_16_outputs_west_2__0111), .s(s), .e(e),
    .reset(reset));
  ML___REG_BYTE ml_reg_byte_144 (
    .op(_247), .\output (ml_reg_byte_1_output), .\input (\input ),
    .h(ml_4_16_decoder_16_outputs_west_1__1111), .v(ml_4_16_decoder_16_outputs_west_2__0111), .s(s), .e(e),
    .reset(reset));
  ML___REG_BYTE ml_reg_byte_145 (
    .op(_6), .\output (ml_reg_byte_1_output), .\input (\input ), .h(ml_4_16_decoder_16_outputs_west_1__0000),
    .v(ml_4_16_decoder_16_outputs_west_2__0110), .s(s), .e(e), .reset(reset));
  ML___REG_BYTE ml_reg_byte_146 (
    .op(_22), .\output (ml_reg_byte_1_output), .\input (\input ),
    .h(ml_4_16_decoder_16_outputs_west_1__0001), .v(ml_4_16_decoder_16_outputs_west_2__0110), .s(s), .e(e),
    .reset(reset));
  ML___REG_BYTE ml_reg_byte_147 (
    .op(_38), .\output (ml_reg_byte_1_output), .\input (\input ),
    .h(ml_4_16_decoder_16_outputs_west_1__0010), .v(ml_4_16_decoder_16_outputs_west_2__0110), .s(s), .e(e),
    .reset(reset));
  ML___REG_BYTE ml_reg_byte_148 (
    .op(_54), .\output (ml_reg_byte_1_output), .\input (\input ),
    .h(ml_4_16_decoder_16_outputs_west_1__0011), .v(ml_4_16_decoder_16_outputs_west_2__0110), .s(s), .e(e),
    .reset(reset));
  ML___REG_BYTE ml_reg_byte_149 (
    .op(_70), .\output (ml_reg_byte_1_output), .\input (\input ),
    .h(ml_4_16_decoder_16_outputs_west_1__0100), .v(ml_4_16_decoder_16_outputs_west_2__0110), .s(s), .e(e),
    .reset(reset));
  ML___REG_BYTE ml_reg_byte_150 (
    .op(_86), .\output (ml_reg_byte_1_output), .\input (\input ),
    .h(ml_4_16_decoder_16_outputs_west_1__0101), .v(ml_4_16_decoder_16_outputs_west_2__0110), .s(s), .e(e),
    .reset(reset));
  ML___REG_BYTE ml_reg_byte_151 (
    .op(_102), .\output (ml_reg_byte_1_output), .\input (\input ),
    .h(ml_4_16_decoder_16_outputs_west_1__0110), .v(ml_4_16_decoder_16_outputs_west_2__0110), .s(s), .e(e),
    .reset(reset));
  ML___REG_BYTE ml_reg_byte_152 (
    .op(_118), .\output (ml_reg_byte_1_output), .\input (\input ),
    .h(ml_4_16_decoder_16_outputs_west_1__0111), .v(ml_4_16_decoder_16_outputs_west_2__0110), .s(s), .e(e),
    .reset(reset));
  ML___REG_BYTE ml_reg_byte_153 (
    .op(_134), .\output (ml_reg_byte_1_output), .\input (\input ),
    .h(ml_4_16_decoder_16_outputs_west_1__1000), .v(ml_4_16_decoder_16_outputs_west_2__0110), .s(s), .e(e),
    .reset(reset));
  ML___REG_BYTE ml_reg_byte_154 (
    .op(_150), .\output (ml_reg_byte_1_output), .\input (\input ),
    .h(ml_4_16_decoder_16_outputs_west_1__1001), .v(ml_4_16_decoder_16_outputs_west_2__0110), .s(s), .e(e),
    .reset(reset));
  ML___REG_BYTE ml_reg_byte_155 (
    .op(_166), .\output (ml_reg_byte_1_output), .\input (\input ),
    .h(ml_4_16_decoder_16_outputs_west_1__1010), .v(ml_4_16_decoder_16_outputs_west_2__0110), .s(s), .e(e),
    .reset(reset));
  ML___REG_BYTE ml_reg_byte_156 (
    .op(_182), .\output (ml_reg_byte_1_output), .\input (\input ),
    .h(ml_4_16_decoder_16_outputs_west_1__1011), .v(ml_4_16_decoder_16_outputs_west_2__0110), .s(s), .e(e),
    .reset(reset));
  ML___REG_BYTE ml_reg_byte_157 (
    .op(_198), .\output (ml_reg_byte_1_output), .\input (\input ),
    .h(ml_4_16_decoder_16_outputs_west_1__1100), .v(ml_4_16_decoder_16_outputs_west_2__0110), .s(s), .e(e),
    .reset(reset));
  ML___REG_BYTE ml_reg_byte_158 (
    .op(_214), .\output (ml_reg_byte_1_output), .\input (\input ),
    .h(ml_4_16_decoder_16_outputs_west_1__1101), .v(ml_4_16_decoder_16_outputs_west_2__0110), .s(s), .e(e),
    .reset(reset));
  ML___REG_BYTE ml_reg_byte_159 (
    .op(_230), .\output (ml_reg_byte_1_output), .\input (\input ),
    .h(ml_4_16_decoder_16_outputs_west_1__1110), .v(ml_4_16_decoder_16_outputs_west_2__0110), .s(s), .e(e),
    .reset(reset));
  ML___REG_BYTE ml_reg_byte_160 (
    .op(_246), .\output (ml_reg_byte_1_output), .\input (\input ),
    .h(ml_4_16_decoder_16_outputs_west_1__1111), .v(ml_4_16_decoder_16_outputs_west_2__0110), .s(s), .e(e),
    .reset(reset));
  ML___REG_BYTE ml_reg_byte_161 (
    .op(_5), .\output (ml_reg_byte_1_output), .\input (\input ), .h(ml_4_16_decoder_16_outputs_west_1__0000),
    .v(ml_4_16_decoder_16_outputs_west_2__0101), .s(s), .e(e), .reset(reset));
  ML___REG_BYTE ml_reg_byte_162 (
    .op(_21), .\output (ml_reg_byte_1_output), .\input (\input ),
    .h(ml_4_16_decoder_16_outputs_west_1__0001), .v(ml_4_16_decoder_16_outputs_west_2__0101), .s(s), .e(e),
    .reset(reset));
  ML___REG_BYTE ml_reg_byte_163 (
    .op(_37), .\output (ml_reg_byte_1_output), .\input (\input ),
    .h(ml_4_16_decoder_16_outputs_west_1__0010), .v(ml_4_16_decoder_16_outputs_west_2__0101), .s(s), .e(e),
    .reset(reset));
  ML___REG_BYTE ml_reg_byte_164 (
    .op(_53), .\output (ml_reg_byte_1_output), .\input (\input ),
    .h(ml_4_16_decoder_16_outputs_west_1__0011), .v(ml_4_16_decoder_16_outputs_west_2__0101), .s(s), .e(e),
    .reset(reset));
  ML___REG_BYTE ml_reg_byte_165 (
    .op(_69), .\output (ml_reg_byte_1_output), .\input (\input ),
    .h(ml_4_16_decoder_16_outputs_west_1__0100), .v(ml_4_16_decoder_16_outputs_west_2__0101), .s(s), .e(e),
    .reset(reset));
  ML___REG_BYTE ml_reg_byte_166 (
    .op(_85), .\output (ml_reg_byte_1_output), .\input (\input ),
    .h(ml_4_16_decoder_16_outputs_west_1__0101), .v(ml_4_16_decoder_16_outputs_west_2__0101), .s(s), .e(e),
    .reset(reset));
  ML___REG_BYTE ml_reg_byte_167 (
    .op(_101), .\output (ml_reg_byte_1_output), .\input (\input ),
    .h(ml_4_16_decoder_16_outputs_west_1__0110), .v(ml_4_16_decoder_16_outputs_west_2__0101), .s(s), .e(e),
    .reset(reset));
  ML___REG_BYTE ml_reg_byte_168 (
    .op(_117), .\output (ml_reg_byte_1_output), .\input (\input ),
    .h(ml_4_16_decoder_16_outputs_west_1__0111), .v(ml_4_16_decoder_16_outputs_west_2__0101), .s(s), .e(e),
    .reset(reset));
  ML___REG_BYTE ml_reg_byte_169 (
    .op(_133), .\output (ml_reg_byte_1_output), .\input (\input ),
    .h(ml_4_16_decoder_16_outputs_west_1__1000), .v(ml_4_16_decoder_16_outputs_west_2__0101), .s(s), .e(e),
    .reset(reset));
  ML___REG_BYTE ml_reg_byte_170 (
    .op(_149), .\output (ml_reg_byte_1_output), .\input (\input ),
    .h(ml_4_16_decoder_16_outputs_west_1__1001), .v(ml_4_16_decoder_16_outputs_west_2__0101), .s(s), .e(e),
    .reset(reset));
  ML___REG_BYTE ml_reg_byte_171 (
    .op(_165), .\output (ml_reg_byte_1_output), .\input (\input ),
    .h(ml_4_16_decoder_16_outputs_west_1__1010), .v(ml_4_16_decoder_16_outputs_west_2__0101), .s(s), .e(e),
    .reset(reset));
  ML___REG_BYTE ml_reg_byte_172 (
    .op(_181), .\output (ml_reg_byte_1_output), .\input (\input ),
    .h(ml_4_16_decoder_16_outputs_west_1__1011), .v(ml_4_16_decoder_16_outputs_west_2__0101), .s(s), .e(e),
    .reset(reset));
  ML___REG_BYTE ml_reg_byte_173 (
    .op(_197), .\output (ml_reg_byte_1_output), .\input (\input ),
    .h(ml_4_16_decoder_16_outputs_west_1__1100), .v(ml_4_16_decoder_16_outputs_west_2__0101), .s(s), .e(e),
    .reset(reset));
  ML___REG_BYTE ml_reg_byte_174 (
    .op(_213), .\output (ml_reg_byte_1_output), .\input (\input ),
    .h(ml_4_16_decoder_16_outputs_west_1__1101), .v(ml_4_16_decoder_16_outputs_west_2__0101), .s(s), .e(e),
    .reset(reset));
  ML___REG_BYTE ml_reg_byte_175 (
    .op(_229), .\output (ml_reg_byte_1_output), .\input (\input ),
    .h(ml_4_16_decoder_16_outputs_west_1__1110), .v(ml_4_16_decoder_16_outputs_west_2__0101), .s(s), .e(e),
    .reset(reset));
  ML___REG_BYTE ml_reg_byte_176 (
    .op(_245), .\output (ml_reg_byte_1_output), .\input (\input ),
    .h(ml_4_16_decoder_16_outputs_west_1__1111), .v(ml_4_16_decoder_16_outputs_west_2__0101), .s(s), .e(e),
    .reset(reset));
  ML___REG_BYTE ml_reg_byte_177 (
    .op(_4), .\output (ml_reg_byte_1_output), .\input (\input ), .h(ml_4_16_decoder_16_outputs_west_1__0000),
    .v(ml_4_16_decoder_16_outputs_west_2__0100), .s(s), .e(e), .reset(reset));
  ML___REG_BYTE ml_reg_byte_178 (
    .op(_20), .\output (ml_reg_byte_1_output), .\input (\input ),
    .h(ml_4_16_decoder_16_outputs_west_1__0001), .v(ml_4_16_decoder_16_outputs_west_2__0100), .s(s), .e(e),
    .reset(reset));
  ML___REG_BYTE ml_reg_byte_179 (
    .op(_36), .\output (ml_reg_byte_1_output), .\input (\input ),
    .h(ml_4_16_decoder_16_outputs_west_1__0010), .v(ml_4_16_decoder_16_outputs_west_2__0100), .s(s), .e(e),
    .reset(reset));
  ML___REG_BYTE ml_reg_byte_180 (
    .op(_52), .\output (ml_reg_byte_1_output), .\input (\input ),
    .h(ml_4_16_decoder_16_outputs_west_1__0011), .v(ml_4_16_decoder_16_outputs_west_2__0100), .s(s), .e(e),
    .reset(reset));
  ML___REG_BYTE ml_reg_byte_181 (
    .op(_68), .\output (ml_reg_byte_1_output), .\input (\input ),
    .h(ml_4_16_decoder_16_outputs_west_1__0100), .v(ml_4_16_decoder_16_outputs_west_2__0100), .s(s), .e(e),
    .reset(reset));
  ML___REG_BYTE ml_reg_byte_182 (
    .op(_84), .\output (ml_reg_byte_1_output), .\input (\input ),
    .h(ml_4_16_decoder_16_outputs_west_1__0101), .v(ml_4_16_decoder_16_outputs_west_2__0100), .s(s), .e(e),
    .reset(reset));
  ML___REG_BYTE ml_reg_byte_183 (
    .op(_100), .\output (ml_reg_byte_1_output), .\input (\input ),
    .h(ml_4_16_decoder_16_outputs_west_1__0110), .v(ml_4_16_decoder_16_outputs_west_2__0100), .s(s), .e(e),
    .reset(reset));
  ML___REG_BYTE ml_reg_byte_184 (
    .op(_116), .\output (ml_reg_byte_1_output), .\input (\input ),
    .h(ml_4_16_decoder_16_outputs_west_1__0111), .v(ml_4_16_decoder_16_outputs_west_2__0100), .s(s), .e(e),
    .reset(reset));
  ML___REG_BYTE ml_reg_byte_185 (
    .op(_132), .\output (ml_reg_byte_1_output), .\input (\input ),
    .h(ml_4_16_decoder_16_outputs_west_1__1000), .v(ml_4_16_decoder_16_outputs_west_2__0100), .s(s), .e(e),
    .reset(reset));
  ML___REG_BYTE ml_reg_byte_186 (
    .op(_148), .\output (ml_reg_byte_1_output), .\input (\input ),
    .h(ml_4_16_decoder_16_outputs_west_1__1001), .v(ml_4_16_decoder_16_outputs_west_2__0100), .s(s), .e(e),
    .reset(reset));
  ML___REG_BYTE ml_reg_byte_187 (
    .op(_164), .\output (ml_reg_byte_1_output), .\input (\input ),
    .h(ml_4_16_decoder_16_outputs_west_1__1010), .v(ml_4_16_decoder_16_outputs_west_2__0100), .s(s), .e(e),
    .reset(reset));
  ML___REG_BYTE ml_reg_byte_188 (
    .op(_180), .\output (ml_reg_byte_1_output), .\input (\input ),
    .h(ml_4_16_decoder_16_outputs_west_1__1011), .v(ml_4_16_decoder_16_outputs_west_2__0100), .s(s), .e(e),
    .reset(reset));
  ML___REG_BYTE ml_reg_byte_189 (
    .op(_196), .\output (ml_reg_byte_1_output), .\input (\input ),
    .h(ml_4_16_decoder_16_outputs_west_1__1100), .v(ml_4_16_decoder_16_outputs_west_2__0100), .s(s), .e(e),
    .reset(reset));
  ML___REG_BYTE ml_reg_byte_190 (
    .op(_212), .\output (ml_reg_byte_1_output), .\input (\input ),
    .h(ml_4_16_decoder_16_outputs_west_1__1101), .v(ml_4_16_decoder_16_outputs_west_2__0100), .s(s), .e(e),
    .reset(reset));
  ML___REG_BYTE ml_reg_byte_191 (
    .op(_228), .\output (ml_reg_byte_1_output), .\input (\input ),
    .h(ml_4_16_decoder_16_outputs_west_1__1110), .v(ml_4_16_decoder_16_outputs_west_2__0100), .s(s), .e(e),
    .reset(reset));
  ML___REG_BYTE ml_reg_byte_192 (
    .op(_244), .\output (ml_reg_byte_1_output), .\input (\input ),
    .h(ml_4_16_decoder_16_outputs_west_1__1111), .v(ml_4_16_decoder_16_outputs_west_2__0100), .s(s), .e(e),
    .reset(reset));
  ML___REG_BYTE ml_reg_byte_193 (
    .op(_3), .\output (ml_reg_byte_1_output), .\input (\input ), .h(ml_4_16_decoder_16_outputs_west_1__0000),
    .v(ml_4_16_decoder_16_outputs_west_2__0011), .s(s), .e(e), .reset(reset));
  ML___REG_BYTE ml_reg_byte_194 (
    .op(_19), .\output (ml_reg_byte_1_output), .\input (\input ),
    .h(ml_4_16_decoder_16_outputs_west_1__0001), .v(ml_4_16_decoder_16_outputs_west_2__0011), .s(s), .e(e),
    .reset(reset));
  ML___REG_BYTE ml_reg_byte_195 (
    .op(_35), .\output (ml_reg_byte_1_output), .\input (\input ),
    .h(ml_4_16_decoder_16_outputs_west_1__0010), .v(ml_4_16_decoder_16_outputs_west_2__0011), .s(s), .e(e),
    .reset(reset));
  ML___REG_BYTE ml_reg_byte_196 (
    .op(_51), .\output (ml_reg_byte_1_output), .\input (\input ),
    .h(ml_4_16_decoder_16_outputs_west_1__0011), .v(ml_4_16_decoder_16_outputs_west_2__0011), .s(s), .e(e),
    .reset(reset));
  ML___REG_BYTE ml_reg_byte_197 (
    .op(_67), .\output (ml_reg_byte_1_output), .\input (\input ),
    .h(ml_4_16_decoder_16_outputs_west_1__0100), .v(ml_4_16_decoder_16_outputs_west_2__0011), .s(s), .e(e),
    .reset(reset));
  ML___REG_BYTE ml_reg_byte_198 (
    .op(_83), .\output (ml_reg_byte_1_output), .\input (\input ),
    .h(ml_4_16_decoder_16_outputs_west_1__0101), .v(ml_4_16_decoder_16_outputs_west_2__0011), .s(s), .e(e),
    .reset(reset));
  ML___REG_BYTE ml_reg_byte_199 (
    .op(_99), .\output (ml_reg_byte_1_output), .\input (\input ),
    .h(ml_4_16_decoder_16_outputs_west_1__0110), .v(ml_4_16_decoder_16_outputs_west_2__0011), .s(s), .e(e),
    .reset(reset));
  ML___REG_BYTE ml_reg_byte_200 (
    .op(_115), .\output (ml_reg_byte_1_output), .\input (\input ),
    .h(ml_4_16_decoder_16_outputs_west_1__0111), .v(ml_4_16_decoder_16_outputs_west_2__0011), .s(s), .e(e),
    .reset(reset));
  ML___REG_BYTE ml_reg_byte_201 (
    .op(_131), .\output (ml_reg_byte_1_output), .\input (\input ),
    .h(ml_4_16_decoder_16_outputs_west_1__1000), .v(ml_4_16_decoder_16_outputs_west_2__0011), .s(s), .e(e),
    .reset(reset));
  ML___REG_BYTE ml_reg_byte_202 (
    .op(_147), .\output (ml_reg_byte_1_output), .\input (\input ),
    .h(ml_4_16_decoder_16_outputs_west_1__1001), .v(ml_4_16_decoder_16_outputs_west_2__0011), .s(s), .e(e),
    .reset(reset));
  ML___REG_BYTE ml_reg_byte_203 (
    .op(_163), .\output (ml_reg_byte_1_output), .\input (\input ),
    .h(ml_4_16_decoder_16_outputs_west_1__1010), .v(ml_4_16_decoder_16_outputs_west_2__0011), .s(s), .e(e),
    .reset(reset));
  ML___REG_BYTE ml_reg_byte_204 (
    .op(_179), .\output (ml_reg_byte_1_output), .\input (\input ),
    .h(ml_4_16_decoder_16_outputs_west_1__1011), .v(ml_4_16_decoder_16_outputs_west_2__0011), .s(s), .e(e),
    .reset(reset));
  ML___REG_BYTE ml_reg_byte_205 (
    .op(_195), .\output (ml_reg_byte_1_output), .\input (\input ),
    .h(ml_4_16_decoder_16_outputs_west_1__1100), .v(ml_4_16_decoder_16_outputs_west_2__0011), .s(s), .e(e),
    .reset(reset));
  ML___REG_BYTE ml_reg_byte_206 (
    .op(_211), .\output (ml_reg_byte_1_output), .\input (\input ),
    .h(ml_4_16_decoder_16_outputs_west_1__1101), .v(ml_4_16_decoder_16_outputs_west_2__0011), .s(s), .e(e),
    .reset(reset));
  ML___REG_BYTE ml_reg_byte_207 (
    .op(_227), .\output (ml_reg_byte_1_output), .\input (\input ),
    .h(ml_4_16_decoder_16_outputs_west_1__1110), .v(ml_4_16_decoder_16_outputs_west_2__0011), .s(s), .e(e),
    .reset(reset));
  ML___REG_BYTE ml_reg_byte_208 (
    .op(_243), .\output (ml_reg_byte_1_output), .\input (\input ),
    .h(ml_4_16_decoder_16_outputs_west_1__1111), .v(ml_4_16_decoder_16_outputs_west_2__0011), .s(s), .e(e),
    .reset(reset));
  ML___REG_BYTE ml_reg_byte_209 (
    .op(_2), .\output (ml_reg_byte_1_output), .\input (\input ), .h(ml_4_16_decoder_16_outputs_west_1__0000),
    .v(ml_4_16_decoder_16_outputs_west_2__0010), .s(s), .e(e), .reset(reset));
  ML___REG_BYTE ml_reg_byte_210 (
    .op(_18), .\output (ml_reg_byte_1_output), .\input (\input ),
    .h(ml_4_16_decoder_16_outputs_west_1__0001), .v(ml_4_16_decoder_16_outputs_west_2__0010), .s(s), .e(e),
    .reset(reset));
  ML___REG_BYTE ml_reg_byte_211 (
    .op(_34), .\output (ml_reg_byte_1_output), .\input (\input ),
    .h(ml_4_16_decoder_16_outputs_west_1__0010), .v(ml_4_16_decoder_16_outputs_west_2__0010), .s(s), .e(e),
    .reset(reset));
  ML___REG_BYTE ml_reg_byte_212 (
    .op(_50), .\output (ml_reg_byte_1_output), .\input (\input ),
    .h(ml_4_16_decoder_16_outputs_west_1__0011), .v(ml_4_16_decoder_16_outputs_west_2__0010), .s(s), .e(e),
    .reset(reset));
  ML___REG_BYTE ml_reg_byte_213 (
    .op(_66), .\output (ml_reg_byte_1_output), .\input (\input ),
    .h(ml_4_16_decoder_16_outputs_west_1__0100), .v(ml_4_16_decoder_16_outputs_west_2__0010), .s(s), .e(e),
    .reset(reset));
  ML___REG_BYTE ml_reg_byte_214 (
    .op(_82), .\output (ml_reg_byte_1_output), .\input (\input ),
    .h(ml_4_16_decoder_16_outputs_west_1__0101), .v(ml_4_16_decoder_16_outputs_west_2__0010), .s(s), .e(e),
    .reset(reset));
  ML___REG_BYTE ml_reg_byte_215 (
    .op(_98), .\output (ml_reg_byte_1_output), .\input (\input ),
    .h(ml_4_16_decoder_16_outputs_west_1__0110), .v(ml_4_16_decoder_16_outputs_west_2__0010), .s(s), .e(e),
    .reset(reset));
  ML___REG_BYTE ml_reg_byte_216 (
    .op(_114), .\output (ml_reg_byte_1_output), .\input (\input ),
    .h(ml_4_16_decoder_16_outputs_west_1__0111), .v(ml_4_16_decoder_16_outputs_west_2__0010), .s(s), .e(e),
    .reset(reset));
  ML___REG_BYTE ml_reg_byte_217 (
    .op(_130), .\output (ml_reg_byte_1_output), .\input (\input ),
    .h(ml_4_16_decoder_16_outputs_west_1__1000), .v(ml_4_16_decoder_16_outputs_west_2__0010), .s(s), .e(e),
    .reset(reset));
  ML___REG_BYTE ml_reg_byte_218 (
    .op(_18_2), .\output (ml_reg_byte_1_output), .\input (\input ),
    .h(ml_4_16_decoder_16_outputs_west_1__1001), .v(ml_4_16_decoder_16_outputs_west_2__0010), .s(s), .e(e),
    .reset(reset));
  ML___REG_BYTE ml_reg_byte_219 (
    .op(_162), .\output (ml_reg_byte_1_output), .\input (\input ),
    .h(ml_4_16_decoder_16_outputs_west_1__1010), .v(ml_4_16_decoder_16_outputs_west_2__0010), .s(s), .e(e),
    .reset(reset));
  ML___REG_BYTE ml_reg_byte_220 (
    .op(_178), .\output (ml_reg_byte_1_output), .\input (\input ),
    .h(ml_4_16_decoder_16_outputs_west_1__1011), .v(ml_4_16_decoder_16_outputs_west_2__0010), .s(s), .e(e),
    .reset(reset));
  ML___REG_BYTE ml_reg_byte_221 (
    .op(_194), .\output (ml_reg_byte_1_output), .\input (\input ),
    .h(ml_4_16_decoder_16_outputs_west_1__1100), .v(ml_4_16_decoder_16_outputs_west_2__0010), .s(s), .e(e),
    .reset(reset));
  ML___REG_BYTE ml_reg_byte_222 (
    .op(_210), .\output (ml_reg_byte_1_output), .\input (\input ),
    .h(ml_4_16_decoder_16_outputs_west_1__1101), .v(ml_4_16_decoder_16_outputs_west_2__0010), .s(s), .e(e),
    .reset(reset));
  ML___REG_BYTE ml_reg_byte_223 (
    .op(_226), .\output (ml_reg_byte_1_output), .\input (\input ),
    .h(ml_4_16_decoder_16_outputs_west_1__1110), .v(ml_4_16_decoder_16_outputs_west_2__0010), .s(s), .e(e),
    .reset(reset));
  ML___REG_BYTE ml_reg_byte_224 (
    .op(_242), .\output (ml_reg_byte_1_output), .\input (\input ),
    .h(ml_4_16_decoder_16_outputs_west_1__1111), .v(ml_4_16_decoder_16_outputs_west_2__0010), .s(s), .e(e),
    .reset(reset));
  ML___REG_BYTE ml_reg_byte_225 (
    .op(_1), .\output (ml_reg_byte_1_output), .\input (\input ), .h(ml_4_16_decoder_16_outputs_west_1__0000),
    .v(ml_4_16_decoder_16_outputs_west_2__0001), .s(s), .e(e), .reset(reset));
  ML___REG_BYTE ml_reg_byte_226 (
    .op(_17), .\output (ml_reg_byte_1_output), .\input (\input ),
    .h(ml_4_16_decoder_16_outputs_west_1__0001), .v(ml_4_16_decoder_16_outputs_west_2__0001), .s(s), .e(e),
    .reset(reset));
  ML___REG_BYTE ml_reg_byte_227 (
    .op(_33), .\output (ml_reg_byte_1_output), .\input (\input ),
    .h(ml_4_16_decoder_16_outputs_west_1__0010), .v(ml_4_16_decoder_16_outputs_west_2__0001), .s(s), .e(e),
    .reset(reset));
  ML___REG_BYTE ml_reg_byte_228 (
    .op(_49), .\output (ml_reg_byte_1_output), .\input (\input ),
    .h(ml_4_16_decoder_16_outputs_west_1__0011), .v(ml_4_16_decoder_16_outputs_west_2__0001), .s(s), .e(e),
    .reset(reset));
  ML___REG_BYTE ml_reg_byte_229 (
    .op(_65), .\output (ml_reg_byte_1_output), .\input (\input ),
    .h(ml_4_16_decoder_16_outputs_west_1__0100), .v(ml_4_16_decoder_16_outputs_west_2__0001), .s(s), .e(e),
    .reset(reset));
  ML___REG_BYTE ml_reg_byte_230 (
    .op(_81), .\output (ml_reg_byte_1_output), .\input (\input ),
    .h(ml_4_16_decoder_16_outputs_west_1__0101), .v(ml_4_16_decoder_16_outputs_west_2__0001), .s(s), .e(e),
    .reset(reset));
  ML___REG_BYTE ml_reg_byte_231 (
    .op(_97), .\output (ml_reg_byte_1_output), .\input (\input ),
    .h(ml_4_16_decoder_16_outputs_west_1__0110), .v(ml_4_16_decoder_16_outputs_west_2__0001), .s(s), .e(e),
    .reset(reset));
  ML___REG_BYTE ml_reg_byte_232 (
    .op(_113), .\output (ml_reg_byte_1_output), .\input (\input ),
    .h(ml_4_16_decoder_16_outputs_west_1__0111), .v(ml_4_16_decoder_16_outputs_west_2__0001), .s(s), .e(e),
    .reset(reset));
  ML___REG_BYTE ml_reg_byte_233 (
    .op(_129), .\output (ml_reg_byte_1_output), .\input (\input ),
    .h(ml_4_16_decoder_16_outputs_west_1__1000), .v(ml_4_16_decoder_16_outputs_west_2__0001), .s(s), .e(e),
    .reset(reset));
  ML___REG_BYTE ml_reg_byte_234 (
    .op(_145), .\output (ml_reg_byte_1_output), .\input (\input ),
    .h(ml_4_16_decoder_16_outputs_west_1__1001), .v(ml_4_16_decoder_16_outputs_west_2__0001), .s(s), .e(e),
    .reset(reset));
  ML___REG_BYTE ml_reg_byte_235 (
    .op(_161), .\output (ml_reg_byte_1_output), .\input (\input ),
    .h(ml_4_16_decoder_16_outputs_west_1__1010), .v(ml_4_16_decoder_16_outputs_west_2__0001), .s(s), .e(e),
    .reset(reset));
  ML___REG_BYTE ml_reg_byte_236 (
    .op(_177), .\output (ml_reg_byte_1_output), .\input (\input ),
    .h(ml_4_16_decoder_16_outputs_west_1__1011), .v(ml_4_16_decoder_16_outputs_west_2__0001), .s(s), .e(e),
    .reset(reset));
  ML___REG_BYTE ml_reg_byte_237 (
    .op(_193), .\output (ml_reg_byte_1_output), .\input (\input ),
    .h(ml_4_16_decoder_16_outputs_west_1__1100), .v(ml_4_16_decoder_16_outputs_west_2__0001), .s(s), .e(e),
    .reset(reset));
  ML___REG_BYTE ml_reg_byte_238 (
    .op(_209), .\output (ml_reg_byte_1_output), .\input (\input ),
    .h(ml_4_16_decoder_16_outputs_west_1__1101), .v(ml_4_16_decoder_16_outputs_west_2__0001), .s(s), .e(e),
    .reset(reset));
  ML___REG_BYTE ml_reg_byte_239 (
    .op(_225), .\output (ml_reg_byte_1_output), .\input (\input ),
    .h(ml_4_16_decoder_16_outputs_west_1__1110), .v(ml_4_16_decoder_16_outputs_west_2__0001), .s(s), .e(e),
    .reset(reset));
  ML___REG_BYTE ml_reg_byte_240 (
    .op(_241), .\output (ml_reg_byte_1_output), .\input (\input ),
    .h(ml_4_16_decoder_16_outputs_west_1__1111), .v(ml_4_16_decoder_16_outputs_west_2__0001), .s(s), .e(e),
    .reset(reset));
  ML___REG_BYTE ml_reg_byte_241 (
    .op(_0), .\output (ml_reg_byte_1_output), .\input (\input ), .h(ml_4_16_decoder_16_outputs_west_1__0000),
    .v(ml_4_16_decoder_16_outputs_west_2__0000), .s(s), .e(e), .reset(reset));
  ML___REG_BYTE ml_reg_byte_242 (
    .op(_16), .\output (ml_reg_byte_1_output), .\input (\input ),
    .h(ml_4_16_decoder_16_outputs_west_1__0001), .v(ml_4_16_decoder_16_outputs_west_2__0000), .s(s), .e(e),
    .reset(reset));
  ML___REG_BYTE ml_reg_byte_243 (
    .op(_32), .\output (ml_reg_byte_1_output), .\input (\input ),
    .h(ml_4_16_decoder_16_outputs_west_1__0010), .v(ml_4_16_decoder_16_outputs_west_2__0000), .s(s), .e(e),
    .reset(reset));
  ML___REG_BYTE ml_reg_byte_244 (
    .op(_48), .\output (ml_reg_byte_1_output), .\input (\input ),
    .h(ml_4_16_decoder_16_outputs_west_1__0011), .v(ml_4_16_decoder_16_outputs_west_2__0000), .s(s), .e(e),
    .reset(reset));
  ML___REG_BYTE ml_reg_byte_245 (
    .op(_64), .\output (ml_reg_byte_1_output), .\input (\input ),
    .h(ml_4_16_decoder_16_outputs_west_1__0100), .v(ml_4_16_decoder_16_outputs_west_2__0000), .s(s), .e(e),
    .reset(reset));
  ML___REG_BYTE ml_reg_byte_246 (
    .op(_80), .\output (ml_reg_byte_1_output), .\input (\input ),
    .h(ml_4_16_decoder_16_outputs_west_1__0101), .v(ml_4_16_decoder_16_outputs_west_2__0000), .s(s), .e(e),
    .reset(reset));
  ML___REG_BYTE ml_reg_byte_247 (
    .op(_96), .\output (ml_reg_byte_1_output), .\input (\input ),
    .h(ml_4_16_decoder_16_outputs_west_1__0110), .v(ml_4_16_decoder_16_outputs_west_2__0000), .s(s), .e(e),
    .reset(reset));
  ML___REG_BYTE ml_reg_byte_248 (
    .op(_112), .\output (ml_reg_byte_1_output), .\input (\input ),
    .h(ml_4_16_decoder_16_outputs_west_1__0111), .v(ml_4_16_decoder_16_outputs_west_2__0000), .s(s), .e(e),
    .reset(reset));
  ML___REG_BYTE ml_reg_byte_249 (
    .op(_128), .\output (ml_reg_byte_1_output), .\input (\input ),
    .h(ml_4_16_decoder_16_outputs_west_1__1000), .v(ml_4_16_decoder_16_outputs_west_2__0000), .s(s), .e(e),
    .reset(reset));
  ML___REG_BYTE ml_reg_byte_250 (
    .op(_144), .\output (ml_reg_byte_1_output), .\input (\input ),
    .h(ml_4_16_decoder_16_outputs_west_1__1001), .v(ml_4_16_decoder_16_outputs_west_2__0000), .s(s), .e(e),
    .reset(reset));
  ML___REG_BYTE ml_reg_byte_251 (
    .op(_160), .\output (ml_reg_byte_1_output), .\input (\input ),
    .h(ml_4_16_decoder_16_outputs_west_1__1010), .v(ml_4_16_decoder_16_outputs_west_2__0000), .s(s), .e(e),
    .reset(reset));
  ML___REG_BYTE ml_reg_byte_252 (
    .op(_176), .\output (ml_reg_byte_1_output), .\input (\input ),
    .h(ml_4_16_decoder_16_outputs_west_1__1011), .v(ml_4_16_decoder_16_outputs_west_2__0000), .s(s), .e(e),
    .reset(reset));
  ML___REG_BYTE ml_reg_byte_253 (
    .op(_192), .\output (ml_reg_byte_1_output), .\input (\input ),
    .h(ml_4_16_decoder_16_outputs_west_1__1100), .v(ml_4_16_decoder_16_outputs_west_2__0000), .s(s), .e(e),
    .reset(reset));
  ML___REG_BYTE ml_reg_byte_254 (
    .op(_208), .\output (ml_reg_byte_1_output), .\input (\input ),
    .h(ml_4_16_decoder_16_outputs_west_1__1101), .v(ml_4_16_decoder_16_outputs_west_2__0000), .s(s), .e(e),
    .reset(reset));
  ML___REG_BYTE ml_reg_byte_255 (
    .op(_224), .\output (ml_reg_byte_1_output), .\input (\input ),
    .h(ml_4_16_decoder_16_outputs_west_1__1110), .v(ml_4_16_decoder_16_outputs_west_2__0000), .s(s), .e(e),
    .reset(reset));
  ML___REG_BYTE ml_reg_byte_256 (
    .op(_240), .\output (ml_reg_byte_1_output), .\input (\input ),
    .h(ml_4_16_decoder_16_outputs_west_1__1111), .v(ml_4_16_decoder_16_outputs_west_2__0000), .s(s), .e(e),
    .reset(reset));

  // Notes on the sheet:
  //   output: pull=down
  //   input: pull=down
  //   address: pull=down
  //   ML - RAM 3 oktober 2025
  //   9-10-25: nog fixen
endmodule

module ML___RAM_V7_32_Byte (
  input  [7:0] address,
  input  sa,
  input  reset,
  input  s,
  input  e,
  input  [7:0] \input ,
  output [7:0] \output ,
  output [7:0] _15,
  output [7:0] _14,
  output [7:0] _13,
  output [7:0] _12,
  output [7:0] _11,
  output [7:0] _10,
  output [7:0] _9,
  output [7:0] _8,
  output [7:0] _7,
  output [7:0] _6,
  output [7:0] _5,
  output [7:0] _4,
  output [7:0] _3,
  output [7:0] _2,
  output [7:0] _1,
  output [7:0] _0,
  output [7:0] _31,
  output [7:0] _30,
  output [7:0] _29,
  output [7:0] _28,
  output [7:0] _27,
  output [7:0] _26,
  output [7:0] _25,
  output [7:0] _24,
  output [7:0] _23,
  output [7:0] _22,
  output [7:0] _21,
  output [7:0] _20,
  output [7:0] _19,
  output [7:0] _18,
  output [7:0] _17,
  output [7:0] _16,
  output [7:0] _47,
  output [7:0] _46,
  output [7:0] _45,
  output [7:0] _44,
  output [7:0] _43,
  output [7:0] _42,
  output [7:0] _41,
  output [7:0] _40,
  output [7:0] _39,
  output [7:0] _38,
  output [7:0] _37,
  output [7:0] _36,
  output [7:0] _35,
  output [7:0] _34,
  output [7:0] _33,
  output [7:0] _32,
  output [7:0] _63,
  output [7:0] _62,
  output [7:0] _61,
  output [7:0] _60,
  output [7:0] _59,
  output [7:0] _58,
  output [7:0] _57,
  output [7:0] _56,
  output [7:0] _55,
  output [7:0] _54,
  output [7:0] _53,
  output [7:0] _52,
  output [7:0] _51,
  output [7:0] _50,
  output [7:0] _49,
  output [7:0] _48,
  output [7:0] _79,
  output [7:0] _78,
  output [7:0] _77,
  output [7:0] _76,
  output [7:0] _75,
  output [7:0] _74,
  output [7:0] _73,
  output [7:0] _72,
  output [7:0] _71,
  output [7:0] _70,
  output [7:0] _69,
  output [7:0] _68,
  output [7:0] _67,
  output [7:0] _66,
  output [7:0] _65,
  output [7:0] _64,
  output [7:0] _95,
  output [7:0] _94,
  output [7:0] _93,
  output [7:0] _92,
  output [7:0] _91,
  output [7:0] _90,
  output [7:0] _89,
  output [7:0] _88,
  output [7:0] _87,
  output [7:0] _86,
  output [7:0] _85,
  output [7:0] _84,
  output [7:0] _83,
  output [7:0] _82,
  output [7:0] _81,
  output [7:0] _80,
  output [7:0] _111,
  output [7:0] _110,
  output [7:0] _109,
  output [7:0] _108,
  output [7:0] _107,
  output [7:0] _106,
  output [7:0] _105,
  output [7:0] _104,
  output [7:0] _103,
  output [7:0] _102,
  output [7:0] _101,
  output [7:0] _100,
  output [7:0] _99,
  output [7:0] _98,
  output [7:0] _97,
  output [7:0] _96,
  output [7:0] _127,
  output [7:0] _126,
  output [7:0] _125,
  output [7:0] _124,
  output [7:0] _123,
  output [7:0] _122,
  output [7:0] _121,
  output [7:0] _120,
  output [7:0] _119,
  output [7:0] _118,
  output [7:0] _117,
  output [7:0] _116,
  output [7:0] _115,
  output [7:0] _114,
  output [7:0] _113,
  output [7:0] _112,
  output [7:0] _143,
  output [7:0] _142,
  output [7:0] _141,
  output [7:0] _140,
  output [7:0] _139,
  output [7:0] _138,
  output [7:0] _137,
  output [7:0] _136,
  output [7:0] _135,
  output [7:0] _134,
  output [7:0] _133,
  output [7:0] _132,
  output [7:0] _131,
  output [7:0] _130,
  output [7:0] _129,
  output [7:0] _128,
  output [7:0] _159,
  output [7:0] _158,
  output [7:0] _157,
  output [7:0] _156,
  output [7:0] _155,
  output [7:0] _154,
  output [7:0] _153,
  output [7:0] _152,
  output [7:0] _151,
  output [7:0] _150,
  output [7:0] _149,
  output [7:0] _148,
  output [7:0] _147,
  output [7:0] _18_2,
  output [7:0] _145,
  output [7:0] _144,
  output [7:0] _175,
  output [7:0] _174,
  output [7:0] _173,
  output [7:0] _172,
  output [7:0] _171,
  output [7:0] _170,
  output [7:0] _169,
  output [7:0] _168,
  output [7:0] _167,
  output [7:0] _166,
  output [7:0] _165,
  output [7:0] _164,
  output [7:0] _163,
  output [7:0] _162,
  output [7:0] _161,
  output [7:0] _160,
  output [7:0] _191,
  output [7:0] _190,
  output [7:0] _189,
  output [7:0] _188,
  output [7:0] _187,
  output [7:0] _186,
  output [7:0] _185,
  output [7:0] _184,
  output [7:0] _183,
  output [7:0] _182,
  output [7:0] _181,
  output [7:0] _180,
  output [7:0] _179,
  output [7:0] _178,
  output [7:0] _177,
  output [7:0] _176,
  output [7:0] _207,
  output [7:0] _206,
  output [7:0] _205,
  output [7:0] _204,
  output [7:0] _203,
  output [7:0] _202,
  output [7:0] _201,
  output [7:0] _72_2,
  output [7:0] _199,
  output [7:0] _198,
  output [7:0] _197,
  output [7:0] _196,
  output [7:0] _195,
  output [7:0] _194,
  output [7:0] _193,
  output [7:0] _192,
  output [7:0] _223,
  output [7:0] _222,
  output [7:0] _221,
  output [7:0] _220,
  output [7:0] _219,
  output [7:0] _218,
  output [7:0] _217,
  output [7:0] _216,
  output [7:0] _215,
  output [7:0] _214,
  output [7:0] _213,
  output [7:0] _212,
  output [7:0] _211,
  output [7:0] _210,
  output [7:0] _209,
  output [7:0] _208,
  output [7:0] _239,
  output [7:0] _238,
  output [7:0] _237,
  output [7:0] _236,
  output [7:0] _235,
  output [7:0] _234,
  output [7:0] _233,
  output [7:0] _232,
  output [7:0] _231,
  output [7:0] _230,
  output [7:0] _229,
  output [7:0] _228,
  output [7:0] _227,
  output [7:0] _226,
  output [7:0] _225,
  output [7:0] _224,
  output [7:0] _255,
  output [7:0] _254,
  output [7:0] _253,
  output [7:0] _252,
  output [7:0] _251,
  output [7:0] _250,
  output [7:0] _249,
  output [7:0] _248,
  output [7:0] _247,
  output [7:0] _246,
  output [7:0] _245,
  output [7:0] _244,
  output [7:0] _243,
  output [7:0] _242,
  output [7:0] _241,
  output [7:0] _240
);

  wire ml_4_16_decoder_16_outputs_west_1__0000, ml_4_16_decoder_16_outputs_west_1__0001,
       ml_4_16_decoder_16_outputs_west_1__0010, ml_4_16_decoder_16_outputs_west_1__0011,
       ml_4_16_decoder_16_outputs_west_1__0100, ml_4_16_decoder_16_outputs_west_1__0101,
       ml_4_16_decoder_16_outputs_west_1__0110, ml_4_16_decoder_16_outputs_west_1__0111,
       ml_4_16_decoder_16_outputs_west_1__1000, ml_4_16_decoder_16_outputs_west_1__1001,
       ml_4_16_decoder_16_outputs_west_1__1010, ml_4_16_decoder_16_outputs_west_1__1011,
       ml_4_16_decoder_16_outputs_west_1__1100, ml_4_16_decoder_16_outputs_west_1__1101,
       ml_4_16_decoder_16_outputs_west_1__1110, ml_4_16_decoder_16_outputs_west_1__1111,
       ml_4_16_decoder_16_outputs_west_2__0000, ml_4_16_decoder_16_outputs_west_2__0001,
       ml_4_16_decoder_16_outputs_west_2__0010, ml_4_16_decoder_16_outputs_west_2__0011,
       ml_4_16_decoder_16_outputs_west_2__0100, ml_4_16_decoder_16_outputs_west_2__0101,
       ml_4_16_decoder_16_outputs_west_2__0110, ml_4_16_decoder_16_outputs_west_2__0111,
       ml_4_16_decoder_16_outputs_west_2__1000, ml_4_16_decoder_16_outputs_west_2__1001,
       ml_4_16_decoder_16_outputs_west_2__1010, ml_4_16_decoder_16_outputs_west_2__1011,
       ml_4_16_decoder_16_outputs_west_2__1100, ml_4_16_decoder_16_outputs_west_2__1101,
       ml_4_16_decoder_16_outputs_west_2__1110, ml_4_16_decoder_16_outputs_west_2__1111;
  wire [7:0] ml_memory_8_1_o, ml_reg_byte_1_output;

  ML___Memory_8 ml_memory_8_1 (.i(address), .o(ml_memory_8_1_o), .s(sa));
  ML___4_16_DECODER_16_outputs_west ml_4_16_decoder_16_outputs_west_1 (
    .in_1(ml_memory_8_1_o[7:4]), ._0000(ml_4_16_decoder_16_outputs_west_1__0000),
    ._0001(ml_4_16_decoder_16_outputs_west_1__0001), ._0010(ml_4_16_decoder_16_outputs_west_1__0010),
    ._0011(ml_4_16_decoder_16_outputs_west_1__0011), ._0100(ml_4_16_decoder_16_outputs_west_1__0100),
    ._0101(ml_4_16_decoder_16_outputs_west_1__0101), ._0110(ml_4_16_decoder_16_outputs_west_1__0110),
    ._0111(ml_4_16_decoder_16_outputs_west_1__0111), ._1000(ml_4_16_decoder_16_outputs_west_1__1000),
    ._1001(ml_4_16_decoder_16_outputs_west_1__1001), ._1010(ml_4_16_decoder_16_outputs_west_1__1010),
    ._1011(ml_4_16_decoder_16_outputs_west_1__1011), ._1100(ml_4_16_decoder_16_outputs_west_1__1100),
    ._1101(ml_4_16_decoder_16_outputs_west_1__1101), ._1110(ml_4_16_decoder_16_outputs_west_1__1110),
    ._1111(ml_4_16_decoder_16_outputs_west_1__1111));  // open: out_2
  assign \output  = e ? ml_reg_byte_1_output : 8'bz;  // Controlled_Buffer controlled_buffer_1
  ML___REG_BYTE ml_reg_byte_1 (
    .op(_15), .\output (ml_reg_byte_1_output), .\input (\input ),
    .h(ml_4_16_decoder_16_outputs_west_1__0000), .v(ml_4_16_decoder_16_outputs_west_2__1111), .s(s), .e(e),
    .reset(reset));
  ML___REG_BYTE ml_reg_byte_2 (
    .op(_31), .\output (ml_reg_byte_1_output), .\input (\input ),
    .h(ml_4_16_decoder_16_outputs_west_1__0001), .v(ml_4_16_decoder_16_outputs_west_2__1111), .s(s), .e(e),
    .reset(reset));
  ML___REG_BYTE ml_reg_byte_3 (
    .op(_14), .\output (ml_reg_byte_1_output), .\input (\input ),
    .h(ml_4_16_decoder_16_outputs_west_1__0000), .v(ml_4_16_decoder_16_outputs_west_2__1110), .s(s), .e(e),
    .reset(reset));
  ML___REG_BYTE ml_reg_byte_4 (
    .op(_30), .\output (ml_reg_byte_1_output), .\input (\input ),
    .h(ml_4_16_decoder_16_outputs_west_1__0001), .v(ml_4_16_decoder_16_outputs_west_2__1110), .s(s), .e(e),
    .reset(reset));
  ML___REG_BYTE ml_reg_byte_5 (
    .op(_13), .\output (ml_reg_byte_1_output), .\input (\input ),
    .h(ml_4_16_decoder_16_outputs_west_1__0000), .v(ml_4_16_decoder_16_outputs_west_2__1101), .s(s), .e(e),
    .reset(reset));
  ML___REG_BYTE ml_reg_byte_6 (
    .op(_29), .\output (ml_reg_byte_1_output), .\input (\input ),
    .h(ml_4_16_decoder_16_outputs_west_1__0001), .v(ml_4_16_decoder_16_outputs_west_2__1101), .s(s), .e(e),
    .reset(reset));
  ML___REG_BYTE ml_reg_byte_7 (
    .op(_12), .\output (ml_reg_byte_1_output), .\input (\input ),
    .h(ml_4_16_decoder_16_outputs_west_1__0000), .v(ml_4_16_decoder_16_outputs_west_2__1100), .s(s), .e(e),
    .reset(reset));
  ML___REG_BYTE ml_reg_byte_8 (
    .op(_28), .\output (ml_reg_byte_1_output), .\input (\input ),
    .h(ml_4_16_decoder_16_outputs_west_1__0001), .v(ml_4_16_decoder_16_outputs_west_2__1100), .s(s), .e(e),
    .reset(reset));
  ML___REG_BYTE ml_reg_byte_9 (
    .op(_11), .\output (ml_reg_byte_1_output), .\input (\input ),
    .h(ml_4_16_decoder_16_outputs_west_1__0000), .v(ml_4_16_decoder_16_outputs_west_2__1011), .s(s), .e(e),
    .reset(reset));
  ML___REG_BYTE ml_reg_byte_10 (
    .op(_27), .\output (ml_reg_byte_1_output), .\input (\input ),
    .h(ml_4_16_decoder_16_outputs_west_1__0001), .v(ml_4_16_decoder_16_outputs_west_2__1011), .s(s), .e(e),
    .reset(reset));
  ML___REG_BYTE ml_reg_byte_11 (
    .op(_10), .\output (ml_reg_byte_1_output), .\input (\input ),
    .h(ml_4_16_decoder_16_outputs_west_1__0000), .v(ml_4_16_decoder_16_outputs_west_2__1010), .s(s), .e(e),
    .reset(reset));
  ML___REG_BYTE ml_reg_byte_12 (
    .op(_26), .\output (ml_reg_byte_1_output), .\input (\input ),
    .h(ml_4_16_decoder_16_outputs_west_1__0001), .v(ml_4_16_decoder_16_outputs_west_2__1010), .s(s), .e(e),
    .reset(reset));
  ML___REG_BYTE ml_reg_byte_13 (
    .op(_9), .\output (ml_reg_byte_1_output), .\input (\input ), .h(ml_4_16_decoder_16_outputs_west_1__0000),
    .v(ml_4_16_decoder_16_outputs_west_2__1001), .s(s), .e(e), .reset(reset));
  ML___REG_BYTE ml_reg_byte_14 (
    .op(_25), .\output (ml_reg_byte_1_output), .\input (\input ),
    .h(ml_4_16_decoder_16_outputs_west_1__0001), .v(ml_4_16_decoder_16_outputs_west_2__1001), .s(s), .e(e),
    .reset(reset));
  ML___REG_BYTE ml_reg_byte_15 (
    .op(_8), .\output (ml_reg_byte_1_output), .\input (\input ), .h(ml_4_16_decoder_16_outputs_west_1__0000),
    .v(ml_4_16_decoder_16_outputs_west_2__1000), .s(s), .e(e), .reset(reset));
  ML___REG_BYTE ml_reg_byte_16 (
    .op(_24), .\output (ml_reg_byte_1_output), .\input (\input ),
    .h(ml_4_16_decoder_16_outputs_west_1__0001), .v(ml_4_16_decoder_16_outputs_west_2__1000), .s(s), .e(e),
    .reset(reset));
  ML___4_16_DECODER_16_outputs_west ml_4_16_decoder_16_outputs_west_2 (
    .in_1(ml_memory_8_1_o[3:0]), ._0000(ml_4_16_decoder_16_outputs_west_2__0000),
    ._0001(ml_4_16_decoder_16_outputs_west_2__0001), ._0010(ml_4_16_decoder_16_outputs_west_2__0010),
    ._0011(ml_4_16_decoder_16_outputs_west_2__0011), ._0100(ml_4_16_decoder_16_outputs_west_2__0100),
    ._0101(ml_4_16_decoder_16_outputs_west_2__0101), ._0110(ml_4_16_decoder_16_outputs_west_2__0110),
    ._0111(ml_4_16_decoder_16_outputs_west_2__0111), ._1000(ml_4_16_decoder_16_outputs_west_2__1000),
    ._1001(ml_4_16_decoder_16_outputs_west_2__1001), ._1010(ml_4_16_decoder_16_outputs_west_2__1010),
    ._1011(ml_4_16_decoder_16_outputs_west_2__1011), ._1100(ml_4_16_decoder_16_outputs_west_2__1100),
    ._1101(ml_4_16_decoder_16_outputs_west_2__1101), ._1110(ml_4_16_decoder_16_outputs_west_2__1110),
    ._1111(ml_4_16_decoder_16_outputs_west_2__1111));  // open: out_2
  ML___REG_BYTE ml_reg_byte_17 (
    .op(_7), .\output (ml_reg_byte_1_output), .\input (\input ), .h(ml_4_16_decoder_16_outputs_west_1__0000),
    .v(ml_4_16_decoder_16_outputs_west_2__0111), .s(s), .e(e), .reset(reset));
  ML___REG_BYTE ml_reg_byte_18 (
    .op(_23), .\output (ml_reg_byte_1_output), .\input (\input ),
    .h(ml_4_16_decoder_16_outputs_west_1__0001), .v(ml_4_16_decoder_16_outputs_west_2__0111), .s(s), .e(e),
    .reset(reset));
  ML___REG_BYTE ml_reg_byte_19 (
    .op(_6), .\output (ml_reg_byte_1_output), .\input (\input ), .h(ml_4_16_decoder_16_outputs_west_1__0000),
    .v(ml_4_16_decoder_16_outputs_west_2__0110), .s(s), .e(e), .reset(reset));
  ML___REG_BYTE ml_reg_byte_20 (
    .op(_22), .\output (ml_reg_byte_1_output), .\input (\input ),
    .h(ml_4_16_decoder_16_outputs_west_1__0001), .v(ml_4_16_decoder_16_outputs_west_2__0110), .s(s), .e(e),
    .reset(reset));
  ML___REG_BYTE ml_reg_byte_21 (
    .op(_5), .\output (ml_reg_byte_1_output), .\input (\input ), .h(ml_4_16_decoder_16_outputs_west_1__0000),
    .v(ml_4_16_decoder_16_outputs_west_2__0101), .s(s), .e(e), .reset(reset));
  ML___REG_BYTE ml_reg_byte_22 (
    .op(_21), .\output (ml_reg_byte_1_output), .\input (\input ),
    .h(ml_4_16_decoder_16_outputs_west_1__0001), .v(ml_4_16_decoder_16_outputs_west_2__0101), .s(s), .e(e),
    .reset(reset));
  ML___REG_BYTE ml_reg_byte_23 (
    .op(_4), .\output (ml_reg_byte_1_output), .\input (\input ), .h(ml_4_16_decoder_16_outputs_west_1__0000),
    .v(ml_4_16_decoder_16_outputs_west_2__0100), .s(s), .e(e), .reset(reset));
  ML___REG_BYTE ml_reg_byte_24 (
    .op(_20), .\output (ml_reg_byte_1_output), .\input (\input ),
    .h(ml_4_16_decoder_16_outputs_west_1__0001), .v(ml_4_16_decoder_16_outputs_west_2__0100), .s(s), .e(e),
    .reset(reset));
  ML___REG_BYTE ml_reg_byte_25 (
    .op(_3), .\output (ml_reg_byte_1_output), .\input (\input ), .h(ml_4_16_decoder_16_outputs_west_1__0000),
    .v(ml_4_16_decoder_16_outputs_west_2__0011), .s(s), .e(e), .reset(reset));
  ML___REG_BYTE ml_reg_byte_26 (
    .op(_19), .\output (ml_reg_byte_1_output), .\input (\input ),
    .h(ml_4_16_decoder_16_outputs_west_1__0001), .v(ml_4_16_decoder_16_outputs_west_2__0011), .s(s), .e(e),
    .reset(reset));
  ML___REG_BYTE ml_reg_byte_27 (
    .op(_2), .\output (ml_reg_byte_1_output), .\input (\input ), .h(ml_4_16_decoder_16_outputs_west_1__0000),
    .v(ml_4_16_decoder_16_outputs_west_2__0010), .s(s), .e(e), .reset(reset));
  ML___REG_BYTE ml_reg_byte_28 (
    .op(_18), .\output (ml_reg_byte_1_output), .\input (\input ),
    .h(ml_4_16_decoder_16_outputs_west_1__0001), .v(ml_4_16_decoder_16_outputs_west_2__0010), .s(s), .e(e),
    .reset(reset));
  ML___REG_BYTE ml_reg_byte_29 (
    .op(_1), .\output (ml_reg_byte_1_output), .\input (\input ), .h(ml_4_16_decoder_16_outputs_west_1__0000),
    .v(ml_4_16_decoder_16_outputs_west_2__0001), .s(s), .e(e), .reset(reset));
  ML___REG_BYTE ml_reg_byte_30 (
    .op(_17), .\output (ml_reg_byte_1_output), .\input (\input ),
    .h(ml_4_16_decoder_16_outputs_west_1__0001), .v(ml_4_16_decoder_16_outputs_west_2__0001), .s(s), .e(e),
    .reset(reset));
  ML___REG_BYTE ml_reg_byte_31 (
    .op(_0), .\output (ml_reg_byte_1_output), .\input (\input ), .h(ml_4_16_decoder_16_outputs_west_1__0000),
    .v(ml_4_16_decoder_16_outputs_west_2__0000), .s(s), .e(e), .reset(reset));
  ML___REG_BYTE ml_reg_byte_32 (
    .op(_16), .\output (ml_reg_byte_1_output), .\input (\input ),
    .h(ml_4_16_decoder_16_outputs_west_1__0001), .v(ml_4_16_decoder_16_outputs_west_2__0000), .s(s), .e(e),
    .reset(reset));

  // Notes on the sheet:
  //   sa: pull=down
  //   output: pull=down
  //   address: pull=down
  //   input: pull=down
  //   18-11-25: CPU Register eruit gehaald. Daarvoor in de plaats gewone CPU MEM 8
  //   ML - RAM 6 oktober 2025: 256 byte werkt te traag dus gebruik deze c.f. les
endmodule

module ML___SHIFT_Left (
  input  shift_in,
  input  [7:0] in_2,
  output [7:0] \output ,
  output shift_out
);

  wire [6:0] ml_register_8_1_o;

  ML___Register_8 ml_register_8_1 (.i(in_2), .o({shift_out, ml_register_8_1_o}), .S(1'b1), .e(1'b1));  // open: out_4
  ML___Register_8 ml_register_8_2 (.i({ml_register_8_1_o, shift_in}), .o(\output ), .S(1'b1), .e(1'b1));  // open: out_4

  // Notes on the sheet:
  //   ML 5-10-2025: Shift Left
  //   in output bit naar links geschoven
endmodule

module ML___SHIFT_Right (
  input  [7:0] in_1,
  input  shift_in_MSB,
  output shift_out_LSB,
  output [7:0] \output 
);

  wire [7:1] ml_register_8_1_o;

  ML___Register_8 ml_register_8_1 (
    .i(in_1), .o({ml_register_8_1_o, shift_out_LSB}), .S(1'b1), .e(1'b1));  // open: out_4
  ML___Register_8 ml_register_8_2 (
    .i({shift_in_MSB, ml_register_8_1_o}), .o(\output ), .S(1'b1), .e(1'b1));  // open: out_4

  // Notes on the sheet:
  //   ML 5-10-2025: Shift Right
  //   LSB: least significant BIT
  //   MSB: Most Significant Bit
  //   in output bit naar links geschoven
endmodule

module ML___NOT_Function_8_Bit (
  input  [7:0] in_1,
  output [7:0] out_2
);

  not not_1 (out_2[0], in_1[0]);
  not not_2 (out_2[1], in_1[1]);
  not not_3 (out_2[2], in_1[2]);
  not not_4 (out_2[3], in_1[3]);
  not not_5 (out_2[4], in_1[4]);
  not not_6 (out_2[5], in_1[5]);
  not not_7 (out_2[6], in_1[6]);
  not not_8 (out_2[7], in_1[7]);

  // Notes on the sheet:
  //   ML 5-10-2025: NOT function
endmodule

module ML___AND_Function_8_Bit (
  input  [7:0] Input_A,
  input  [7:0] Input_B,
  output [7:0] Output
);

  and and_1 (Output[0], Input_A[0], Input_B[0]);
  and and_2 (Output[1], Input_A[1], Input_B[1]);
  and and_3 (Output[2], Input_A[2], Input_B[2]);
  and and_4 (Output[3], Input_A[3], Input_B[3]);
  and and_5 (Output[4], Input_A[4], Input_B[4]);
  and and_6 (Output[5], Input_A[5], Input_B[5]);
  and and_7 (Output[6], Input_A[6], Input_B[6]);
  and and_8 (Output[7], Input_A[7], Input_B[7]);

  // Notes on the sheet:
  //   ML 5-10-25: AND-Function
endmodule

module ML___OR_Function_8_Bit (
  input  [7:0] Input_A,
  input  [7:0] Input_B,
  output [7:0] Output
);

  or or_1 (Output[0], Input_A[0], Input_B[0]);
  or or_2 (Output[1], Input_A[1], Input_B[1]);
  or or_3 (Output[2], Input_A[2], Input_B[2]);
  or or_4 (Output[3], Input_A[3], Input_B[3]);
  or or_5 (Output[4], Input_A[4], Input_B[4]);
  or or_6 (Output[5], Input_A[5], Input_B[5]);
  or or_7 (Output[6], Input_A[6], Input_B[6]);
  or or_8 (Output[7], Input_A[7], Input_B[7]);

  // Notes on the sheet:
  //   ML 5-10-25: OR-Function
endmodule

module ML___XOR_LE_1 (
  input  Above_Equal,
  input  a_Larger,
  input  Input_a,
  input  Input_b,
  output c,
  output equal,
  output a_large
);

  wire and_2_out, not_1_out;

  xor XOR (c, Input_a, Input_b);
  not not_1 (not_1_out, c);
  and and_1 (equal, not_1_out, Above_Equal);
  and and_2 (and_2_out, Above_Equal, Input_a, c);
  or or_1 (a_large, and_2_out, a_Larger);

  // Notes on the sheet:
  //   ML 5-10-25: XOR_LE_1
  //   LSB
  //   Higher Significant Bits
endmodule

module ML___XOR_LE_8 (
  input  [7:0] a,
  input  [7:0] b,
  output [7:0] out_3,
  output larger,
  output equal
);

  wire ml_xor_le_1_1_a_large, ml_xor_le_1_1_equal, ml_xor_le_1_2_a_large, ml_xor_le_1_2_equal,
       ml_xor_le_1_3_a_large, ml_xor_le_1_3_equal, ml_xor_le_1_4_a_large, ml_xor_le_1_4_equal,
       ml_xor_le_1_5_a_large, ml_xor_le_1_5_equal, ml_xor_le_1_6_a_large, ml_xor_le_1_6_equal,
       ml_xor_le_1_7_a_large, ml_xor_le_1_7_equal;

  ML___XOR_LE_1 ml_xor_le_1_1 (
    .Input_a(a[0]), .Input_b(b[0]), .c(out_3[0]), .Above_Equal(1'b1), .a_Larger(1'b0),
    .equal(ml_xor_le_1_1_equal), .a_large(ml_xor_le_1_1_a_large));
  ML___XOR_LE_1 ml_xor_le_1_2 (
    .Input_a(a[1]), .Input_b(b[1]), .c(out_3[1]), .Above_Equal(ml_xor_le_1_1_equal),
    .a_Larger(ml_xor_le_1_1_a_large), .equal(ml_xor_le_1_2_equal), .a_large(ml_xor_le_1_2_a_large));
  ML___XOR_LE_1 ml_xor_le_1_3 (
    .Input_a(a[2]), .Input_b(b[2]), .c(out_3[2]), .Above_Equal(ml_xor_le_1_2_equal),
    .a_Larger(ml_xor_le_1_2_a_large), .equal(ml_xor_le_1_3_equal), .a_large(ml_xor_le_1_3_a_large));
  ML___XOR_LE_1 ml_xor_le_1_4 (
    .Input_a(a[3]), .Input_b(b[3]), .c(out_3[3]), .Above_Equal(ml_xor_le_1_3_equal),
    .a_Larger(ml_xor_le_1_3_a_large), .equal(ml_xor_le_1_4_equal), .a_large(ml_xor_le_1_4_a_large));
  ML___XOR_LE_1 ml_xor_le_1_5 (
    .Input_a(a[4]), .Input_b(b[4]), .c(out_3[4]), .Above_Equal(ml_xor_le_1_4_equal),
    .a_Larger(ml_xor_le_1_4_a_large), .equal(ml_xor_le_1_5_equal), .a_large(ml_xor_le_1_5_a_large));
  ML___XOR_LE_1 ml_xor_le_1_6 (
    .Input_a(a[5]), .Input_b(b[5]), .c(out_3[5]), .Above_Equal(ml_xor_le_1_5_equal),
    .a_Larger(ml_xor_le_1_5_a_large), .equal(ml_xor_le_1_6_equal), .a_large(ml_xor_le_1_6_a_large));
  ML___XOR_LE_1 ml_xor_le_1_7 (
    .Input_a(a[6]), .Input_b(b[6]), .c(out_3[6]), .Above_Equal(ml_xor_le_1_6_equal),
    .a_Larger(ml_xor_le_1_6_a_large), .equal(ml_xor_le_1_7_equal), .a_large(ml_xor_le_1_7_a_large));
  ML___XOR_LE_1 ml_xor_le_1_8 (
    .Input_a(a[7]), .Input_b(b[7]), .c(out_3[7]), .Above_Equal(ml_xor_le_1_7_equal),
    .a_Larger(ml_xor_le_1_7_a_large), .equal(equal), .a_large(larger));

  // Notes on the sheet:
  //   ML 5-10-2025: XOR_LE8
  //   If a is higher than b, this goes high
endmodule

module ML___ZERO_Function (
  input  [7:0] i,
  output out_2
);

  wire or_1_out;

  or or_1 (or_1_out, i[0], i[1], i[2], i[3], i[4], i[5], i[6], i[7]);
  not not_1 (out_2, or_1_out);

  // Notes on the sheet:
  //   ML 5-10-25: Inputs equal to zero
endmodule

module ML___ALU__Arithmetic___Logical_Unit (
  input  [7:0] a,
  input  [7:0] b,
  input  carry_in,
  input  c_Msb,
  input  b_2,
  input  a_Lsb,
  output a_larger,
  output equal,
  output Zero,
  output [7:0] \output ,
  output carry_out
);

  wire and_1_out, and_2_out, and_3_out, ml_adder_8_1_carry_out, ml_shift_left_1_shift_out,
       ml_shift_right_1_shift_out_lsb;
  wire [7:0] ml_3_8_decoder_1_output_east_1_out_4, ml_adder_8_1_out_5, ml_and_function_8_bit_1_output,
       ml_not_function_8_bit_1_out_2, ml_or_function_8_bit_1_output, ml_shift_left_1_output,
       ml_shift_right_1_output, ml_xor_le_8_1_out_3;

  ML___3_8_DECODER_1_output_east ml_3_8_decoder_1_output_east_1 (
    .C__Msb(a_Lsb), .B(b_2), .A__Lsb(c_Msb), .out_4(ml_3_8_decoder_1_output_east_1_out_4));
  ML___XOR_LE_8 ml_xor_le_8_1 (.a(a), .b(b), .out_3(ml_xor_le_8_1_out_3), .larger(a_larger), .equal(equal));
  ML___OR_Function_8_Bit ml_or_function_8_bit_1 (.Input_A(a), .Input_B(b), .Output(ml_or_function_8_bit_1_output));
  ML___AND_Function_8_Bit ml_and_function_8_bit_1 (.Input_A(a), .Input_B(b), .Output(ml_and_function_8_bit_1_output));
  ML___NOT_Function_8_Bit ml_not_function_8_bit_1 (.in_1(a), .out_2(ml_not_function_8_bit_1_out_2));
  ML___SHIFT_Left ml_shift_left_1 (
    .in_2(a), .\output (ml_shift_left_1_output), .shift_in(carry_in), .shift_out(ml_shift_left_1_shift_out));
  ML___SHIFT_Right ml_shift_right_1 (
    .in_1(a), .\output (ml_shift_right_1_output), .shift_out_LSB(ml_shift_right_1_shift_out_lsb),
    .shift_in_MSB(carry_in));
  ML___Adder_8 ml_adder_8_1 (
    .in_1(a), .in_3(b), .out_5(ml_adder_8_1_out_5), .Carry_Out(ml_adder_8_1_carry_out), .Carry_In(carry_in));
  ML___ENABLER_VARIANT_2 ml_enabler_variant_2_1 (
    .i(ml_xor_le_8_1_out_3), .o(\output ), .e(ml_3_8_decoder_1_output_east_1_out_4[6]));
  ML___ENABLER_VARIANT_2 ml_enabler_variant_2_2 (
    .i(ml_or_function_8_bit_1_output), .o(\output ), .e(ml_3_8_decoder_1_output_east_1_out_4[5]));
  ML___ENABLER_VARIANT_2 ml_enabler_variant_2_3 (
    .i(ml_and_function_8_bit_1_output), .o(\output ), .e(ml_3_8_decoder_1_output_east_1_out_4[4]));
  ML___ENABLER_VARIANT_2 ml_enabler_variant_2_4 (
    .i(ml_not_function_8_bit_1_out_2), .o(\output ), .e(ml_3_8_decoder_1_output_east_1_out_4[3]));
  ML___ENABLER_VARIANT_2 ml_enabler_variant_2_5 (
    .i(ml_shift_left_1_output), .o(\output ), .e(ml_3_8_decoder_1_output_east_1_out_4[2]));
  ML___ENABLER_VARIANT_2 ml_enabler_variant_2_6 (
    .i(ml_shift_right_1_output), .o(\output ), .e(ml_3_8_decoder_1_output_east_1_out_4[1]));
  ML___ENABLER_VARIANT_2 ml_enabler_variant_2_7 (
    .i(ml_adder_8_1_out_5), .o(\output ), .e(ml_3_8_decoder_1_output_east_1_out_4[0]));
  and and_1 (and_1_out, ml_shift_left_1_shift_out, ml_3_8_decoder_1_output_east_1_out_4[2]);
  and and_2 (and_2_out, ml_shift_right_1_shift_out_lsb, ml_3_8_decoder_1_output_east_1_out_4[1]);
  and and_3 (and_3_out, ml_adder_8_1_carry_out, ml_3_8_decoder_1_output_east_1_out_4[0]);
  assign carry_out = ml_3_8_decoder_1_output_east_1_out_4[2] ? and_1_out : 1'bz;  // Controlled_Buffer controlled_buffer_1
  assign carry_out = ml_3_8_decoder_1_output_east_1_out_4[1] ? and_2_out : 1'bz;  // Controlled_Buffer controlled_buffer_2
  assign carry_out = ml_3_8_decoder_1_output_east_1_out_4[0] ? and_3_out : 1'bz;  // Controlled_Buffer controlled_buffer_3
  ML___ZERO_Function ml_zero_function_1 (.i(\output ), .out_2(Zero));

  // Notes on the sheet:
  //   b_2: pull=down
  //   carry_out: pull=down
  //   equal: pull=down
  //   a: pull=down
  //   c_Msb: pull=down
  //   b: pull=down
  //   a_Lsb: pull=down
  //   carry_in: pull=down
  //   a_larger: pull=down
  //   output: pull=down
  //   Zero: pull=down
  //   ML 6-10-2025: Zie uitleg college
  //   Met a, b, c kiezen we de functie die we uit de ALU willen gebruiken
endmodule

module ML___Clock (
  input  clkin,
  output Clock__clk,
  output Clock_Set__clks,
  output Clock_Enable__clke
);

  wire j_k_ff_1_qn, nand_1_out;

  J_K_Flip_Flop j_k_ff_1 (
    .J(1'b1), .clk(clkin), .K(1'b1), .Q(Clock__clk), .Qn(j_k_ff_1_qn));  // open: preset, en, reset
  nand nand_1 (nand_1_out, clkin, Clock__clk);
  nand nand_2 (Clock_Enable__clke, j_k_ff_1_qn, clkin);
  not not_1 (Clock_Set__clks, nand_1_out);

  // Notes on the sheet:
  //   6-10-2025 Niet als een echte klok maar een simulatie. Gebruik gemaakt van reeds bestaande j/k flip flop
endmodule

module ML___J_K_Flip_Flop_Master_Slave (
  input  J__Set_Input,
  input  CK__Clock_Input,
  input  K__Reset_Input,
  output Q,
  output Q_Complement
);

  wire nand_1_out, nand_2_out, nand_3_out, nand_4_out, nand_5_out, nand_6_out, not_1_out;

  not not_1 (not_1_out, CK__Clock_Input);
  nand nand_1 (nand_1_out, Q_Complement, J__Set_Input, CK__Clock_Input);
  nand nand_2 (nand_2_out, CK__Clock_Input, K__Reset_Input, Q);
  nand nand_3 (nand_3_out, nand_1_out, nand_4_out);
  nand nand_4 (nand_4_out, nand_3_out, nand_2_out);
  nand nand_5 (nand_5_out, nand_3_out, not_1_out);
  nand nand_6 (nand_6_out, not_1_out, nand_4_out);
  nand nand_7 (Q, nand_5_out, Q_Complement);
  nand nand_8 (Q_Complement, Q, nand_6_out);

  // Notes on the sheet:
  //   ML 6-10-25: Eigen J K Flip Flop in Master - Slave. Is een verbetering van de SR Flop. Daar kreeg je bij een input van 1-1 een race condition
  //   is bedoelt voor het simuleren van een clock in logisim (ik gebruik kant en klare J K flipflop maar heb hem nog even nagebouwd hier)
  //   q1
  //   q1 complement
endmodule

module ML___Control_Section_Stepper (
  input  reset,
  input  clk,
  output step_1,
  output step_2,
  output step_3,
  output step_4,
  output step_5,
  output step_6,
  output step_7
);

  wire ml_cpu_mem_1_1_o, ml_cpu_mem_1_2_o, ml_cpu_mem_1_3_o, ml_cpu_mem_1_4_o, ml_cpu_mem_1_5_o,
       ml_cpu_mem_1_6_o, ml_cpu_mem_1_7_o, ml_cpu_mem_1_8_o, ml_cpu_mem_1_9_o, ml_cpu_mem_1_10_o,
       ml_cpu_mem_1_11_o, not_1_out, not_2_out, not_3_out, not_4_out, not_5_out, not_6_out, not_7_out,
       not_8_out, or_1_out, or_2_out;

  not not_1 (not_1_out, reset);
  not not_2 (not_2_out, clk);
  or or_1 (or_1_out, reset, clk);
  or or_2 (or_2_out, reset, not_2_out);
  or or_3 (step_1, reset, not_3_out);
  ML___CPU_MEM_1 ml_cpu_mem_1_1 (.i(not_1_out), .s(or_1_out), .o(ml_cpu_mem_1_1_o));
  not not_3 (not_3_out, ml_cpu_mem_1_2_o);
  and and_1 (step_2, ml_cpu_mem_1_2_o, not_4_out);
  ML___CPU_MEM_1 ml_cpu_mem_1_2 (.i(ml_cpu_mem_1_1_o), .s(or_2_out), .o(ml_cpu_mem_1_2_o));
  ML___CPU_MEM_1 ml_cpu_mem_1_3 (.i(ml_cpu_mem_1_2_o), .s(or_1_out), .o(ml_cpu_mem_1_3_o));
  not not_4 (not_4_out, ml_cpu_mem_1_4_o);
  ML___CPU_MEM_1 ml_cpu_mem_1_4 (.i(ml_cpu_mem_1_3_o), .s(or_2_out), .o(ml_cpu_mem_1_4_o));
  and and_2 (step_3, ml_cpu_mem_1_4_o, not_5_out);
  ML___CPU_MEM_1 ml_cpu_mem_1_5 (.i(ml_cpu_mem_1_4_o), .s(or_1_out), .o(ml_cpu_mem_1_5_o));
  not not_5 (not_5_out, ml_cpu_mem_1_6_o);
  ML___CPU_MEM_1 ml_cpu_mem_1_6 (.i(ml_cpu_mem_1_5_o), .s(or_2_out), .o(ml_cpu_mem_1_6_o));
  and and_3 (step_4, ml_cpu_mem_1_6_o, not_6_out);
  ML___CPU_MEM_1 ml_cpu_mem_1_7 (.i(ml_cpu_mem_1_6_o), .s(or_1_out), .o(ml_cpu_mem_1_7_o));
  not not_6 (not_6_out, ml_cpu_mem_1_8_o);
  ML___CPU_MEM_1 ml_cpu_mem_1_8 (.i(ml_cpu_mem_1_7_o), .s(or_2_out), .o(ml_cpu_mem_1_8_o));
  and and_4 (step_5, ml_cpu_mem_1_8_o, not_7_out);
  ML___CPU_MEM_1 ml_cpu_mem_1_9 (.i(ml_cpu_mem_1_8_o), .s(or_1_out), .o(ml_cpu_mem_1_9_o));
  not not_7 (not_7_out, ml_cpu_mem_1_10_o);
  and and_5 (step_6, ml_cpu_mem_1_10_o, not_8_out);
  ML___CPU_MEM_1 ml_cpu_mem_1_10 (.i(ml_cpu_mem_1_9_o), .s(or_2_out), .o(ml_cpu_mem_1_10_o));
  ML___CPU_MEM_1 ml_cpu_mem_1_11 (.i(ml_cpu_mem_1_10_o), .s(or_1_out), .o(ml_cpu_mem_1_11_o));
  not not_8 (not_8_out, step_7);
  ML___CPU_MEM_1 ml_cpu_mem_1_12 (.i(ml_cpu_mem_1_11_o), .s(or_2_out), .o(step_7));

  // Notes on the sheet:
  //   reset: pull=down
  //   Stepper
  //   ML 7-10-25: 12 bits?
  //   18-11-25: inmiddels is dit weer pul down
  //   Let op: pull behaviour is 'Pull Up' bij de reset knop. Als er geen signal wordt gegeven, is met 'Pull' Up de waarde standaard 1 (zelf: en je zet hem dan met step 7 reset weer uit denk ik))
endmodule
module ML___Control_Section (
  input  clks,
  input  clk_masterclock,
  input  clke,
  input  _256,
  input  Reset,
  input  C__Carry,
  input  A__A_is_greater,
  input  E__A_is_equal,
  input  Z__Zero,
  input  [7:0] IR_In,
  output IR_S,
  output BUS_1,
  output MAR_S,
  output IAR_E,
  output IAR_S,
  output RAM_E,
  output ACC_S,
  output ACC_E,
  output RAM_S,
  output IO_CLKE_E,
  output C,
  output TMP_S,
  output FLAGS_S,
  output IO_CLKS_S,
  output R0_S,
  output R0_E,
  output R1_S,
  output R1_E,
  output R2_S,
  output R2_E,
  output R3_S,
  output R3_E,
  output END,
  output IO,
  output DA,
  output LOAD,
  output ALU_0,
  output ALU_1,
  output ALU_2
);

  wire and_5_out, and_6_out, and_7_out, and_8_out, and_9_out, and_10_out, and_11_out, and_12_out, and_17_out,
       and_18_out, and_19_out, and_20_out, and_21_out, and_22_out, and_23_out, and_24_out, and_25_out,
       and_26_out, and_27_out, and_28_out, and_29_out, and_30_out, and_31_out, and_32_out, and_33_out,
       and_34_out, and_35_out, and_36_out, and_37_out, and_38_out, and_39_out, and_40_out, and_44_out,
       and_45_out, and_46_out, and_47_out, and_48_out, and_49_out, and_50_out, and_51_out, and_52_out,
       and_53_out, and_54_out, and_55_out, and_56_out, and_57_out, and_58_out, and_59_out, and_60_out,
       and_62_out, and_63_out, and_64_out, and_65_out, L1, ml_2_4_decoder_4_outputs_east_1_out_3,
       ml_2_4_decoder_4_outputs_east_1_out_4, ml_2_4_decoder_4_outputs_east_1_out_5,
       ml_2_4_decoder_4_outputs_east_1_out_6, ml_2_4_decoder_4_outputs_west_1_out_3,
       ml_2_4_decoder_4_outputs_west_1_out_4, ml_2_4_decoder_4_outputs_west_1_out_5,
       ml_2_4_decoder_4_outputs_west_1_out_6, ml_2_4_decoder_4_outputs_west_2_out_3,
       ml_2_4_decoder_4_outputs_west_2_out_4, ml_2_4_decoder_4_outputs_west_2_out_5,
       ml_2_4_decoder_4_outputs_west_2_out_6, ml_3_8_decoder_8_outputs_east_1_out_4,
       ml_3_8_decoder_8_outputs_east_1_out_5, ml_3_8_decoder_8_outputs_east_1_out_6,
       ml_3_8_decoder_8_outputs_east_1_out_7, ml_3_8_decoder_8_outputs_east_1_out_8,
       ml_3_8_decoder_8_outputs_east_1_out_9, ml_3_8_decoder_8_outputs_east_1_out_10,
       ml_3_8_decoder_8_outputs_east_1_out_11, ml_control_section_stepper_1_step_1,
       ml_control_section_stepper_1_step_2, ml_control_section_stepper_1_step_3,
       ml_control_section_stepper_1_step_4, ml_control_section_stepper_1_step_5,
       ml_control_section_stepper_1_step_6, ml_control_section_stepper_1_step_7, not_1_out, not_2_out,
       not_3_out, not_4_out, not_5_out, not_6_out, not_7_out, not_8_out, not_9_out, not_10_out, not_11_out,
       not_12_out, not_13_out, not_14_out, not_15_out, not_16_out, or_6_out, or_7_out, or_8_out, or_9_out,
       or_10_out, or_11_out, or_12_out, or_13_out, or_14_out, or_15_out, REG_A_out, REG_B_E_out;

  or or_1 (R0_E, and_5_out, and_9_out);
  or or_2 (R1_E, and_6_out, and_10_out);
  or or_3 (R2_E, and_7_out, and_11_out);
  or or_4 (R3_E, and_8_out, and_12_out);
  and and_1 (IAR_E, clke, or_6_out);
  and and_2 (RAM_E, clke, or_7_out);
  and and_3 (ACC_E, clke, or_8_out);
  and and_4 (IO_CLKE_E, clke, and_49_out);
  and and_5 (and_5_out, clke, REG_B_E_out, ml_2_4_decoder_4_outputs_west_1_out_3);
  and and_6 (and_6_out, clke, REG_B_E_out, ml_2_4_decoder_4_outputs_west_1_out_4);
  and and_7 (and_7_out, clke, REG_B_E_out, ml_2_4_decoder_4_outputs_west_1_out_5);
  and and_8 (and_8_out, clke, REG_B_E_out, ml_2_4_decoder_4_outputs_west_1_out_6);
  and and_9 (and_9_out, clke, REG_A_out, ml_2_4_decoder_4_outputs_west_2_out_3);
  and and_10 (and_10_out, clke, REG_A_out, ml_2_4_decoder_4_outputs_west_2_out_4);
  and and_11 (and_11_out, clke, REG_A_out, ml_2_4_decoder_4_outputs_west_2_out_5);
  and and_12 (and_12_out, clke, REG_A_out, ml_2_4_decoder_4_outputs_west_2_out_6);
  and and_13 (ALU_0, ml_control_section_stepper_1_step_5, IR_In[7], IR_In[4]);
  and and_14 (ALU_1, ml_control_section_stepper_1_step_5, IR_In[7], IR_In[5]);
  and and_15 (ALU_2, ml_control_section_stepper_1_step_5, IR_In[7], IR_In[6]);
  not not_1 (not_1_out, _256);
  and and_16 (L1, not_1_out, LOAD);
  or REG_B_E (REG_B_E_out, and_32_out, and_45_out, and_36_out, and_40_out);
  not not_2 (not_2_out, L1);
  not not_3 (not_3_out, L1);
  or or_5 (BUS_1, and_18_out, and_39_out, and_38_out, and_35_out);
  or or_6 (or_6_out, and_18_out, and_35_out, and_37_out, and_38_out);
  or or_7 (or_7_out, ml_control_section_stepper_1_step_2, and_52_out, and_47_out, and_46_out, and_44_out);
  or or_8 (or_8_out, ml_control_section_stepper_1_step_3, and_48_out, and_51_out, and_50_out);
  or REG_A (REG_A_out, and_34_out, and_33_out, C);
  and and_17 (and_17_out, clk_masterclock, not_2_out);
  and and_18 (and_18_out, not_3_out, ml_control_section_stepper_1_step_1);
  ML___2_4_DECODER_4_outputs_west ml_2_4_decoder_4_outputs_west_1 (
    .out_3(ml_2_4_decoder_4_outputs_west_1_out_3), .out_4(ml_2_4_decoder_4_outputs_west_1_out_4),
    .out_5(ml_2_4_decoder_4_outputs_west_1_out_5), .out_6(ml_2_4_decoder_4_outputs_west_1_out_6),
    .A(IR_In[0]), .B(IR_In[1]));
  ML___2_4_DECODER_4_outputs_west ml_2_4_decoder_4_outputs_west_2 (
    .out_3(ml_2_4_decoder_4_outputs_west_2_out_3), .out_4(ml_2_4_decoder_4_outputs_west_2_out_4),
    .out_5(ml_2_4_decoder_4_outputs_west_2_out_5), .out_6(ml_2_4_decoder_4_outputs_west_2_out_6),
    .A(IR_In[2]), .B(IR_In[3]));
  ML___Control_Section_Stepper ml_control_section_stepper_1 (
    .reset(ml_control_section_stepper_1_step_7), .clk(and_17_out),
    .step_1(ml_control_section_stepper_1_step_1), .step_2(ml_control_section_stepper_1_step_2),
    .step_3(ml_control_section_stepper_1_step_3), .step_4(ml_control_section_stepper_1_step_4),
    .step_5(ml_control_section_stepper_1_step_5), .step_6(ml_control_section_stepper_1_step_6),
    .step_7(ml_control_section_stepper_1_step_7));
  not not_4 (not_4_out, IR_In[7]);
  ML___3_8_DECODER_8_outputs_east ml_3_8_decoder_8_outputs_east_1 (
    .out_4(ml_3_8_decoder_8_outputs_east_1_out_4), .out_5(ml_3_8_decoder_8_outputs_east_1_out_5),
    .out_6(ml_3_8_decoder_8_outputs_east_1_out_6), .out_7(ml_3_8_decoder_8_outputs_east_1_out_7),
    .out_8(ml_3_8_decoder_8_outputs_east_1_out_8), .out_9(ml_3_8_decoder_8_outputs_east_1_out_9),
    .out_10(ml_3_8_decoder_8_outputs_east_1_out_10), .out_11(ml_3_8_decoder_8_outputs_east_1_out_11),
    .C__Msb(IR_In[6]), .B(IR_In[5]), .A__Lsb(IR_In[4]));
  not not_5 (not_5_out, IR_In[0]);
  not not_6 (not_6_out, IR_In[1]);
  not not_7 (not_7_out, IR_In[2]);
  not not_8 (not_8_out, IR_In[3]);
  not not_9 (not_9_out, IR_In[4]);
  not not_10 (not_10_out, IR_In[5]);
  not not_11 (not_11_out, IR_In[6]);
  not not_12 (not_12_out, IR_In[7]);
  and and_19 (and_19_out, not_4_out, ml_3_8_decoder_8_outputs_east_1_out_4);
  and and_20 (and_20_out, not_4_out, ml_3_8_decoder_8_outputs_east_1_out_5);
  and and_21 (and_21_out, not_4_out, ml_3_8_decoder_8_outputs_east_1_out_6);
  and and_22 (and_22_out, not_4_out, ml_3_8_decoder_8_outputs_east_1_out_7);
  and and_23 (and_23_out, not_4_out, ml_3_8_decoder_8_outputs_east_1_out_8);
  and and_24 (and_24_out, not_4_out, ml_3_8_decoder_8_outputs_east_1_out_9);
  and and_25 (and_25_out, not_4_out, ml_3_8_decoder_8_outputs_east_1_out_10);
  and and_26 (and_26_out, not_4_out, ml_3_8_decoder_8_outputs_east_1_out_11);
  not not_13 (not_13_out, IR_In[5]);
  not not_14 (not_14_out, IR_In[4]);
  and and_27 (and_27_out, C__Carry, IR_In[3]);
  and and_28 (and_28_out, A__A_is_greater, IR_In[2]);
  and and_29 (and_29_out, E__A_is_equal, IR_In[1]);
  and and_30 (and_30_out, Z__Zero, IR_In[0]);
  and and_31 (and_31_out, IR_In[4], IR_In[5], IR_In[6]);
  and and_32 (and_32_out, ml_control_section_stepper_1_step_4, IR_In[7]);
  and and_33 (and_33_out, ml_control_section_stepper_1_step_4, and_19_out);
  and and_34 (and_34_out, ml_control_section_stepper_1_step_4, and_20_out);
  and and_35 (and_35_out, ml_control_section_stepper_1_step_4, and_21_out);
  and and_36 (and_36_out, ml_control_section_stepper_1_step_4, and_22_out);
  and and_37 (and_37_out, ml_control_section_stepper_1_step_4, and_23_out);
  and and_38 (and_38_out, ml_control_section_stepper_1_step_4, and_24_out);
  and and_39 (and_39_out, ml_control_section_stepper_1_step_4, and_25_out);
  and and_40 (and_40_out, ml_control_section_stepper_1_step_4, and_26_out, IR_In[3]);
  and and_41 (LOAD, not_5_out, not_6_out, not_7_out, not_8_out, not_9_out, not_10_out, not_11_out, not_12_out);
  or or_9 (or_9_out, and_27_out, and_28_out, and_29_out, and_30_out);
  and and_42 (END, IR_In[7], IR_In[6], not_13_out, not_14_out, IR_In[3], IR_In[2], IR_In[1], IR_In[0]);
  not not_15 (not_15_out, and_31_out);
  not not_16 (not_16_out, IR_In[3]);
  and and_43 (C, ml_control_section_stepper_1_step_5, IR_In[7]);
  and and_44 (and_44_out, ml_control_section_stepper_1_step_5, and_19_out);
  and and_45 (and_45_out, ml_control_section_stepper_1_step_5, and_20_out);
  and and_46 (and_46_out, ml_control_section_stepper_1_step_5, and_21_out);
  and and_47 (and_47_out, ml_control_section_stepper_1_step_5, and_23_out);
  and and_48 (and_48_out, ml_control_section_stepper_1_step_5, and_24_out);
  and and_49 (and_49_out, ml_control_section_stepper_1_step_5, and_26_out, not_16_out);
  and and_50 (and_50_out, ml_control_section_stepper_1_step_6, IR_In[7], not_15_out);
  and and_51 (and_51_out, ml_control_section_stepper_1_step_6, and_21_out);
  and and_52 (and_52_out, ml_control_section_stepper_1_step_6, and_24_out, or_9_out);
  ML___2_4_DECODER_4_outputs_east ml_2_4_decoder_4_outputs_east_1 (
    .out_3(ml_2_4_decoder_4_outputs_east_1_out_3), .out_4(ml_2_4_decoder_4_outputs_east_1_out_4),
    .out_5(ml_2_4_decoder_4_outputs_east_1_out_5), .out_6(ml_2_4_decoder_4_outputs_east_1_out_6),
    .A(IR_In[0]), .B(IR_In[1]));
  or or_10 (or_10_out, and_18_out, and_35_out, and_38_out, and_33_out, and_34_out, and_37_out);
  or or_11 (or_11_out, ml_control_section_stepper_1_step_3, and_36_out, and_48_out, and_47_out, and_51_out, and_52_out);
  or or_12 (or_12_out, and_18_out, and_35_out, and_38_out, C);
  or or_13 (or_13_out, and_39_out, C);
  or or_14 (or_14_out, and_44_out, and_50_out, and_46_out, and_49_out);
  or or_15 (or_15_out, L1, Reset);
  and and_53 (and_53_out, L1, clks);
  and and_54 (and_54_out, clks, ml_control_section_stepper_1_step_2);
  and and_55 (and_55_out, clks, or_10_out);
  and and_56 (and_56_out, clks, or_11_out);
  and and_57 (and_57_out, clks, or_12_out);
  and and_58 (and_58_out, clks, and_45_out);
  and and_59 (and_59_out, clks, and_32_out);
  and and_60 (and_60_out, clks, or_13_out);
  and and_61 (IO_CLKS_S, clks, and_40_out);
  and and_62 (and_62_out, clks, or_14_out, ml_2_4_decoder_4_outputs_east_1_out_3);
  and and_63 (and_63_out, clks, or_14_out, ml_2_4_decoder_4_outputs_east_1_out_4);
  and and_64 (and_64_out, clks, or_14_out, ml_2_4_decoder_4_outputs_east_1_out_5);
  and and_65 (and_65_out, clks, or_14_out, ml_2_4_decoder_4_outputs_east_1_out_6);
  or or_16 (IR_S, Reset, and_54_out);
  or or_17 (MAR_S, or_15_out, and_55_out);
  or or_18 (IAR_S, Reset, and_56_out);
  or or_19 (ACC_S, Reset, and_57_out);
  or or_20 (RAM_S, and_53_out, and_58_out);
  or or_21 (TMP_S, Reset, and_59_out);
  or or_22 (FLAGS_S, Reset, and_60_out);
  or or_23 (R0_S, Reset, and_62_out);
  or or_24 (R1_S, Reset, and_63_out);
  or or_25 (R2_S, Reset, and_64_out);
  or or_26 (R3_S, Reset, and_65_out);

  assign DA = IR_In[3];
  assign IO = IR_In[2];

  // Notes on the sheet:
  //   LOAD: pull=down
  //   7-10-25: CONTROL SECTION
  //   Enablers: Actief maken registers
  //   Reg A en reg B: Geen echte registers. Refereren aan r0,r1,r2,r3
  //   Interface tussen hardware en software
  //   REG B
  //   REG A
  //   step 1,2,3 voor Fetch
  //   Dus gebruik ALU(1) tel op (000) Reg 2 (10) Bij Reg 3 (geloof ik)
  //   10001011: 1)ALU 000)ADD 10)RegA 2 11)RegB
  //   step 5,6,7 gebruikt voor sectie 17 Adder
  //   Set: Waarde registers op 1 zetten
  //   14-11-25: Zie hier dat de reset knop dus gewoon alle outputs op nul zet. Is dus makkelijker dan dat het eruit ziet
endmodule

module ML___Accumulator (
  input  [7:0] in_1,
  input  s,
  input  e,
  output [7:0] ACC,
  output [7:0] o
);

  ML___Register_8 ml_register_8_1 (.i(in_1), .o(o), .S(s), .e(e), .out_4(ACC));

  // Notes on the sheet:
  //   s: pull=down
  //   ACC: pull=down
  //   in_1: pull=down
  //   o: pull=down
  //   e: pull=down
  //   7-10-25: Reg niet nodig om aan te sluiten hier
endmodule

module ML___BUS (
  input  bus_1,
  input  [7:0] i,
  output [7:0] o
);

  wire not_1_out;

  not not_1 (not_1_out, bus_1);
  or or_1 (o[0], bus_1, i[0]);
  and and_1 (o[1], not_1_out, i[1]);
  and and_2 (o[2], not_1_out, i[2]);
  and and_3 (o[3], not_1_out, i[3]);
  and and_4 (o[4], not_1_out, i[4]);
  and and_5 (o[5], not_1_out, i[5]);
  and and_6 (o[6], not_1_out, i[6]);
  and and_7 (o[7], not_1_out, i[7]);

  // Notes on the sheet:
  //   o: pull=down
  //   bus_1: pull=down
  //   i: pull=down
  //   ML 7-10-25: BUS
endmodule

module ML___TMP (
  input  [7:0] \input ,
  input  s,
  output [7:0] \output 
);

  wire [7:0] controlled_buffer_1_out;

  assign controlled_buffer_1_out = s ? \input  : 8'bz;  // Controlled_Buffer controlled_buffer_1
  ML___Memory_8 ml_memory_8_1 (.i(controlled_buffer_1_out), .o(\output ), .s(s));

  // Notes on the sheet:
  //   input: pull=down
  //   output: pull=down
  //   7-10-25: CPU - TEMP
endmodule

module ML___CPU (
  input  clock,
  input  RESET,
  input  [7:0] RAM_INPUT,
  output [7:0] out_4,
  output [7:0] _0,
  output [7:0] _1,
  output [7:0] _2,
  output clkl,
  output LOAD,
  output END,
  output clke,
  output clks,
  output S,
  output E,
  output IO,
  output DA,
  output [7:0] out_17,
  output [7:0] out_18,
  output [7:0] out_19,
  output [7:0] BUS_OUTPUT
);

  wire _256, and_1_out, and_2_out, C, ml_alu_arithmetic_logical_unit_1_a_larger,
       ml_alu_arithmetic_logical_unit_1_carry_out, ml_alu_arithmetic_logical_unit_1_equal,
       ml_alu_arithmetic_logical_unit_1_zero, ml_carry_temp_1_o, ml_control_section_1_acc_e,
       ml_control_section_1_acc_s, ml_control_section_1_alu_0, ml_control_section_1_alu_1,
       ml_control_section_1_alu_2, ml_control_section_1_bus_1, ml_control_section_1_flags_s,
       ml_control_section_1_iar_e, ml_control_section_1_iar_s, ml_control_section_1_ir_s,
       ml_control_section_1_mar_s, ml_control_section_1_r0_e, ml_control_section_1_r0_s,
       ml_control_section_1_r1_e, ml_control_section_1_r1_s, ml_control_section_1_r2_e,
       ml_control_section_1_r2_s, ml_control_section_1_r3_e, ml_control_section_1_r3_s,
       ml_control_section_1_ram_e, ml_control_section_1_ram_s, ml_flags_1_a_2, ml_flags_1_c_2,
       ml_flags_1_e_2, ml_flags_1_z_2, not_1_out, not_2_out, S_t;
  wire [7:0] ml_alu_arithmetic_logical_unit_1_output, ml_bus_1_o, ml_load_256_count_1_count,
       ml_ram_v7_32_byte_1__141, ml_tmp_1_output, multiplexer_1_out;

  ML___TMP ml_tmp_1 (.\input (BUS_OUTPUT), .s(S_t), .\output (ml_tmp_1_output));
  ML___BUS ml_bus_1 (.bus_1(ml_control_section_1_bus_1), .i(ml_tmp_1_output), .o(ml_bus_1_o));
  ML___ALU__Arithmetic___Logical_Unit ml_alu_arithmetic_logical_unit_1 (
    .a(BUS_OUTPUT), .b(ml_bus_1_o), .carry_in(and_1_out), .c_Msb(ml_control_section_1_alu_2),
    .b_2(ml_control_section_1_alu_1), .a_Lsb(ml_control_section_1_alu_0),
    .a_larger(ml_alu_arithmetic_logical_unit_1_a_larger), .equal(ml_alu_arithmetic_logical_unit_1_equal),
    .Zero(ml_alu_arithmetic_logical_unit_1_zero), .\output (ml_alu_arithmetic_logical_unit_1_output),
    .carry_out(ml_alu_arithmetic_logical_unit_1_carry_out));
  and and_1 (and_1_out, ml_carry_temp_1_o, C);
  ML___Accumulator ml_accumulator_1 (
    .in_1(ml_alu_arithmetic_logical_unit_1_output), .o(BUS_OUTPUT), .s(ml_control_section_1_acc_s),
    .e(ml_control_section_1_acc_e), .ACC(out_17));
  not not_1 (not_1_out, END);
  and and_2 (and_2_out, clock, not_1_out);
  ML_CARRY_TEMP ml_carry_temp_1 (.c(ml_flags_1_c_2), .o(ml_carry_temp_1_o), .s(S_t));
  ML___Clock ml_clock_1 (.clkin(and_2_out), .Clock__clk(clkl), .Clock_Set__clks(clks), .Clock_Enable__clke(clke));
  ML___FLAGS ml_flags_1 (
    .C(ml_alu_arithmetic_logical_unit_1_carry_out), .A(ml_alu_arithmetic_logical_unit_1_a_larger),
    .E(ml_alu_arithmetic_logical_unit_1_equal), .Z(ml_alu_arithmetic_logical_unit_1_zero),
    .C_2(ml_flags_1_c_2), .A_2(ml_flags_1_a_2), .E_2(ml_flags_1_e_2), .Z_2(ml_flags_1_z_2),
    .s(ml_control_section_1_flags_s));
  not not_2 (not_2_out, _256);
  assign BUS_OUTPUT = not_2_out ? ml_load_256_count_1_count : 8'bz;  // Controlled_Buffer controlled_buffer_1
  ML___LOAD_256_Count ml_load_256_count_1 (
    .count(ml_load_256_count_1_count), .clk(clkl), .carry(_256), .LOAD(not_2_out));
  ML___Register ml_register_1 (
    .out_4(out_4), .\input (BUS_OUTPUT), .\output (BUS_OUTPUT), .s(ml_control_section_1_r0_s),
    .e(ml_control_section_1_r0_e));
  ML___Control_Section ml_control_section_1 (
    .clks(clks), .clk_masterclock(clkl), .clke(clke), .RAM_E(ml_control_section_1_ram_e),
    .ACC_E(ml_control_section_1_acc_e), .R0_E(ml_control_section_1_r0_e), .R1_E(ml_control_section_1_r1_e),
    .R2_E(ml_control_section_1_r2_e), .R3_E(ml_control_section_1_r3_e), .MAR_S(ml_control_section_1_mar_s),
    .ACC_S(ml_control_section_1_acc_s), .TMP_S(S_t), .IR_S(ml_control_section_1_ir_s),
    .IAR_S(ml_control_section_1_iar_s), .IAR_E(ml_control_section_1_iar_e),
    .BUS_1(ml_control_section_1_bus_1), .IR_In(out_18), .IO_CLKE_E(E), .ALU_0(ml_control_section_1_alu_0),
    .ALU_1(ml_control_section_1_alu_1), .ALU_2(ml_control_section_1_alu_2),
    .RAM_S(ml_control_section_1_ram_s), .FLAGS_S(ml_control_section_1_flags_s), .IO_CLKS_S(S),
    .R0_S(ml_control_section_1_r0_s), .R1_S(ml_control_section_1_r1_s), .R2_S(ml_control_section_1_r2_s),
    .R3_S(ml_control_section_1_r3_s), .C__Carry(ml_flags_1_c_2), .A__A_is_greater(ml_flags_1_a_2),
    .E__A_is_equal(ml_flags_1_e_2), .Z__Zero(ml_flags_1_z_2), ._256(_256), .END(END), .IO(IO), .DA(DA),
    .Reset(RESET), .C(C), .LOAD(LOAD));
  ML___Register ml_register_2 (
    .out_4(_0), .\input (BUS_OUTPUT), .\output (BUS_OUTPUT), .s(ml_control_section_1_r1_s),
    .e(ml_control_section_1_r1_e));
  ML___IAR ml_iar_1 (
    .\input (BUS_OUTPUT), .\output (BUS_OUTPUT), .s(ml_control_section_1_iar_s),
    .e(ml_control_section_1_iar_e), .IAR(out_19));
  ML___Instruction_Register___Uitleg ml_instruction_register_uitleg_1 (
    .in_1(BUS_OUTPUT), .out_3(out_18), .in_2(ml_control_section_1_ir_s));
  ML___Register ml_register_3 (
    .out_4(_1), .\input (BUS_OUTPUT), .\output (BUS_OUTPUT), .s(ml_control_section_1_r2_s),
    .e(ml_control_section_1_r2_e));
  ML___Register ml_register_4 (
    .out_4(_2), .\input (BUS_OUTPUT), .\output (BUS_OUTPUT), .s(ml_control_section_1_r3_s),
    .e(ml_control_section_1_r3_e));
  Multiplexer #(.width(8)) multiplexer_1 (
    .in0(BUS_OUTPUT), .in1(RAM_INPUT), .out(multiplexer_1_out), .sel(LOAD));  // open: en
  ML___RAM_V7_32_Byte ml_ram_v7_32_byte_1 (
    .address(BUS_OUTPUT), .sa(ml_control_section_1_mar_s), .\output (BUS_OUTPUT), .reset(RESET),
    .s(ml_control_section_1_ram_s), .e(ml_control_section_1_ram_e), .\input (multiplexer_1_out),
    ._141(ml_ram_v7_32_byte_1__141), ._157(ml_ram_v7_32_byte_1__141));  // open: _15, _31, _47, _63, _79, _95, _111, _127, _143, _159, _175, _191, _207, _223, _239, _255, _14, _30, _46, _62, _78, _94, _110, _126, _142, _158, _174, _190, _206, _222, _238, _254, _13, _29, _45, _61, _77, _93, _109, _125, _173, _189, _205, _221, _237, _253, _12, _28, _44, _60, _76, _92, _108, _124, _140, _156, _172, _188, _204, _220, _236, _252, _11, _27, _43, _59, _75, _91, _107, _123, _139, _155, _171, _187, _203, _219, _235, _251, _10, _26, _42, _58, _74, _90, _106, _122, _138, _154, _170, _186, _202, _218, _234, _250, _9, _25, _41, _57, _73, _89, _105, _121, _137, _153, _169, _185, _201, _217, _233, _249, _8, _24, _40, _56, _72, _88, _104, _120, _136, _152, _168, _184, _72_2, _216, _232, _248, _7, _23, _39, _55, _71, _87, _103, _119, _135, _151, _167, _183, _199, _215, _231, _247, _6, _22, _38, _54, _70, _86, _102, _118, _134, _150, _166, _182, _198, _214, _230, _246, _5, _21, _37, _53, _69, _85, _101, _117, _133, _149, _165, _181, _197, _213, _229, _245, _4, _20, _36, _52, _68, _84, _100, _116, _132, _148, _164, _180, _196, _212, _228, _244, _3, _19, _35, _51, _67, _83, _99, _115, _131, _147, _163, _179, _195, _211, _227, _243, _2, _18, _34, _50, _66, _82, _98, _114, _130, _18_2, _162, _178, _194, _210, _226, _242, _1, _17, _33, _49, _65, _81, _97, _113, _129, _145, _161, _177, _193, _209, _225, _241, _0, _16, _32, _48, _64, _80, _96, _112, _128, _144, _160, _176, _192, _208, _224, _240

  // Notes on the sheet:
  //   BUS_OUTPUT: pull=down
  //   LOAD: pull=down
  //   ML 15-10-25: Werkt c.f. uitleg
  //   3
  //   Input vanuit top level CPU
endmodule

module ML___IAR (
  input  [7:0] \input ,
  input  s,
  input  e,
  output [7:0] IAR,
  output [7:0] \output 
);

  ML___Register_8 ml_register_8_1 (.i(\input ), .o(\output ), .S(s), .e(e), .out_4(IAR));

  // Notes on the sheet:
  //   output: pull=down
  //   input: pull=down
  //   e: pull=down
  //   Zelfde als gewoon register en register_8
  //   IAR = Instruction Address Register: Ook Program Counter
  //   IAR contains the address of the next instruction that we are going to fetch
endmodule

module ML___Instruction_Register___Uitleg (
  input  [7:0] in_1,
  input  in_2,
  output [7:0] out_3
);

  ML___Memory_8 ml_memory_8_1 (.i(in_1), .o(out_3), .s(in_2));

  // Notes on the sheet:
  //   out_3: pull=down
  //   in_1: pull=down
  //   in_2: pull=down
  //   27-10-2025
  //   Tweede, Derde, Vierde Bit: 
  //   Functions:
  //   000 - ADD
  //   001 - Shift Right
  //   010 - Shift Left
  //   011 - Not
  //   100 - AND
  //   101 - OR
  //   110 - XOR
  //   111 - CMP (compare)
  //   0010 - Data Instruction
  //   Jump to address in Register B
  //   0100 - Jump Address Instruction
  //   Jump to address in Register B
  //   0110 - Clear Flags Instruction
  //   Instruction Register
  //   Instruction Register: ALU Instruction
  //   Eerste Bit: 1: Activeren ALU instructie. 
  //   Instruction Register: Data Instruction 
  //   Load From RAM To Register B
  //   Eerste, Tweede, Derde, Vierde Bit:
  //   Instruction Register: Jump Address Instruction
  //   Eerste, Tweede, Derde, Vierde Bit:
  //   Instruction Register: Clear Flags Instruction
  //   Eerste, Tweede, Derde, Vierde Bit:
  //   Register A
  //   00 - R0
  //   01 - R1
  //   10 - R2
  //   11 - R3
  //   Vijfde, Zesde Bit
  //   geen functie
  //   geen functie
  //   geen functie
  //   Zevende, Achtste Bit
  //   Register B
  //   00 - R0
  //   01 - R1
  //   10 - R2
  //   11 - R3
  //   Vijfde, Zesde Bit
  //   Vijfde, Zesde Bit
  //   Vijfde, Zesde, Zevende, Achtste Bit
  //   Zevende, Achtste Bit
  //   Register B
  //   00 - R0
  //   01 - R1
  //   10 - R2
  //   11 - R3
  //   Zevende, Achtste Bit
  //   Register B
  //   00 - R0
  //   01 - R1
  //   10 - R2
  //   11 - R3
  //   Tweede, Derde Bit
  //   geen functie
  //   0011 - Jump Instruction
  //   28-10-2025
  //   Zelf 28/10/25: Instructions
  //   1XXXXXXX - ALU
  //   0010--XX - Data Instruction
  //   11001111 - End Instruction
  //   Eerst Bit: 0: Activeren LOAD/ STORE instruction
  //   0 - Load
  //   1 - Store
  //   Van Register B naar RAM via register A (Address)
  //   Instruction Register: Jump instruction
  //   Jump to address in Register B
  //   Eerste, Tweede, Derde, Vierde Bit:
  //   Jump to address in next RAM location if flag set
  //   Eerste, Tweede, Derde, Vierde Bit:
  //   0101 - Jump If Instruction
  //   End of Program
  //   Eerste, Tweede, Derde, Vierde Bit:
  //   11001111- End Instruction
  //   0--0XXXX - Load: From RAM to Reg A via Reg B address
  //   0--1XXXX - Store: From Reg B to RAM via Reg A Adress
  //   0011--XX - Jump Instruction
  //   0100--XX   -  Jump Address Instruction
  //   0101XXXX - Jump If Instruction
  //   0110----   - Clear Flags Instruction
  //   Instruction Register: Load/Store Instruction
  //   Vierde Bit
  //   Instruction Register: Jump If Instruction
  //   Instruction Register: End Instruction
  //   Vijfde, Zesde Bit
  //   Register A
  //   00 - R0
  //   01 - R1
  //   10 - R2
  //   11 - R3
  //   Register B
  //   00 - R0
  //   01 - R1
  //   10 - R2
  //   11 - R3
  //   Vijfde, Zesde Bit
  //   geen functie
  //   (C) CarryFlag
  //   (A) A => B
  //   0000 - No Jump
  //   0001 - JZ(jump zero)
  //   0010 - JE(Jump A=B)
  //   0011 - JEZ
  //   0100 - JA(Jump A>B)
  //   0101 - JAZ
  //   0110 - JAE
  //   0111 - JAEZ
  //   1000 - JC (jump carry)
  //   1001 - JCZ
  //   1010 - JCE
  //   1011 - JCEZ
  //   1100 - JCA
  //   1101 - JCAZ
  //   1110 - JCAE
  //   1111 - JCA EZ
  //   Zevende, Achtste Bit
  //   Zevende, Achtste Bit
  //   Register B
  //   00 - R0
  //   01 - R1
  //   10 - R2
  //   11 - R3
  //   Vijfde, Zesde, Zevende, Achtste Bit
  //   (E) = E==B
  //   (Z) Zero
  //   Vijfde, Zesde, Zevende, Achtste Bit
  //   geen functie (maar altijd 1 dus?)
  //   Zelf: denk bij Load alleen lezen (const) en schrijven (store) in c++
endmodule

module ML___LOAD_256_Count (
  input  LOAD,
  input  clk,
  output [7:0] count,
  output carry
);

  wire and_1_out;

  Counter counter_1 (.count(1'b1), .Q(count), .carry(carry), .clk(and_1_out));  // open: load, D, clr
  and and_1 (and_1_out, LOAD, clk);

  // Notes on the sheet:
  //   D-type Flip Flop
endmodule

module ML___FLAGS (
  input  C,
  input  A,
  input  E,
  input  Z,
  input  s,
  output C_2,
  output A_2,
  output E_2,
  output Z_2
);

  ML___CPU_MEM_1 ml_cpu_mem_1_1 (.i(C), .s(s), .o(C_2));
  ML___CPU_MEM_1 ml_cpu_mem_1_2 (.i(A), .s(s), .o(A_2));
  ML___CPU_MEM_1 ml_cpu_mem_1_3 (.i(E), .s(s), .o(E_2));
  ML___CPU_MEM_1 ml_cpu_mem_1_4 (.i(Z), .s(s), .o(Z_2));
endmodule

module ML_CARRY_TEMP (
  input  c,
  input  s,
  output o
);

  ML___CPU_MEM_1 ml_cpu_mem_1_1 (.i(c), .s(s), .o(o));
endmodule

module ML___CPU_Test (
);

  wire CLK, CLKE, CLKL, CLKS, END, LOAD, ml_load_256_count_1_carry, not_1_out, RESET;
  wire [7:0] ACC, BUS_OUTPUT, IAR, IR, ml_load_256_count_1_count, R0, R1, R2, R3, RAM_INPUT;

  not not_1 (not_1_out, ml_load_256_count_1_carry);
  Hex_Digit_Display hex_digit_display_1 (.value(BUS_OUTPUT[7:4]));  // open: dp
  Hex_Digit_Display hex_digit_display_2 (.value(BUS_OUTPUT[3:0]));  // open: dp
  Hex_Digit_Display hex_digit_display_3 (.value(ACC[7:4]));  // open: dp
  Hex_Digit_Display hex_digit_display_4 (.value(ACC[3:0]));  // open: dp
  ML___LOAD_256_Count ml_load_256_count_1 (
    .count(ml_load_256_count_1_count), .clk(CLKL), .carry(ml_load_256_count_1_carry), .LOAD(not_1_out));
  Hex_Digit_Display hex_digit_display_5 (.value(IAR[7:4]));  // open: dp
  Hex_Digit_Display hex_digit_display_6 (.value(IAR[3:0]));  // open: dp
  ML___CPU ml_cpu_1 (
    .out_4(R0), ._0(R1), ._1(R2), ._2(R3), .clkl(CLKL), .END(END), .RESET(RESET), .out_17(ACC),
    .RAM_INPUT(RAM_INPUT), .clock(CLK), .clke(CLKE), .clks(CLKS), .out_19(IAR), .out_18(IR),
    .BUS_OUTPUT(BUS_OUTPUT), .LOAD(LOAD));  // open: S, E, IO, DA
  Hex_Digit_Display hex_digit_display_7 (.value(IR[7:4]));  // open: dp
  RAM ram_1 (.addr(ml_load_256_count_1_count), .data(RAM_INPUT), .sel(not_1_out), .clk(CLKL), .ld(1'b1), .clr(1'b0));
  Hex_Digit_Display hex_digit_display_8 (.value(IR[3:0]));  // open: dp
  Hex_Digit_Display hex_digit_display_9 (.value(R0[3:0]));  // open: dp
  Hex_Digit_Display hex_digit_display_10 (.value(R0[7:4]));  // open: dp
  Hex_Digit_Display hex_digit_display_11 (.value(R1[7:4]));  // open: dp
  Hex_Digit_Display hex_digit_display_12 (.value(R1[3:0]));  // open: dp
  Hex_Digit_Display hex_digit_display_13 (.value(R2[7:4]));  // open: dp
  Hex_Digit_Display hex_digit_display_14 (.value(R2[3:0]));  // open: dp
  Hex_Digit_Display hex_digit_display_15 (.value(R3[3:0]));  // open: dp
  Hex_Digit_Display hex_digit_display_16 (.value(R3[7:4]));  // open: dp
  Button u_RESET (.out(RESET));
  LED #(.active("false")) led_1 (.in(END));
  Clock u_CLK (.out(CLK));

  // Notes on the sheet:
  //   Hexadecimalen dus 0 tm F
  //   BUS
  //   ACC
  //   IAR
  //   EXTERNAL RAM
  //   IR
  //   R0
  //   R1
  //   0
  //   1
  //   0
  //   R2
  //   R3
endmodule
